// Digital circuit 16_bit_PC_and_ROM.dig as structural Verilog
module _16_bit_PC_and_ROM (
  input  clk,
  input  in_2,
  input  in_3,
  input  in_4,
  input  in_5,
  input  in_6,
  input  in_7,
  input  in_8,
  input  in_9,
  input  in_10,
  input  in_11,
  input  in_12,
  input  in_13,
  input  in_14,
  input  in_15,
  input  in_16,
  input  in_17,
  input  in_18,
  input  in_19,
  input  in_20
);

  wire [3:0] _27c1024_1_p3, _27c1024_1_p7, pc1634_1_p12, undriven;

  // _27C1024 _27c1024_1: pin names not known; wires that end beside it: 1'b0, 1'b1, _27c1024_1_p3[3], _27c1024_1_p3[2], _27c1024_1_p3[1], _27c1024_1_p3[0], _27c1024_1_p7[3], _27c1024_1_p7[2], _27c1024_1_p7[1]
  Seven_Seg_Hex seven_seg_hex_1 (.d(_27c1024_1_p3), .dp(1'b0));
  Seven_Seg_Hex seven_seg_hex_2 (.d(_27c1024_1_p7), .dp(1'b0));
  Seven_Seg_Hex seven_seg_hex_3 (.d(pc1634_1_p12), .dp(1'b0));
  Seven_Seg_Hex seven_seg_hex_4 (.d(undriven), .dp(1'b0));
  // PC1634 pc1634_1: pin names not known; wires that end beside it: in_2, in_3, _27c1024_1_p3[3], _27c1024_1_p3[2], _27c1024_1_p3[1], _27c1024_1_p3[0], _27c1024_1_p7[3], _27c1024_1_p7[2], _27c1024_1_p7[1], 1'b0, _27c1024_1_p7[0], pc1634_1_p12[3], pc1634_1_p12[2], pc1634_1_p12[1], pc1634_1_p12[0], 1'b1, in_20, clk, in_4, in_5, in_6, in_7, in_8, in_9, in_10
endmodule
