// Digital circuit 17_gate_ALU.dig as structural Verilog
module _17_gate_ALU (
  input  A,
  input  B,
  input  I1,
  input  I0,
  input  Cin,
  input  I4,
  input  I2,
  input  I3,
  input  B_2,
  input  I1_2,
  input  I0_2,
  input  A_2,
  output SUM,
  output CARRY,
  output Q
);

  wire nand_1_out, nand_2_out, nand_3_out, nand_4_out, nand_5_out, nand_6_out, nand_7_out, nand_8_out,
       nand_9_out, nand_10_out, nand_11_out, nand_12_out, nand_13_out, nand_14_out, nand_15_out, nand_16_out,
       nand_17_out, nand_18_out, nand_19_out, nand_21_out, nand_22_out, nand_23_out;

  nand nand_1 (nand_1_out, A, A);
  nand nand_2 (nand_2_out, nand_1_out, I3);
  nand nand_3 (nand_3_out, nand_2_out, B);
  nand nand_4 (nand_4_out, A_2, B_2);
  nand nand_5 (nand_5_out, nand_2_out, nand_3_out);
  nand nand_6 (nand_6_out, nand_3_out, nand_3_out);
  nand nand_7 (nand_7_out, nand_3_out, B);
  nand nand_8 (nand_8_out, A_2, nand_4_out);
  nand nand_9 (nand_9_out, nand_4_out, nand_4_out);
  nand nand_10 (nand_10_out, nand_4_out, B_2);
  nand nand_11 (nand_11_out, nand_5_out, nand_7_out);
  nand nand_12 (nand_12_out, I4, Cin);
  nand nand_13 (nand_13_out, nand_8_out, nand_10_out);
  nand nand_14 (nand_14_out, I1, nand_11_out);
  nand nand_15 (nand_15_out, nand_6_out, I0);
  nand nand_16 (nand_16_out, I2, nand_12_out);
  nand nand_17 (nand_17_out, I1_2, nand_13_out);
  nand nand_18 (nand_18_out, nand_9_out, I0_2);
  nand nand_19 (nand_19_out, nand_14_out, nand_15_out);
  nand nand_20 (Q, nand_17_out, nand_18_out);
  nand nand_21 (nand_21_out, nand_19_out, nand_16_out);
  nand nand_22 (nand_22_out, nand_19_out, nand_21_out);
  nand nand_23 (nand_23_out, nand_21_out, nand_16_out);
  nand nand_24 (CARRY, nand_3_out, nand_21_out);
  nand nand_25 (SUM, nand_22_out, nand_23_out);

  // Notes on the sheet:
  //   Multifunction Gate #1 - Zero, AND, XOR, OR
  //   Zero, AND, XOR, OR
endmodule
