// Digital circuit 2_input_mux_3_gates.dig as structural Verilog
module _2_input_mux_3_gates (
  input  SEL_B,
  input  Bin,
  input  Ain,
  input  SEL_A,
  input  A,
  input  B,
  input  DATA,
  input  CLK,
  input  A_2,
  input  AL,
  input  B_2,
  input  nC,
  input  I3,
  input  I2,
  input  I1,
  input  I0,
  input  B_3,
  input  A_3,
  input  I1_2,
  input  A_4,
  input  B_4,
  input  C,
  input  in_32,
  input  I0_2,
  input  A_5,
  input  B_5,
  input  C_2,
  input  I1_3,
  input  I0_3,
  input  A_6,
  input  B_6,
  input  C_3,
  input  I1_4,
  input  I0_4,
  input  I3_2,
  input  I2_2,
  input  A_7,
  input  B_7,
  input  C_4,
  input  I5,
  input  I4,
  input  I7,
  input  I6,
  input  AL_2,
  input  A_8,
  input  B_8,
  input  C_5,
  input  I1_5,
  input  I0_5,
  input  AL_3,
  input  XOR,
  input  AND,
  input  A_9,
  input  B_9,
  input  C_6,
  input  I1_6,
  input  I0_6,
  input  AL_4,
  input  I2_3,
  input  A_10,
  input  B_10,
  input  C_7,
  input  I1_7,
  input  I0_7,
  input  AL_5,
  input  A_11,
  input  B_11,
  input  I1_8,
  input  I0_8,
  input  I2_4,
  input  I3_3,
  input  I2_5,
  input  I11,
  input  I10,
  input  I9,
  input  I8,
  input  B_12,
  input  A_12,
  input  A_13,
  input  B_13,
  input  I1_9,
  input  I0_9,
  input  A_14,
  input  B_14,
  input  I1_10,
  input  I0_10,
  input  C_8,
  input  I2_6,
  input  B_15,
  input  I1_11,
  input  I0_11,
  input  I2_7,
  input  A_15,
  input  B_16,
  input  I1_12,
  input  I0_12,
  input  C_9,
  input  I3_4,
  input  I2_8,
  input  A_16,
  input  B_17,
  input  I1_13,
  input  I0_13,
  input  I2_9,
  input  C_10,
  input  B_18,
  input  I1_14,
  input  I0_14,
  input  A_17,
  input  C_11,
  input  nSet,
  input  nReset,
  input  nWRX,
  input  nCLX,
  input  nWRY,
  input  nCLY,
  input  nRDX,
  input  nRDY,
  input  I3_5,
  input  A_18,
  input  I12,
  input  I,
  input  A_19,
  input  B_19,
  input  XOR_nOR,
  input  A_20,
  input  B_20,
  input  XOR_nOR_2,
  input  C_12,
  input  XOR_nOR_3,
  input  A_21,
  input  B_21,
  input  C_13,
  input  A_22,
  input  B_22,
  input  I1_15,
  input  I0_15,
  input  Cin,
  input  I3_6,
  input  I2_10,
  input  Blk,
  output Dout,
  output Sum,
  output nQ,
  output Q,
  output Carry,
  output out_18,
  output F,
  output Sum_2,
  output Carry_2,
  output Sum_3,
  output Carry_3,
  output Sum_4,
  output Carry_4,
  output Sum_5,
  output Carry_5,
  output Sum_6,
  output Carry_6,
  output Sum_7,
  output Carry_7,
  output Carry_8,
  output Sum_8,
  output Carry_9,
  output F_2,
  output out_106,
  output Sum_9,
  output Carry_10,
  output out_118,
  output Sum_10,
  output Carry_11,
  output Sum_11,
  output Carry_12,
  output Sum_12,
  output Carry_13,
  output Q_2,
  output nQ_2,
  output out_160,
  output Sum_13,
  output Carry_14,
  output Sum_14,
  output Carry_15,
  output SUM_15,
  output CARRY_16
);

  wire nand_1_out, nand_2_out, nand_3_out, nand_4_out, nand_5_out, nand_6_out, nand_7_out, nand_8_out,
       nand_9_out, nand_10_out, nand_11_out, nand_12_out, nand_13_out, nand_14_out, nand_15_out, nand_16_out,
       nand_17_out, nand_18_out, nand_19_out, nand_20_out, nand_21_out, nand_22_out, nand_23_out,
       nand_24_out, nand_25_out, nand_26_out, nand_27_out, nand_28_out, nand_29_out, nand_30_out,
       nand_31_out, nand_32_out, nand_33_out, nand_34_out, nand_35_out, nand_36_out, nand_37_out,
       nand_38_out, nand_39_out, nand_40_out, nand_41_out, nand_42_out, nand_43_out, nand_44_out,
       nand_45_out, nand_46_out, nand_47_out, nand_48_out, nand_49_out, nand_50_out, nand_51_out,
       nand_52_out, nand_53_out, nand_54_out, nand_55_out, nand_56_out, nand_57_out, nand_58_out,
       nand_59_out, nand_60_out, nand_61_out, nand_62_out, nand_63_out, nand_65_out, nand_66_out,
       nand_67_out, nand_68_out, nand_69_out, nand_70_out, nand_71_out, nand_72_out, nand_73_out,
       nand_74_out, nand_75_out, nand_76_out, nand_77_out, nand_78_out, nand_79_out, nand_80_out,
       nand_81_out, nand_82_out, nand_83_out, nand_84_out, nand_87_out, nand_88_out, nand_89_out,
       nand_90_out, nand_91_out, nand_92_out, nand_93_out, nand_94_out, nand_95_out, nand_96_out,
       nand_97_out, nand_98_out, nand_99_out, nand_100_out, nand_101_out, nand_102_out, nand_105_out,
       nand_106_out, nand_107_out, nand_118_out, nand_119_out, nand_120_out, nand_121_out, nand_122_out,
       nand_123_out, nand_124_out, nand_125_out, nand_126_out, nand_127_out, nand_128_out, nand_129_out,
       nand_130_out, nand_131_out, nand_132_out, nand_133_out, nand_134_out, nand_135_out, nand_136_out,
       nand_137_out, nand_138_out, nand_139_out, nand_140_out, nand_141_out, nand_142_out, nand_143_out,
       nand_144_out, nand_145_out, nand_146_out, nand_147_out, nand_148_out, nand_150_out, nand_151_out,
       nand_152_out, nand_153_out, nand_154_out, nand_155_out, nand_156_out, nand_157_out, nand_158_out,
       nand_159_out, nand_160_out, nand_161_out, nand_162_out, nand_163_out, nand_164_out, nand_165_out,
       nand_166_out, nand_167_out, nand_168_out, nand_169_out, nand_170_out, nand_171_out, nand_172_out,
       nand_173_out, nand_174_out, nand_175_out, nand_176_out, nand_177_out, nand_178_out, nand_179_out,
       nand_180_out, nand_181_out, nand_182_out, nand_183_out, nand_184_out, nand_185_out, nand_186_out,
       nand_187_out, nand_188_out, nand_189_out, nand_190_out, nand_191_out, nand_192_out, nand_194_out,
       nand_195_out, nand_196_out, nand_197_out, nand_198_out, nand_199_out, nand_201_out, nand_202_out,
       nand_203_out, nand_204_out, nand_205_out, nand_206_out, nand_207_out, nand_208_out, nand_209_out,
       nand_210_out, nand_211_out, nand_212_out, nand_213_out, nand_214_out, nand_215_out, nand_216_out,
       nand_217_out, nand_218_out, nand_219_out, nand_220_out, nand_221_out, nand_223_out, nand_224_out,
       nand_225_out, nand_229_out, nand_230_out, nand_233_out, nand_234_out, nand_236_out, nand_237_out,
       nand_238_out, nand_239_out, nand_240_out, nand_241_out, nand_242_out, nand_243_out, nand_244_out,
       nand_246_out, nand_247_out, nand_248_out, nand_251_out, nand_253_out, nand_255_out, nand_257_out,
       nand_258_out, nand_264_out, nand_265_out, nand_266_out, nand_267_out, nand_270_out, nand_271_out,
       nand_272_out, nand_275_out, nand_276_out, nand_277_out, nand_278_out, nand_279_out, nand_280_out,
       nand_281_out, nand_282_out, nand_283_out, nand_284_out, nand_285_out, nand_286_out, nand_287_out,
       nand_288_out, nand_289_out, nand_290_out, nand_291_out, nand_292_out, nand_293_out;

  nand nand_1 (nand_1_out, A_11, B_11);
  nand nand_2 (nand_2_out, A_11, I1_8);
  nand nand_3 (nand_3_out, I0_8, B_11);
  nand nand_4 (nand_4_out, I2_4, nand_2_out);
  nand nand_5 (nand_5_out, nand_3_out, nand_1_out);
  nand nand_6 (nand_6_out, nand_4_out, nand_5_out);
  nand nand_7 (nand_7_out, A_9, B_9);
  nand nand_8 (nand_8_out, A_5, B_5);
  nand nand_9 (nand_9_out, A_10, B_10);
  nand nand_10 (nand_10_out, A_8, B_8);
  nand nand_11 (nand_11_out, A_6, B_6);
  nand nand_12 (nand_12_out, A_7, B_7);
  nand nand_13 (nand_13_out, A_9, nand_7_out);
  nand nand_14 (nand_14_out, nand_7_out, B_9);
  nand nand_15 (nand_15_out, A_5, nand_8_out);
  nand nand_16 (nand_16_out, nand_8_out, B_5);
  nand nand_17 (nand_17_out, A_10, nand_9_out);
  nand nand_18 (nand_18_out, nand_9_out, B_10);
  nand nand_19 (nand_19_out, A_8, nand_10_out);
  nand nand_20 (nand_20_out, nand_10_out, B_8);
  nand nand_21 (nand_21_out, nand_13_out, nand_14_out);
  nand nand_22 (nand_22_out, A_6, nand_11_out);
  nand nand_23 (nand_23_out, nand_11_out, B_6);
  nand nand_24 (nand_24_out, A_7, nand_12_out);
  nand nand_25 (nand_25_out, nand_12_out, B_7);
  nand nand_26 (nand_26_out, A_4, B_4);
  nand nand_27 (nand_27_out, nand_15_out, nand_16_out);
  nand nand_28 (nand_28_out, nand_17_out, nand_18_out);
  nand nand_29 (nand_29_out, nand_19_out, nand_20_out);
  nand nand_30 (nand_30_out, nand_22_out, nand_23_out);
  nand nand_31 (nand_31_out, nand_24_out, nand_25_out);
  nand nand_32 (nand_32_out, I1_6, nand_21_out);
  nand nand_33 (nand_33_out, B_9, I0_6);
  nand nand_34 (nand_34_out, I1_3, nand_27_out);
  nand nand_35 (nand_35_out, I0_3, B_5);
  nand nand_36 (nand_36_out, I1_7, nand_28_out);
  nand nand_37 (nand_37_out, I0_7, B_10);
  nand nand_38 (nand_38_out, A_4, nand_26_out);
  nand nand_39 (nand_39_out, nand_26_out, B_4);
  nand nand_40 (nand_40_out, I1_5, nand_29_out);
  nand nand_41 (nand_41_out, B_8, I0_5);
  nand nand_42 (nand_42_out, I1_4, nand_30_out);
  nand nand_43 (nand_43_out, B_6, I0_4);
  nand nand_44 (nand_44_out, I5, nand_31_out);
  nand nand_45 (nand_45_out, B_7, I4);
  nand nand_46 (nand_46_out, nand_32_out, nand_33_out);
  nand nand_47 (nand_47_out, I2_3, I2_3);
  nand nand_48 (nand_48_out, nand_34_out, nand_35_out);
  nand nand_49 (nand_49_out, nand_36_out, nand_37_out);
  nand nand_50 (nand_50_out, B_4, nand_26_out);
  nand nand_51 (nand_51_out, nand_38_out, nand_39_out);
  nand nand_52 (nand_52_out, nand_40_out, nand_41_out);
  nand nand_53 (nand_53_out, nand_42_out, nand_43_out);
  nand nand_54 (nand_54_out, nand_44_out, nand_45_out);
  nand nand_55 (nand_55_out, nand_48_out, C_2);
  nand nand_56 (nand_56_out, I3_3, nand_9_out);
  nand nand_57 (nand_57_out, I2_5, nand_49_out);
  nand nand_58 (nand_58_out, nand_67_out, C_7);
  nand nand_59 (nand_59_out, nand_46_out, C_6);
  nand nand_60 (nand_60_out, nand_53_out, C_3);
  nand nand_61 (nand_61_out, nand_54_out, C_4);
  nand nand_62 (nand_62_out, I1_2, nand_50_out);
  nand nand_63 (nand_63_out, nand_51_out, I0_2);
  nand nand_64 (Carry_8, nand_8_out, nand_55_out);
  nand nand_65 (nand_65_out, nand_48_out, nand_55_out);
  nand nand_66 (nand_66_out, nand_55_out, C_2);
  nand nand_67 (nand_67_out, nand_56_out, nand_57_out);
  nand nand_68 (nand_68_out, nand_52_out, C_5);
  nand nand_69 (nand_69_out, nand_7_out, nand_59_out);
  nand nand_70 (nand_70_out, nand_46_out, nand_59_out);
  nand nand_71 (nand_71_out, nand_59_out, C_6);
  nand nand_72 (nand_72_out, nand_67_out, nand_58_out);
  nand nand_73 (nand_73_out, nand_58_out, C_7);
  nand nand_74 (nand_74_out, nand_11_out, nand_60_out);
  nand nand_75 (nand_75_out, nand_53_out, nand_60_out);
  nand nand_76 (nand_76_out, nand_60_out, C_3);
  nand nand_77 (nand_77_out, nand_12_out, nand_61_out);
  nand nand_78 (nand_78_out, nand_54_out, nand_61_out);
  nand nand_79 (nand_79_out, nand_61_out, C_4);
  nand nand_80 (nand_80_out, nand_62_out, nand_63_out);
  nand nand_81 (nand_81_out, nand_10_out, nand_68_out);
  nand nand_82 (nand_82_out, nand_52_out, nand_68_out);
  nand nand_83 (nand_83_out, nand_68_out, C_5);
  nand nand_84 (nand_84_out, nand_70_out, nand_71_out);
  nand nand_85 (Sum_3, nand_65_out, nand_66_out);
  nand nand_86 (Sum_8, nand_72_out, nand_73_out);
  nand nand_87 (nand_87_out, nand_80_out, C);
  nand nand_88 (nand_88_out, nand_82_out, nand_83_out);
  LED led_1 (.in(nand_74_out));
  nand nand_89 (nand_89_out, nand_74_out, I3_2);
  nand nand_90 (nand_90_out, nand_75_out, nand_76_out);
  nand nand_91 (nand_91_out, nand_78_out, nand_79_out);
  LED led_2 (.in(nand_84_out));
  nand nand_92 (nand_92_out, nand_80_out, nand_87_out);
  nand nand_93 (nand_93_out, nand_87_out, C);
  nand nand_94 (nand_94_out, nand_90_out, I2_2);
  nand nand_95 (nand_95_out, nand_77_out, I7);
  nand nand_96 (nand_96_out, nand_91_out, I6);
  nand nand_97 (nand_97_out, nand_69_out, AL_4);
  nand nand_98 (nand_98_out, nand_84_out, nand_47_out);
  nand nand_99 (nand_99_out, nand_69_out, I2_3);
  nand nand_100 (nand_100_out, Carry_8, AL_2);
  nand nand_101 (nand_101_out, nand_9_out, AL_5);
  nand nand_102 (nand_102_out, nand_58_out, AL_5);
  nand nand_103 (Sum_2, nand_92_out, nand_93_out);
  nand nand_104 (Carry_2, nand_87_out, nand_26_out);
  nand nand_105 (nand_105_out, nand_81_out, AL_3);
  nand nand_106 (nand_106_out, nand_88_out, XOR);
  nand nand_107 (nand_107_out, AND, nand_81_out);
  nand nand_108 (Carry_4, nand_89_out, nand_89_out);
  nand nand_109 (Sum_4, nand_89_out, nand_94_out);
  nand nand_110 (Carry_5, nand_95_out, nand_95_out);
  nand nand_111 (Sum_5, nand_96_out, nand_96_out);
  nand nand_112 (Carry_7, nand_97_out, nand_97_out);
  nand nand_113 (Sum_7, nand_98_out, nand_99_out);
  nand nand_114 (Carry_3, nand_100_out, nand_100_out);
  nand nand_115 (Carry_9, nand_101_out, nand_102_out);
  nand nand_116 (Carry_6, nand_105_out, nand_105_out);
  nand nand_117 (Sum_6, nand_106_out, nand_107_out);
  LED led_3 (.in(Carry_5));
  nand nand_118 (nand_118_out, A_20, B_20);
  nand nand_119 (nand_119_out, A_21, B_21);
  nand nand_120 (nand_120_out, I, A_19);
  nand nand_121 (nand_121_out, nand_118_out, nand_118_out);
  nand nand_122 (nand_122_out, nand_119_out, nand_119_out);
  nand nand_123 (nand_123_out, I2_8, A_16);
  nand nand_124 (nand_124_out, I3_5, A_18);
  nand nand_125 (nand_125_out, nand_120_out, B_19);
  nand nand_126 (nand_126_out, nand_121_out, XOR_nOR);
  nand nand_127 (nand_127_out, nand_122_out, XOR_nOR_3);
  nand nand_128 (nand_128_out, I2_8, nand_123_out);
  nand nand_129 (nand_129_out, I3_5, nand_124_out);
  nand nand_130 (nand_130_out, I2_7, A_15);
  nand nand_131 (nand_131_out, nand_120_out, nand_125_out);
  nand nand_132 (nand_132_out, nand_125_out, B_19);
  nand nand_133 (nand_133_out, A_20, nand_126_out);
  nand nand_134 (nand_134_out, nand_126_out, B_20);
  nand nand_135 (nand_135_out, A_21, nand_127_out);
  nand nand_136 (nand_136_out, nand_127_out, B_21);
  nand nand_137 (nand_137_out, A_17, B_18);
  nand nand_138 (nand_138_out, B_12, B_12);
  nand nand_139 (nand_139_out, A_12, A_12);
  nand nand_140 (nand_140_out, I2_7, nand_130_out);
  nand nand_141 (nand_141_out, A_14, B_14);
  nand nand_142 (nand_142_out, nand_128_out, B_16);
  nand nand_143 (nand_143_out, nand_129_out, B_17);
  nand nand_144 (nand_144_out, nand_133_out, nand_134_out);
  nand nand_145 (nand_145_out, nand_135_out, nand_136_out);
  nand nand_146 (nand_146_out, A_17, nand_137_out);
  nand nand_147 (nand_147_out, nand_137_out, nand_137_out);
  nand nand_148 (nand_148_out, nand_137_out, B_18);
  nand nand_149 (out_160, nand_131_out, nand_132_out);
  nand nand_150 (nand_150_out, I11, A_12);
  nand nand_151 (nand_151_out, I10, nand_139_out);
  nand nand_152 (nand_152_out, I9, A_12);
  nand nand_153 (nand_153_out, I8, nand_139_out);
  nand nand_154 (nand_154_out, A_14, nand_141_out);
  nand nand_155 (nand_155_out, nand_141_out, nand_141_out);
  nand nand_156 (nand_156_out, nand_141_out, B_14);
  nand nand_157 (nand_157_out, nand_128_out, nand_142_out);
  nand nand_158 (nand_158_out, nand_142_out, nand_142_out);
  nand nand_159 (nand_159_out, nand_142_out, B_16);
  nand nand_160 (nand_160_out, nand_129_out, nand_143_out);
  nand nand_161 (nand_161_out, nand_143_out, nand_143_out);
  nand nand_162 (nand_162_out, nand_143_out, B_17);
  nand nand_163 (nand_163_out, nand_145_out, C_13);
  nand nand_164 (nand_164_out, A_13, B_13);
  nand nand_165 (nand_165_out, nand_140_out, B_15);
  nand nand_166 (nand_166_out, nand_150_out, nand_151_out);
  nand nand_167 (nand_167_out, nand_152_out, nand_153_out);
  nand nand_168 (nand_168_out, nand_154_out, nand_156_out);
  nand nand_169 (nand_169_out, nand_157_out, nand_159_out);
  nand nand_170 (nand_170_out, nand_146_out, nand_148_out);
  nand nand_171 (nand_171_out, nand_144_out, C_12);
  nand nand_172 (nand_172_out, B_2, A_2);
  nand nand_173 (nand_173_out, B_3, B_3);
  nand nand_174 (nand_174_out, A_3, A_3);
  nand nand_175 (nand_175_out, A_13, nand_164_out);
  nand nand_176 (nand_176_out, nand_164_out, nand_164_out);
  nand nand_177 (nand_177_out, nand_164_out, B_13);
  nand nand_178 (nand_178_out, nand_140_out, nand_165_out);
  nand nand_179 (nand_179_out, nand_165_out, nand_165_out);
  nand nand_180 (nand_180_out, nand_165_out, B_15);
  nand nand_181 (nand_181_out, nand_160_out, nand_162_out);
  nand nand_182 (nand_182_out, I1_14, nand_170_out);
  nand nand_183 (nand_183_out, nand_147_out, I0_14);
  nand nand_184 (nand_184_out, A, B);
  nand nand_185 (nand_185_out, B_12, nand_166_out);
  nand nand_186 (nand_186_out, nand_167_out, nand_138_out);
  nand nand_187 (nand_187_out, I1_10, nand_168_out);
  nand nand_188 (nand_188_out, nand_155_out, I0_10);
  nand nand_189 (nand_189_out, I1_12, nand_169_out);
  nand nand_190 (nand_190_out, nand_158_out, I0_12);
  nand nand_191 (nand_191_out, I1_13, nand_181_out);
  nand nand_192 (nand_192_out, nand_161_out, I0_13);
  nand nand_193 (Carry_14, nand_118_out, nand_171_out);
  nand nand_194 (nand_194_out, nand_171_out, nand_171_out);
  nand nand_195 (nand_195_out, nC, nand_172_out);
  nand nand_196 (nand_196_out, I3, A_3);
  nand nand_197 (nand_197_out, I2, nand_174_out);
  nand nand_198 (nand_198_out, I1, A_3);
  nand nand_199 (nand_199_out, I0, nand_174_out);
  nand nand_200 (F_2, nand_185_out, nand_186_out);
  nand nand_201 (nand_201_out, nand_175_out, nand_177_out);
  nand nand_202 (nand_202_out, nand_178_out, nand_180_out);
  nand nand_203 (nand_203_out, nand_182_out, nand_183_out);
  nand nand_204 (nand_204_out, nand_194_out, XOR_nOR);
  nand nand_205 (nand_205_out, nand_195_out, AL);
  nand nand_206 (nand_206_out, nand_187_out, nand_188_out);
  nand nand_207 (nand_207_out, nand_189_out, nand_190_out);
  nand nand_208 (nand_208_out, nand_191_out, nand_192_out);
  nand nand_209 (nand_209_out, A, nand_184_out);
  nand nand_210 (nand_210_out, nand_184_out, B);
  nand nand_211 (nand_211_out, SEL_B, Bin);
  nand nand_212 (nand_212_out, SEL_A, Ain);
  nand nand_213 (nand_213_out, nand_196_out, nand_197_out);
  nand nand_214 (nand_214_out, nand_198_out, nand_199_out);
  nand nand_215 (nand_215_out, I1_9, nand_201_out);
  nand nand_216 (nand_216_out, nand_176_out, I0_9);
  nand nand_217 (nand_217_out, I1_11, nand_202_out);
  nand nand_218 (nand_218_out, nand_179_out, I0_11);
  nand nand_219 (nand_219_out, nand_203_out, C_11);
  nand nand_220 (nand_220_out, nand_144_out, nand_204_out);
  nand nand_221 (nand_221_out, nand_204_out, C_12);
  nand nand_222 (out_18, nand_205_out, nand_205_out);
  nand nand_223 (nand_223_out, nand_206_out, C_8);
  nand nand_224 (nand_224_out, nand_207_out, C_9);
  nand nand_225 (nand_225_out, nand_208_out, C_10);
  nand nand_226 (Carry, nand_184_out, nand_184_out);
  nand nand_227 (Sum, nand_209_out, nand_210_out);
  nand nand_228 (Dout, nand_211_out, nand_212_out);
  nand nand_229 (nand_229_out, B_3, nand_213_out);
  nand nand_230 (nand_230_out, nand_214_out, nand_173_out);
  nand nand_231 (out_106, nand_215_out, nand_216_out);
  nand nand_232 (out_118, nand_217_out, nand_218_out);
  nand nand_233 (nand_233_out, nand_145_out, nand_163_out);
  nand nand_234 (nand_234_out, nand_163_out, C_13);
  nand nand_235 (F, nand_229_out, nand_230_out);
  nand nand_236 (nand_236_out, nand_141_out, nand_223_out);
  nand nand_237 (nand_237_out, nand_206_out, nand_223_out);
  nand nand_238 (nand_238_out, nand_223_out, C_8);
  nand nand_239 (nand_239_out, nand_142_out, nand_224_out);
  nand nand_240 (nand_240_out, nand_207_out, nand_224_out);
  nand nand_241 (nand_241_out, nand_224_out, C_9);
  nand nand_242 (nand_242_out, nand_137_out, nand_219_out);
  nand nand_243 (nand_243_out, nand_203_out, nand_219_out);
  nand nand_244 (nand_244_out, nand_219_out, C_11);
  nand nand_245 (Sum_13, nand_220_out, nand_221_out);
  nand nand_246 (nand_246_out, nand_225_out, nand_225_out);
  nand nand_247 (nand_247_out, nand_208_out, nand_225_out);
  nand nand_248 (nand_248_out, nand_225_out, C_10);
  nand nand_249 (Carry_15, nand_127_out, nand_163_out);
  nand nand_250 (Sum_14, nand_233_out, nand_234_out);
  nand nand_251 (nand_251_out, I12, nand_242_out);
  nand nand_252 (Sum_12, nand_243_out, nand_244_out);
  nand nand_253 (nand_253_out, I2_6, nand_236_out);
  nand nand_254 (Sum_9, nand_237_out, nand_238_out);
  nand nand_255 (nand_255_out, I3_4, nand_239_out);
  nand nand_256 (Sum_10, nand_240_out, nand_241_out);
  nand nand_257 (nand_257_out, nand_161_out, I2_9);
  nand nand_258 (nand_258_out, I2_9, nand_246_out);
  nand nand_259 (Sum_11, nand_247_out, nand_248_out);
  nand nand_260 (Carry_13, nand_251_out, nand_251_out);
  nand nand_261 (Carry_10, nand_253_out, nand_253_out);
  nand nand_262 (Carry_11, nand_255_out, nand_255_out);
  nand nand_263 (Carry_12, nand_257_out, nand_258_out);
  nand nand_264 (nand_264_out, A_22, A_22);
  nand nand_265 (nand_265_out, nand_264_out, Blk);
  nand nand_266 (nand_266_out, DATA, CLK);
  nand nand_267 (nand_267_out, nand_266_out, CLK);
  nand nand_268 (Q_2, nSet, nQ_2);
  nand nand_269 (nQ_2, Q_2, nReset);
  nand nand_270 (nand_270_out, nWRX, nand_290_out);
  nand nand_271 (nand_271_out, nWRY, nand_290_out);
  nand nand_272 (nand_272_out, nand_265_out, B_22);
  nand nand_273 (Q, nand_266_out, nQ);
  nand nand_274 (nQ, Q, nand_267_out);
  nand nand_275 (nand_275_out, nand_265_out, nand_272_out);
  nand nand_276 (nand_276_out, nand_272_out, nand_272_out);
  nand nand_277 (nand_277_out, nand_272_out, B_22);
  nand nand_278 (nand_278_out, nand_270_out, nand_279_out);
  nand nand_279 (nand_279_out, nand_278_out, nCLX);
  nand nand_280 (nand_280_out, nand_271_out, nand_281_out);
  nand nand_281 (nand_281_out, nand_280_out, nCLY);
  nand nand_282 (nand_282_out, nand_275_out, nand_277_out);
  nand nand_283 (nand_283_out, I3_6, Cin);
  nand nand_284 (nand_284_out, I1_15, nand_282_out);
  nand nand_285 (nand_285_out, nand_276_out, I0_15);
  nand nand_286 (nand_286_out, I2_10, nand_283_out);
  nand nand_287 (nand_287_out, nRDX, nand_278_out);
  nand nand_288 (nand_288_out, nRDY, nand_280_out);
  nand nand_289 (nand_289_out, nand_284_out, nand_285_out);
  nand nand_290 (nand_290_out, nand_287_out, nand_288_out);
  nand nand_291 (nand_291_out, nand_289_out, nand_286_out);
  LED led_4 (.in(nand_290_out));
  nand nand_292 (nand_292_out, nand_289_out, nand_291_out);
  nand nand_293 (nand_293_out, nand_291_out, nand_286_out);
  nand nand_294 (CARRY_16, nand_272_out, nand_291_out);
  nand nand_295 (SUM_15, nand_292_out, nand_293_out);

  // Notes on the sheet:
  //   C  I1 I0
  //   0   0   0      F = 0
  //   0   0   1      F = B 
  //   0   1   0      F = A XOR B
  //   0   1   1      F = A OR B
  //   1   0   0      F = 1
  //   1   0   1      F = ~B
  //   1   1   0      F = A XNOR B
  //   1   1   1      F = A NOR B
  //   C  I1 I0
  //   0   0   0    F = 0
  //   0   0   1    F = A XOR B 
  //   0   1   0    F = A AND B
  //   0   1   1    F = A OR B
  //   1   0   0    F = 1
  //   1   0   1    F = A XNOR B
  //   1   1   0    F = A NAND B
  //   1   1   1    F = A NOR B
  //   12+2 GATE ALU  - With Carry Suppression
  //   Half Adder AND/XOR
  //   16 GATE ALU
  //   2 Input Mux
  //   13 Gate ALU
  //   Half Adder / Invert
  //   15 Gate ALU bit-slice with Zero, B, ~B, One, Zero, AND, XOR, OR,  ADD
  //   0 0     Zero
  //   0 1     A AND B
  //   1 0     A XOR B
  //   1 1     A OR B
  //   18 Gate ALU bit-slice with Zero, B, ~B, One, Zero, AND, XOR, OR,  ADD
  //   Instruction I3 I2 I1 I0
  //   0000   F = 0
  //   0001   F = A NOR B
  //   0010   F = A AND ~B
  //   0011  F = ~B
  //   0100  F = ~A AND B
  //   0101  F = ~A
  //   0110  F = A XOR B
  //   0111  F = A NAND B
  //   1000  F = A AND B
  //   1001  F = A XNOR B
  //   1010  F = A
  //   1011  F = A OR ~B
  //   1100  F = B
  //   1101 F = ~A OR B
  //   1110   F = A OR B
  //   1111  F = 1
  //   17 Gate ALU bit-slice with Zero, B, ~B, One, Zero, AND, XOR, OR,  ADD
  //   LOGIC UNIT (74HC153 4:1 MUX)
  //   Zero,  B, ~B, One, Zero, AND, XOR, OR,
  //   15 Gate ALU with Zero, AND, XOR, OR,  ADD
  //   Zero, AND, XOR, OR
  //   0 0 0     Zero
  //   0 0 1     B
  //   0 1 0     ~B
  //   0 1 1     One
  //   1 0 0     Zero
  //   1 0 1     A AND B
  //   1 1 0     A XOR B
  //   1 1 1     A OR B
  //   CARRY LOGIC
  //   2 Input Multiplexer
  //   NOT(A&B)
  //   NOT(B&C)
  //   SR Flipflop
  //   Gated Latch
endmodule
