// Digital circuit 2_phase_clock.dig as structural Verilog
module _2_phase_clock (
  input  CLK,
  input  RESET,
  input  in_5,
  input  in_6,
  input  nJMP,
  input  IR4,
  input  Cout,
  input  IR2,
  input  IR3,
  input  AC7,
  output SELPC,
  output SELDATA,
  output out_13
);

  wire AL, AR0, AR1, AR2, AR3, diodebackward_1_out, diodebackward_3_out, diodebackward_5_out,
       diodebackward_9_out, diodebackward_14_out, diodebackward_17_out, IR4_t, IR5, IR6, nand_1_out,
       nand_2_out, nand_3_out, nand_4_out, nand_5_out, nand_6_out, nand_7_out, nand_8_out, nand_9_out,
       nand_10_out, nand_11_out, nand_13_out, nand_14_out, nand_15_out, nand_16_out, nand_17_out,
       nand_20_out, nand_21_out, nand_25_out, nand_26_out, nand_27_out, nand_28_out, nand_29_out,
       nand_30_out, nand_31_out, nand_32_out, nand_33_out, nand_34_out, nand_35_out, nand_36_out,
       nand_37_out, nand_38_out, nand_41_out, nand_42_out, nand_43_out, nand_44_out, nand_45_out,
       nand_46_out, nand_47_out, nand_48_out, nand_49_out, nand_50_out, nand_51_out, nand_52_out,
       nand_53_out, nand_54_out, nand_55_out, nand_56_out, nand_57_out, nand_58_out, nand_59_out,
       nand_60_out, nand_61_out, nand_62_out, nand_63_out, nand_64_out, nand_65_out, nand_74_out,
       nand_75_out, nextS, nJMP_t, nPH0, nPH1, nW, PH0, PH1, W;

  DiodeBackward diodebackward_1 (.in(nJMP), .out(diodebackward_1_out));
  DiodeBackward diodebackward_2 (.in(SELDATA), .out(diodebackward_1_out));
  nand nand_1 (nand_1_out, CLK, CLK);
  PullUp pullup_1 (.out(diodebackward_1_out));
  nand nand_2 (nand_2_out, in_5, in_6);
  nand nand_3 (nand_3_out, nand_2_out, in_6);
  nand nand_4 (nand_4_out, nand_1_out, nand_1_out);
  nand nand_5 (nand_5_out, PH1, PH1);
  nand nand_6 (nand_6_out, PH0, PH0);
  nand nand_7 (nand_7_out, CLK, CLK);
  nand nand_8 (nand_8_out, diodebackward_1_out, PH1);
  nand nand_9 (nand_9_out, nand_8_out, PH1);
  nand nand_10 (nand_10_out, nand_4_out, nand_5_out);
  nand nand_11 (nand_11_out, nand_6_out, nand_7_out);
  nand nand_12 (nextS, nand_8_out, nand_13_out);
  nand nand_13 (nand_13_out, nextS, nand_9_out);
  nand nand_14 (nand_14_out, nand_2_out, nand_15_out);
  nand nand_15 (nand_15_out, nand_14_out, nand_3_out);
  nand nand_16 (nand_16_out, nand_10_out, nand_10_out);
  nand nand_17 (nand_17_out, nand_11_out, nand_11_out);
  nand nand_18 (nPH0, nand_16_out, nand_16_out);
  nand nand_19 (nPH1, nand_17_out, nand_17_out);
  nand nand_20 (nand_20_out, nextS, PH0);
  nand nand_21 (nand_21_out, nand_20_out, PH0);
  nand nand_22 (PH0, nPH0, nPH0);
  nand nand_23 (PH1, nPH1, nPH1);
  nand nand_24 (SELPC, nand_20_out, nand_25_out);
  nand nand_25 (nand_25_out, SELPC, nand_21_out);
  nand nand_26 (nand_26_out, Cout, Cout);
  nand nand_27 (nand_27_out, AC7, AC7);
  nand nand_28 (nand_28_out, 1'b0, Cout);
  nand nand_29 (nand_29_out, IR4, nand_26_out);
  nand nand_30 (nand_30_out, IR3, Cout);
  nand nand_31 (nand_31_out, IR2, nand_26_out);
  nand nand_32 (nand_32_out, nand_28_out, nand_29_out);
  nand nand_33 (nand_33_out, nand_30_out, nand_31_out);
  nand nand_34 (nand_34_out, SELPC, SELPC);
  nand nand_35 (nand_35_out, RESET, RESET);
  nand nand_36 (nand_36_out, AC7, nand_32_out);
  nand nand_37 (nand_37_out, nand_33_out, nand_27_out);
  nand nand_38 (nand_38_out, nand_34_out, nand_35_out);
  nand nand_39 (out_13, nand_36_out, nand_37_out);
  nand nand_40 (SELDATA, nand_38_out, nand_38_out);
  nand nand_41 (nand_41_out, IR4_t, IR4_t);
  nand nand_42 (nand_42_out, IR5, IR5);
  nand nand_43 (nand_43_out, IR6, IR6);
  nand nand_44 (nand_44_out, nand_41_out, nand_42_out);
  nand nand_45 (nand_45_out, IR4_t, nand_42_out);
  nand nand_46 (nand_46_out, nand_41_out, IR5);
  nand nand_47 (nand_47_out, IR4_t, IR5);
  nand nand_48 (nand_48_out, nand_41_out, nand_42_out);
  nand nand_49 (nand_49_out, IR4_t, nand_42_out);
  nand nand_50 (nand_50_out, nand_41_out, IR5);
  nand nand_51 (nand_51_out, IR4_t, IR5);
  nand nand_52 (nand_52_out, nand_44_out, nand_44_out);
  nand nand_53 (nand_53_out, nand_45_out, nand_45_out);
  nand nand_54 (nand_54_out, nand_46_out, nand_46_out);
  nand nand_55 (nand_55_out, nand_47_out, nand_47_out);
  nand nand_56 (nand_56_out, nand_48_out, nand_48_out);
  nand nand_57 (nand_57_out, nand_49_out, nand_49_out);
  nand nand_58 (nand_58_out, nand_50_out, nand_50_out);
  nand nand_59 (nand_59_out, nand_51_out, nand_51_out);
  nand nand_60 (nand_60_out, nand_52_out, nand_43_out);
  nand nand_61 (nand_61_out, nand_53_out, nand_43_out);
  nand nand_62 (nand_62_out, nand_54_out, nand_43_out);
  nand nand_63 (nand_63_out, nand_55_out, nand_43_out);
  nand nand_64 (nand_64_out, nand_56_out, IR6);
  nand nand_65 (nand_65_out, nand_57_out, IR6);
  nand nand_66 (nW, nand_58_out, IR6);
  nand nand_67 (nJMP_t, nand_59_out, IR6);
  DiodeBackward diodebackward_3 (.in(nJMP_t), .out(diodebackward_3_out));
  DiodeBackward diodebackward_4 (.in(IR6), .out(diodebackward_3_out));
  PullUp pullup_2 (.out(diodebackward_3_out));
  DiodeBackward diodebackward_5 (.in(nand_60_out), .out(diodebackward_5_out));
  DiodeBackward diodebackward_6 (.in(nand_61_out), .out(diodebackward_5_out));
  DiodeBackward diodebackward_7 (.in(nand_62_out), .out(diodebackward_5_out));
  DiodeBackward diodebackward_8 (.in(nand_64_out), .out(diodebackward_5_out));
  nand nand_68 (AL, diodebackward_3_out, diodebackward_3_out);
  PullUp pullup_3 (.out(diodebackward_5_out));
  DiodeBackward diodebackward_9 (.in(nand_60_out), .out(diodebackward_9_out));
  DiodeBackward diodebackward_10 (.in(nand_62_out), .out(diodebackward_9_out));
  DiodeBackward diodebackward_11 (.in(nand_63_out), .out(diodebackward_9_out));
  DiodeBackward diodebackward_12 (.in(nand_64_out), .out(diodebackward_9_out));
  DiodeBackward diodebackward_13 (.in(nW), .out(diodebackward_9_out));
  nand nand_69 (AR3, diodebackward_5_out, diodebackward_5_out);
  PullUp pullup_4 (.out(diodebackward_9_out));
  DiodeBackward diodebackward_14 (.in(nand_62_out), .out(diodebackward_14_out));
  DiodeBackward diodebackward_15 (.in(nand_63_out), .out(diodebackward_14_out));
  DiodeBackward diodebackward_16 (.in(nand_65_out), .out(diodebackward_14_out));
  nand nand_70 (AR2, diodebackward_9_out, diodebackward_9_out);
  PullUp pullup_5 (.out(diodebackward_14_out));
  DiodeBackward diodebackward_17 (.in(nand_65_out), .out(diodebackward_17_out));
  DiodeBackward diodebackward_18 (.in(nW), .out(diodebackward_17_out));
  nand nand_71 (AR1, diodebackward_14_out, diodebackward_14_out);
  PullUp pullup_6 (.out(diodebackward_17_out));
  nand nand_72 (AR0, diodebackward_17_out, diodebackward_17_out);
  nand nand_73 (W, nW, nW);
  nand nand_74 (nand_74_out, 1'b0, 1'b0);
  LED led_1 (.in(nand_60_out));
  LED led_2 (.in(nand_61_out));
  LED led_3 (.in(nand_62_out));
  LED led_4 (.in(nand_63_out));
  LED led_5 (.in(nand_64_out));
  LED led_6 (.in(nand_65_out));
  LED led_7 (.in(nW));
  LED led_8 (.in(nJMP_t));
  nand nand_75 (nand_75_out, 1'b0, 1'b0);

  // Other names for the same wires on the sheet: S = SELPC; SD = SELDATA

  // Notes on the sheet:
  //   CLK: Hz: 2
  //   IR4  IR3  IR2
  //   0      0      0   Far Jump
  //   0      0      1   AC > 0    BGT
  //   0      1      0   AC < 0    BLT
  //   0      1      1   AC  != 0  BNE
  //   1      0      0   AC = 0    BEQ
  //   1      0      1   AC >= 0   BGE
  //   1      1      0   AC <= 0   BLE
  //   1      1      1   Branch Always BRA
  //   Two Phase Clock Generator
  //   Carry latch
  //   Next State
  //   Stare Generator
  //   Current State
  //   Condition Decoder
  //   CONTROL UNIT
  //   3 to 8 Instruction decoder - 27 Gates
  //   Octal Inverter/Driver
  //   LOAD
  //   AND
  //   OR
  //   XOR
  //   ADD
  //   SUB
  //   STORE
  //   JMP
endmodule
