// Digital circuit 2x157_Octal_Mux.dig as structural Verilog
module _2x157_Octal_Mux (
  input  B0,
  input  A_nB,
  input  A0,
  input  B1,
  input  A1,
  input  B2,
  input  A2,
  input  B3,
  input  A3,
  input  B4,
  input  A4,
  input  B5,
  input  A5,
  input  B6,
  input  A6,
  input  B7,
  input  A7,
  input  VCC,
  input  GND,
  input  VSS,
  input  EN,
  output D0,
  output D1,
  output D2,
  output D3,
  output D4,
  output D5,
  output D6,
  output D7
);

  wire nand_1_out, nand_2_out, nand_3_out, nand_4_out, nand_5_out, nand_6_out, nand_7_out, nand_8_out,
       nand_9_out, nand_10_out, nand_11_out, nand_12_out, nand_13_out, nand_14_out, nand_15_out, nand_16_out,
       nand_17_out, nand_18_out, nand_19_out, nand_20_out, nand_21_out, nand_22_out, nand_23_out,
       nand_24_out, nand_25_out, nand_26_out, nand_27_out, nand_28_out, nand_29_out, nand_30_out,
       nand_31_out, nand_32_out, nand_33_out, nand_34_out, nand_35_out, nand_36_out, nand_37_out,
       nand_38_out, nand_39_out, nand_40_out;

  PowerSupply powersupply_1 (.VDD(VCC), .GND(GND));
  nand nand_1 (nand_1_out, A_nB, A_nB);
  nand nand_2 (nand_2_out, A_nB, A_nB);
  nand nand_3 (nand_3_out, A_nB, A_nB);
  nand nand_4 (nand_4_out, A_nB, A_nB);
  nand nand_5 (nand_5_out, A_nB, A_nB);
  nand nand_6 (nand_6_out, A_nB, A_nB);
  nand nand_7 (nand_7_out, A_nB, A_nB);
  nand nand_8 (nand_8_out, A_nB, A_nB);
  nand nand_9 (nand_9_out, A0, A_nB);
  nand nand_10 (nand_10_out, nand_1_out, B0);
  nand nand_11 (nand_11_out, A1, A_nB);
  nand nand_12 (nand_12_out, nand_2_out, B1);
  nand nand_13 (nand_13_out, A2, A_nB);
  nand nand_14 (nand_14_out, nand_3_out, B2);
  nand nand_15 (nand_15_out, A3, A_nB);
  nand nand_16 (nand_16_out, nand_4_out, B3);
  nand nand_17 (nand_17_out, A4, A_nB);
  nand nand_18 (nand_18_out, nand_5_out, B4);
  nand nand_19 (nand_19_out, A5, A_nB);
  nand nand_20 (nand_20_out, nand_6_out, B5);
  nand nand_21 (nand_21_out, A6, A_nB);
  nand nand_22 (nand_22_out, nand_7_out, B6);
  nand nand_23 (nand_23_out, A7, A_nB);
  nand nand_24 (nand_24_out, nand_8_out, B7);
  nand nand_25 (nand_25_out, nand_9_out, nand_10_out);
  nand nand_26 (nand_26_out, nand_11_out, nand_12_out);
  nand nand_27 (nand_27_out, nand_13_out, nand_14_out);
  nand nand_28 (nand_28_out, nand_15_out, nand_16_out);
  nand nand_29 (nand_29_out, nand_17_out, nand_18_out);
  nand nand_30 (nand_30_out, nand_19_out, nand_20_out);
  nand nand_31 (nand_31_out, nand_21_out, nand_22_out);
  nand nand_32 (nand_32_out, nand_23_out, nand_24_out);
  nand nand_33 (nand_33_out, EN, nand_25_out);
  nand nand_34 (nand_34_out, EN, nand_26_out);
  nand nand_35 (nand_35_out, EN, nand_27_out);
  nand nand_36 (nand_36_out, EN, nand_28_out);
  nand nand_37 (nand_37_out, EN, nand_29_out);
  nand nand_38 (nand_38_out, EN, nand_30_out);
  nand nand_39 (nand_39_out, EN, nand_31_out);
  nand nand_40 (nand_40_out, EN, nand_32_out);
  nand nand_41 (D0, nand_33_out, nand_33_out);
  nand nand_42 (D1, nand_34_out, nand_34_out);
  nand nand_43 (D2, nand_35_out, nand_35_out);
  nand nand_44 (D3, nand_36_out, nand_36_out);
  nand nand_45 (D4, nand_37_out, nand_37_out);
  nand nand_46 (D5, nand_38_out, nand_38_out);
  nand nand_47 (D6, nand_39_out, nand_39_out);
  nand nand_48 (D7, nand_40_out, nand_40_out);

  assign VSS = GND;

  // Notes on the sheet:
  //   B0: pin 12
  //   A_nB: pin 1
  //   A0: pin 3
  //   B1: pin 13
  //   A1: pin 4
  //   B2: pin 14
  //   A2: pin 5
  //   B3: pin 15
  //   A3: pin 6
  //   B4: pin 16
  //   A4: pin 7
  //   B5: pin 17
  //   A5: pin 8
  //   B6: pin 18
  //   A6: pin 9
  //   B7: pin 19
  //   A7: pin 10
  //   D0: pin 38
  //   D1: pin 37
  //   D2: pin 36
  //   D3: pin 35
  //   D4: pin 34
  //   D5: pin 33
  //   D6: pin 32
  //   D7: pin 31
  //   VCC: pin 40, default 1
  //   GND: pin 20
  //   VSS: pin 11
  //   EN: pin 2
endmodule
