// Digital circuit 4_bit_datapath_1.dig as structural Verilog
module _4_bit_datapath_1 (
  input  in_1,
  input  in_2,
  input  in_3,
  input  in_4,
  input  in_5,
  input  in_6,
  input  in_7,
  input  in_8,
  input  A,
  input  B,
  input  DAT,
  input  CLK,
  input  in_13,
  input  DAT_2,
  input  in_15,
  input  DAT_3,
  input  in_17,
  input  DATA_0,
  input  CK,
  input  nLD,
  input  in_21,
  input  in_22,
  input  in_23,
  input  in_24,
  input  in_25,
  input  in_26,
  input  D3,
  input  D2,
  input  D1,
  input  D0,
  input  S1,
  input  S0,
  input  E1,
  input  E0,
  input  in_35,
  input  in_36,
  input  in_37,
  input  in_38,
  input  C,
  input  S0_2,
  input  D,
  input  A_2,
  input  B_2,
  input  S1_2,
  input  EN,
  input  in_46,
  input  in_47,
  input  in_48,
  input  in_49,
  input  in_50,
  input  in_51,
  input  in_52,
  input  in_53,
  input  in_54,
  input  A_3,
  input  B_3,
  input  A_4,
  input  B_4,
  input  in_59,
  input  in_60,
  input  in_61,
  input  in_62,
  input  in_63,
  input  in_64,
  input  Zin,
  input  I0,
  input  I1,
  input  I2,
  input  I3,
  input  DATA_1,
  input  DATA_2,
  input  DATA_3,
  input  DATA,
  input  CK_2,
  input  nLD_2,
  input  RES,
  input  in_77,
  input  A_5,
  input  B_5,
  input  EN_2,
  input  S0_3,
  input  S1_3,
  input  EN_3,
  input  S0_4,
  input  S1_4,
  input  S2,
  input  B0,
  input  A_nB,
  input  A0,
  input  B1,
  input  A1,
  input  B2,
  input  A2,
  input  B3,
  input  A3,
  input  B4,
  input  A4,
  input  B5,
  input  A5,
  input  B6,
  input  A6,
  input  B7,
  input  A7,
  input  A_6,
  input  Invert_A_nA,
  input  B_6,
  input  Select_A_nB,
  input  A_7,
  input  A_8,
  input  in_120,
  input  D_2,
  input  LD,
  input  A_9,
  input  B_7,
  input  in_126,
  input  in_127,
  input  in_128,
  input  in_129,
  input  in_131,
  input  in_132,
  input  in_133,
  input  in_134,
  input  DATAin3,
  input  DATAin2,
  input  DATAin1,
  input  Din,
  input  C_in,
  input  Sel_Data,
  input  Sel_PC,
  input  CLK_2,
  input  C_2,
  input  D_3,
  input  A_10,
  input  B_8,
  input  Din0,
  input  EN_4,
  input  Cin,
  input  clk_3,
  input  Din1,
  input  Din2,
  input  Din3,
  output out_104,
  output out_105,
  output out_106,
  output out_107,
  output out_108,
  output out_109,
  output out_110,
  output out_111,
  output out_112,
  output out_113,
  output out_125,
  output out_130,
  output out_135,
  output out_137,
  output out_139,
  output out_141,
  output Dout,
  output Carry_Out,
  output Dout0,
  output Dout1,
  output Dout2,
  output Dout3
);

  wire nand_1_out, nand_2_out, nand_3_out, nand_4_out, nand_5_out, nand_6_out, nand_7_out, nand_8_out,
       nand_9_out, nand_10_out, nand_11_out, nand_12_out, nand_13_out, nand_14_out, nand_15_out, nand_16_out,
       nand_17_out, nand_18_out, nand_19_out, nand_20_out, nand_21_out, nand_22_out, nand_23_out,
       nand_24_out, nand_25_out, nand_26_out, nand_27_out, nand_28_out, nand_29_out, nand_30_out,
       nand_31_out, nand_32_out, nand_33_out, nand_34_out, nand_35_out, nand_36_out, nand_37_out,
       nand_38_out, nand_39_out, nand_40_out, nand_41_out, nand_42_out, nand_43_out, nand_44_out,
       nand_45_out, nand_46_out, nand_47_out, nand_48_out, nand_49_out, nand_50_out, nand_51_out,
       nand_52_out, nand_53_out, nand_54_out, nand_55_out, nand_56_out, nand_57_out, nand_58_out,
       nand_59_out, nand_60_out, nand_61_out, nand_62_out, nand_63_out, nand_64_out, nand_65_out,
       nand_66_out, nand_67_out, nand_68_out, nand_69_out, nand_70_out, nand_71_out, nand_72_out,
       nand_73_out, nand_74_out, nand_75_out, nand_76_out, nand_77_out, nand_78_out, nand_79_out,
       nand_80_out, nand_81_out, nand_82_out, nand_83_out, nand_84_out, nand_85_out, nand_86_out,
       nand_87_out, nand_88_out, nand_89_out, nand_90_out, nand_91_out, nand_92_out, nand_93_out,
       nand_94_out, nand_95_out, nand_96_out, nand_97_out, nand_98_out, nand_99_out, nand_100_out,
       nand_101_out, nand_102_out, nand_103_out, nand_104_out, nand_105_out, nand_106_out, nand_107_out,
       nand_108_out, nand_109_out, nand_110_out, nand_111_out, nand_112_out, nand_113_out, nand_114_out,
       nand_115_out, nand_116_out, nand_117_out, nand_118_out, nand_119_out, nand_120_out, nand_121_out,
       nand_122_out, nand_123_out, nand_124_out, nand_125_out, nand_126_out, nand_127_out, nand_128_out,
       nand_129_out, nand_130_out, nand_131_out, nand_132_out, nand_133_out, nand_134_out, nand_135_out,
       nand_136_out, nand_137_out, nand_138_out, nand_139_out, nand_141_out, nand_143_out, nand_145_out,
       nand_147_out, nand_148_out, nand_149_out, nand_150_out, nand_151_out, nand_152_out, nand_153_out,
       nand_154_out, nand_155_out, nand_156_out, nand_157_out, nand_158_out, nand_159_out, nand_160_out,
       nand_161_out, nand_162_out, nand_163_out, nand_164_out, nand_165_out, nand_166_out, nand_167_out,
       nand_168_out, nand_169_out, nand_170_out, nand_171_out, nand_172_out, nand_173_out, nand_174_out,
       nand_175_out, nand_176_out, nand_177_out, nand_178_out, nand_179_out, nand_180_out, nand_181_out,
       nand_182_out, nand_183_out, nand_184_out, nand_185_out, nand_186_out, nand_187_out, nand_188_out,
       nand_189_out, nand_190_out, nand_191_out, nand_192_out, nand_193_out, nand_194_out, nand_195_out,
       nand_196_out, nand_197_out, nand_198_out, nand_199_out, nand_200_out, nand_201_out, nand_202_out,
       nand_203_out, nand_204_out, nand_205_out, nand_206_out, nand_207_out, nand_208_out, nand_209_out,
       nand_210_out, nand_211_out, nand_212_out, nand_213_out, nand_214_out, nand_215_out, nand_216_out,
       nand_217_out, nand_218_out, nand_219_out, nand_220_out, nand_221_out, nand_222_out, nand_223_out,
       nand_224_out, nand_225_out, nand_226_out, nand_227_out, nand_228_out, nand_229_out, nand_230_out,
       nand_232_out, nand_233_out, nand_234_out, nand_235_out, nand_236_out, nand_237_out, nand_238_out,
       nand_239_out, nand_240_out, nand_241_out, nand_242_out, nand_243_out, nand_244_out, nand_245_out,
       nand_246_out, nand_247_out, nand_248_out, nand_249_out, nand_250_out, nand_251_out, nand_252_out,
       nand_253_out, nand_254_out, nand_255_out, nand_256_out, nand_257_out, nand_258_out, nand_259_out,
       nand_260_out, nand_261_out, nand_262_out, nand_263_out, nand_264_out, nand_265_out, nand_266_out,
       nand_267_out, nand_268_out, nand_269_out, nand_270_out, nand_271_out, nand_272_out, nand_273_out,
       nand_274_out, nand_275_out, nand_276_out, nand_277_out, nand_278_out, nand_279_out, nand_280_out,
       nand_281_out, nand_282_out, nand_283_out, nand_284_out, nand_285_out, nand_286_out, nand_287_out,
       nand_288_out, nand_289_out, nand_290_out, nand_291_out, nand_292_out, nand_293_out, nand_294_out,
       nand_295_out, nand_296_out, nand_297_out, nand_298_out, nand_299_out, nand_300_out, nand_301_out,
       nand_302_out, nand_303_out, nand_304_out, nand_305_out, nand_306_out, nand_307_out, nand_309_out,
       nand_311_out, nand_313_out, nand_315_out, nand_316_out, nand_317_out, nand_318_out, nand_319_out,
       nand_320_out, nand_321_out, nand_322_out, nand_323_out, nand_324_out, nand_325_out, nand_326_out,
       nand_327_out, nand_328_out, nand_329_out, nand_330_out, nand_331_out, nand_332_out, nand_333_out,
       nand_336_out, nand_337_out, nand_338_out, nand_340_out, nand_341_out, nand_343_out, nand_344_out,
       nand_346_out, nand_347_out, nand_348_out, nand_349_out, nand_350_out, nand_351_out, nand_352_out,
       nand_353_out, nand_354_out, nand_355_out, nand_356_out, nand_357_out, nand_358_out, nand_359_out,
       nand_360_out, nand_361_out, nand_362_out, nand_363_out, nand_364_out, nand_365_out, nand_366_out,
       nand_367_out, nand_368_out, nand_369_out, nand_370_out, nand_371_out, nand_372_out, nand_373_out,
       nand_374_out, nand_375_out, nand_376_out, nand_377_out, nand_378_out, nand_379_out, nand_380_out,
       nand_381_out, nand_382_out, nand_383_out, nand_384_out, nand_385_out, nand_386_out, nand_387_out,
       nand_388_out, nand_389_out, nand_390_out, nand_391_out, nand_392_out, nand_393_out, nand_394_out,
       nand_395_out, nand_396_out, nand_397_out, nand_398_out, nand_399_out, nand_400_out, nand_401_out,
       nand_402_out, nand_403_out, nand_404_out, nand_405_out, nand_406_out, nand_407_out, nand_408_out,
       nand_409_out, nand_410_out, nand_411_out, nand_412_out, nand_413_out, nand_414_out, nand_415_out,
       nand_416_out, nand_417_out, nand_418_out, nand_419_out, nand_420_out, nand_421_out, nand_422_out,
       nand_423_out, nand_424_out, nand_425_out, nand_426_out, nand_427_out, nand_428_out, nand_429_out,
       nand_430_out, nand_431_out, nand_432_out, nand_433_out, nand_434_out, nand_435_out, nand_436_out,
       nand_437_out, nand_438_out, nand_439_out, nand_440_out, nand_441_out, nand_442_out, nand_443_out,
       nand_444_out, nand_445_out, nand_446_out, nand_447_out, nand_448_out, nand_449_out, nand_450_out,
       nand_451_out, nand_452_out, nand_453_out, nand_454_out, nand_455_out, nand_456_out, nand_457_out,
       nand_458_out, nand_459_out, nand_460_out, nand_461_out, nand_462_out, nand_463_out, nand_464_out,
       nand_465_out, nand_466_out, nand_467_out, nand_468_out, nand_477_out, nand_478_out, nand_479_out,
       nand_480_out, nand_481_out, nand_482_out, nand_483_out, nand_484_out, nand_485_out, nand_486_out,
       nand_487_out, nand_488_out, nand_489_out, nand_490_out, nand_491_out, nand_492_out, nand_493_out,
       nand_494_out, nand_495_out, nand_496_out, nand_497_out, nand_498_out, nand_499_out, nand_500_out,
       nand_501_out, nand_502_out, nand_503_out, nand_504_out, nand_505_out, nand_506_out, nand_507_out,
       nand_508_out, nand_509_out, nand_510_out, nand_511_out, nand_512_out, nand_513_out, nand_514_out,
       nand_515_out, nand_516_out, nand_517_out, nand_518_out, nand_519_out, nand_520_out, nor_1_out,
       nor_2_out, xor_1_out, xor_2_out, xor_3_out, xor_4_out;

  nand nand_1 (nand_1_out, clk_3, clk_3);
  nand nand_2 (nand_2_out, clk_3, clk_3);
  nand nand_3 (nand_3_out, clk_3, clk_3);
  nand nand_4 (nand_4_out, clk_3, clk_3);
  nand nand_5 (nand_5_out, Dout3, nand_1_out);
  nand nand_6 (nand_6_out, nand_5_out, nand_1_out);
  nand nand_7 (nand_7_out, Dout2, nand_2_out);
  nand nand_8 (nand_8_out, nand_7_out, nand_2_out);
  nand nand_9 (nand_9_out, Dout1, nand_3_out);
  nand nand_10 (nand_10_out, nand_9_out, nand_3_out);
  nand nand_11 (nand_11_out, Dout0, nand_4_out);
  nand nand_12 (nand_12_out, nand_11_out, nand_4_out);
  nand nand_13 (nand_13_out, nand_5_out, nand_14_out);
  nand nand_14 (nand_14_out, nand_13_out, nand_6_out);
  nand nand_15 (nand_15_out, nand_7_out, nand_16_out);
  nand nand_16 (nand_16_out, nand_15_out, nand_8_out);
  nand nand_17 (nand_17_out, nand_9_out, nand_18_out);
  nand nand_18 (nand_18_out, nand_17_out, nand_10_out);
  nand nand_19 (nand_19_out, nand_11_out, nand_20_out);
  nand nand_20 (nand_20_out, nand_19_out, nand_12_out);
  LED u_Dout (.in(Dout3));
  LED u_A (.in(nand_13_out));
  LED u_B (.in(Din3));
  LED Dout_2 (.in(Dout2));
  LED u_A_2 (.in(nand_15_out));
  LED u_B_2 (.in(Din2));
  LED Dout_3 (.in(Dout1));
  LED u_A_3 (.in(nand_17_out));
  LED u_B_3 (.in(Din1));
  LED Dout_4 (.in(Dout0));
  LED u_A_4 (.in(nand_19_out));
  LED u_B_4 (.in(Din0));
  nand nand_21 (nand_21_out, D_3, nand_13_out);
  nand nand_22 (nand_22_out, C_2, nand_14_out);
  nand nand_23 (nand_23_out, B_8, nand_13_out);
  nand nand_24 (nand_24_out, A_10, nand_14_out);
  nand nand_25 (nand_25_out, D_3, nand_15_out);
  nand nand_26 (nand_26_out, C_2, nand_16_out);
  nand nand_27 (nand_27_out, B_8, nand_15_out);
  nand nand_28 (nand_28_out, A_10, nand_16_out);
  nand nand_29 (nand_29_out, D_3, nand_17_out);
  nand nand_30 (nand_30_out, C_2, nand_18_out);
  nand nand_31 (nand_31_out, B_8, nand_17_out);
  nand nand_32 (nand_32_out, A_10, nand_18_out);
  nand nand_33 (nand_33_out, D_3, nand_19_out);
  nand nand_34 (nand_34_out, C_2, nand_20_out);
  nand nand_35 (nand_35_out, B_8, nand_19_out);
  nand nand_36 (nand_36_out, A_10, nand_20_out);
  nand nand_37 (nand_37_out, nand_21_out, nand_22_out);
  nand nand_38 (nand_38_out, nand_23_out, nand_24_out);
  nand nand_39 (nand_39_out, Din3, Din3);
  nand nand_40 (nand_40_out, nand_25_out, nand_26_out);
  nand nand_41 (nand_41_out, nand_27_out, nand_28_out);
  nand nand_42 (nand_42_out, Din2, Din2);
  nand nand_43 (nand_43_out, nand_29_out, nand_30_out);
  nand nand_44 (nand_44_out, nand_31_out, nand_32_out);
  nand nand_45 (nand_45_out, Din1, Din1);
  nand nand_46 (nand_46_out, nand_33_out, nand_34_out);
  nand nand_47 (nand_47_out, nand_35_out, nand_36_out);
  nand nand_48 (nand_48_out, Din0, Din0);
  nand nand_49 (nand_49_out, Din3, nand_37_out);
  nand nand_50 (nand_50_out, nand_38_out, nand_39_out);
  nand nand_51 (nand_51_out, Din2, nand_40_out);
  nand nand_52 (nand_52_out, nand_41_out, nand_42_out);
  nand nand_53 (nand_53_out, Din1, nand_43_out);
  nand nand_54 (nand_54_out, nand_44_out, nand_45_out);
  nand nand_55 (nand_55_out, Din0, nand_46_out);
  nand nand_56 (nand_56_out, nand_47_out, nand_48_out);
  nand nand_57 (nand_57_out, nand_49_out, nand_50_out);
  nand nand_58 (nand_58_out, nand_51_out, nand_52_out);
  nand nand_59 (nand_59_out, nand_53_out, nand_54_out);
  nand nand_60 (nand_60_out, nand_55_out, nand_56_out);
  LED F (.in(nand_58_out));
  LED F_2 (.in(nand_59_out));
  LED F_3 (.in(nand_60_out));
  LED F_4 (.in(nand_57_out));
  nand nand_61 (nand_61_out, nand_57_out, EN_4);
  nand nand_62 (nand_62_out, nand_58_out, EN_4);
  nand nand_63 (nand_63_out, nand_59_out, EN_4);
  nand nand_64 (nand_64_out, nand_60_out, EN_4);
  nand nand_65 (nand_65_out, nand_61_out, nand_61_out);
  nand nand_66 (nand_66_out, nand_62_out, nand_62_out);
  nand nand_67 (nand_67_out, nand_63_out, nand_63_out);
  nand nand_68 (nand_68_out, nand_64_out, nand_64_out);
  nand nand_69 (nand_69_out, nand_65_out, Din3);
  nand nand_70 (nand_70_out, nand_66_out, Din2);
  nand nand_71 (nand_71_out, nand_67_out, Din1);
  nand nand_72 (nand_72_out, nand_68_out, Din0);
  nand nand_73 (nand_73_out, nand_65_out, nand_69_out);
  nand nand_74 (nand_74_out, nand_69_out, Din3);
  nand nand_75 (nand_75_out, nand_66_out, nand_70_out);
  nand nand_76 (nand_76_out, nand_70_out, Din2);
  nand nand_77 (nand_77_out, nand_67_out, nand_71_out);
  nand nand_78 (nand_78_out, nand_71_out, Din1);
  nand nand_79 (nand_79_out, nand_68_out, nand_72_out);
  nand nand_80 (nand_80_out, nand_72_out, Din0);
  nand nand_81 (nand_81_out, nand_73_out, nand_74_out);
  nand nand_82 (nand_82_out, nand_75_out, nand_76_out);
  nand nand_83 (nand_83_out, nand_77_out, nand_78_out);
  nand nand_84 (nand_84_out, nand_79_out, nand_80_out);
  nand nand_85 (nand_85_out, S0_4, S0_4);
  nand nand_86 (nand_86_out, S1_4, S1_4);
  nand nand_87 (nand_87_out, S2, S2);
  nand nand_88 (nand_88_out, nand_81_out, nand_97_out);
  nand nand_89 (nand_89_out, nand_82_out, nand_100_out);
  nand nand_90 (nand_90_out, nand_83_out, nand_103_out);
  nand nand_91 (nand_91_out, nand_84_out, Cin);
  nand nand_92 (nand_92_out, nand_81_out, nand_88_out);
  nand nand_93 (nand_93_out, nand_88_out, nand_97_out);
  nand nand_94 (nand_94_out, nand_88_out, nand_69_out);
  nand nand_95 (nand_95_out, nand_82_out, nand_89_out);
  nand nand_96 (nand_96_out, nand_89_out, nand_100_out);
  nand nand_97 (nand_97_out, nand_89_out, nand_70_out);
  nand nand_98 (nand_98_out, nand_83_out, nand_90_out);
  nand nand_99 (nand_99_out, nand_90_out, nand_103_out);
  nand nand_100 (nand_100_out, nand_90_out, nand_71_out);
  nand nand_101 (nand_101_out, nand_84_out, nand_91_out);
  nand nand_102 (nand_102_out, nand_91_out, Cin);
  nand nand_103 (nand_103_out, nand_91_out, nand_72_out);
  nand nand_104 (nand_104_out, nand_85_out, nand_86_out);
  nand nand_105 (nand_105_out, S0_4, nand_86_out);
  nand nand_106 (nand_106_out, nand_85_out, S1_4);
  nand nand_107 (nand_107_out, S0_4, S1_4);
  nand nand_108 (nand_108_out, nand_85_out, nand_86_out);
  nand nand_109 (nand_109_out, S0_4, nand_86_out);
  nand nand_110 (nand_110_out, nand_85_out, S1_4);
  nand nand_111 (nand_111_out, S0_4, S1_4);
  nand nand_112 (nand_112_out, nand_104_out, nand_104_out);
  nand nand_113 (nand_113_out, nand_105_out, nand_105_out);
  nand nand_114 (nand_114_out, nand_106_out, nand_106_out);
  nand nand_115 (nand_115_out, nand_107_out, nand_107_out);
  nand nand_116 (nand_116_out, nand_108_out, nand_108_out);
  nand nand_117 (nand_117_out, nand_109_out, nand_109_out);
  nand nand_118 (nand_118_out, nand_110_out, nand_110_out);
  nand nand_119 (nand_119_out, nand_111_out, nand_111_out);
  nand nand_120 (nand_120_out, nand_92_out, nand_93_out);
  nand nand_121 (nand_121_out, nand_95_out, nand_96_out);
  nand nand_122 (nand_122_out, nand_98_out, nand_99_out);
  nand nand_123 (nand_123_out, nand_101_out, nand_102_out);
  LED Cout (.in(nand_94_out));
  LED Cout_2 (.in(nand_97_out));
  LED Cout_3 (.in(nand_100_out));
  LED Cout_4 (.in(nand_103_out));
  nand nand_124 (nand_124_out, nand_112_out, nand_87_out);
  nand nand_125 (nand_125_out, nand_113_out, nand_87_out);
  nand nand_126 (nand_126_out, nand_114_out, nand_87_out);
  nand nand_127 (nand_127_out, nand_115_out, nand_87_out);
  nand nand_128 (nand_128_out, nand_116_out, S2);
  nand nand_129 (nand_129_out, nand_117_out, S2);
  nand nand_130 (nand_130_out, nand_118_out, S2);
  nand nand_131 (nand_131_out, nand_119_out, S2);
  nand nand_132 (nand_132_out, nand_120_out, clk_3);
  nand nand_133 (nand_133_out, nand_132_out, clk_3);
  nand nand_134 (nand_134_out, nand_121_out, clk_3);
  nand nand_135 (nand_135_out, nand_134_out, clk_3);
  nand nand_136 (nand_136_out, nand_122_out, clk_3);
  nand nand_137 (nand_137_out, nand_136_out, clk_3);
  nand nand_138 (nand_138_out, nand_123_out, clk_3);
  nand nand_139 (nand_139_out, nand_138_out, clk_3);
  LED led_1 (.in(nand_124_out));
  LED led_2 (.in(nand_125_out));
  LED led_3 (.in(nand_126_out));
  LED led_4 (.in(nand_127_out));
  LED led_5 (.in(nand_128_out));
  LED led_6 (.in(nand_129_out));
  LED led_7 (.in(nand_130_out));
  LED led_8 (.in(nand_131_out));
  nand nand_140 (Dout3, nand_132_out, nand_141_out);
  nand nand_141 (nand_141_out, Dout3, nand_133_out);
  nand nand_142 (Dout2, nand_134_out, nand_143_out);
  nand nand_143 (nand_143_out, Dout2, nand_135_out);
  nand nand_144 (Dout1, nand_136_out, nand_145_out);
  nand nand_145 (nand_145_out, Dout1, nand_137_out);
  nand nand_146 (Dout0, nand_138_out, nand_147_out);
  nand nand_147 (nand_147_out, Dout0, nand_139_out);
  Seven_Seg_Hex seven_seg_hex_1 (.d({Dout3, Dout2, Dout1, Dout0}), .dp(1'b0));
  nand nand_148 (nand_148_out, S0_2, S0_2);
  nand nand_149 (nand_149_out, S1_2, S1_2);
  nand nand_150 (nand_150_out, S0_3, S0_3);
  nand nand_151 (nand_151_out, S1_3, S1_3);
  nand nand_152 (nand_152_out, S0, S0);
  nand nand_153 (nand_153_out, E1, E0);
  nand nand_154 (nand_154_out, S1, S1);
  nand nand_155 (nand_155_out, D, S0_2);
  nand nand_156 (nand_156_out, C, nand_148_out);
  nand nand_157 (nand_157_out, B_2, S0_2);
  nand nand_158 (nand_158_out, A_2, nand_148_out);
  nand nand_159 (nand_159_out, D3, nand_153_out);
  nand nand_160 (nand_160_out, S1, S0);
  nand nand_161 (nand_161_out, D2, nand_153_out);
  nand nand_162 (nand_162_out, nand_152_out, S1);
  nand nand_163 (nand_163_out, D1, nand_153_out);
  nand nand_164 (nand_164_out, S0, nand_154_out);
  nand nand_165 (nand_165_out, D0, nand_153_out);
  nand nand_166 (nand_166_out, nand_152_out, nand_154_out);
  nand nand_167 (nand_167_out, nand_150_out, nand_151_out);
  nand nand_168 (nand_168_out, S0_3, nand_151_out);
  nand nand_169 (nand_169_out, nand_150_out, S1_3);
  nand nand_170 (nand_170_out, S0_3, S1_3);
  nand nand_171 (nand_171_out, nand_155_out, nand_156_out);
  nand nand_172 (nand_172_out, nand_157_out, nand_158_out);
  nand nand_173 (nand_173_out, nand_167_out, nand_167_out);
  nand nand_174 (nand_174_out, nand_168_out, nand_168_out);
  nand nand_175 (nand_175_out, nand_169_out, nand_169_out);
  nand nand_176 (nand_176_out, nand_170_out, nand_170_out);
  nand nand_177 (nand_177_out, nand_159_out, nand_159_out);
  nand nand_178 (nand_178_out, nand_160_out, nand_160_out);
  nand nand_179 (nand_179_out, nand_161_out, nand_161_out);
  nand nand_180 (nand_180_out, nand_162_out, nand_162_out);
  nand nand_181 (nand_181_out, nand_163_out, nand_163_out);
  nand nand_182 (nand_182_out, nand_164_out, nand_164_out);
  nand nand_183 (nand_183_out, nand_165_out, nand_165_out);
  nand nand_184 (nand_184_out, nand_166_out, nand_166_out);
  nand nand_185 (nand_185_out, S1_2, nand_171_out);
  nand nand_186 (nand_186_out, nand_172_out, nand_149_out);
  nand nand_187 (nand_187_out, nand_173_out, EN_3);
  nand nand_188 (nand_188_out, nand_174_out, EN_3);
  nand nand_189 (nand_189_out, nand_175_out, EN_3);
  nand nand_190 (nand_190_out, nand_176_out, EN_3);
  nand nand_191 (nand_191_out, Zin, Zin);
  nand nand_192 (nand_192_out, I0, I0);
  nand nand_193 (nand_193_out, I1, I1);
  nand nand_194 (nand_194_out, I2, I2);
  nand nand_195 (nand_195_out, I3, I3);
  nand nand_196 (nand_196_out, in_59, in_59);
  nand nand_197 (nand_197_out, in_60, in_60);
  nand nand_198 (nand_198_out, nand_185_out, nand_186_out);
  LED led_9 (.in(nand_187_out));
  LED led_10 (.in(nand_188_out));
  LED led_11 (.in(nand_189_out));
  LED led_12 (.in(nand_190_out));
  nand nand_199 (nand_199_out, nand_177_out, nand_178_out);
  nand nand_200 (nand_200_out, nand_179_out, nand_180_out);
  nand nand_201 (nand_201_out, nand_181_out, nand_182_out);
  nand nand_202 (nand_202_out, nand_183_out, nand_184_out);
  nand nand_203 (nand_203_out, nand_196_out, nand_197_out);
  nand nand_204 (nand_204_out, nand_198_out, EN);
  nand nand_205 (nand_205_out, nand_191_out, nand_192_out);
  nand nand_206 (nand_206_out, nand_203_out, nand_203_out);
  nand nand_207 (nand_207_out, in_61, in_61);
  nand nand_208 (nand_208_out, nand_199_out, nand_200_out);
  nand nand_209 (nand_209_out, nand_201_out, nand_202_out);
  nand nand_210 (nand_210_out, nand_204_out, nand_204_out);
  nand nand_211 (nand_211_out, nand_205_out, nand_205_out);
  nand nand_212 (nand_212_out, nand_211_out, nand_193_out);
  nand nand_213 (nand_213_out, nand_206_out, nand_207_out);
  nand nand_214 (nand_214_out, nand_208_out, nand_208_out);
  nand nand_215 (nand_215_out, nand_209_out, nand_209_out);
  LED led_13 (.in(nand_210_out));
  nand nand_216 (nand_216_out, nand_212_out, nand_212_out);
  nand nand_217 (nand_217_out, nand_213_out, nand_213_out);
  nand nand_218 (nand_218_out, in_62, in_62);
  nand nand_219 (nand_219_out, nand_214_out, nand_215_out);
  nand nand_220 (nand_220_out, nand_216_out, nand_194_out);
  nand nand_221 (nand_221_out, nand_217_out, nand_218_out);
  LED led_14 (.in(nand_219_out));
  nand nand_222 (nand_222_out, nand_220_out, nand_220_out);
  nand nand_223 (nand_223_out, nand_221_out, nand_221_out);
  nand nand_224 (nand_224_out, in_63, in_63);
  nand nand_225 (nand_225_out, nand_226_out, nand_226_out);
  nand nand_226 (nand_226_out, nand_227_out, out_137);
  nand nand_227 (nand_227_out, nand_228_out, nand_228_out);
  nand nand_228 (nand_228_out, nand_229_out, out_139);
  nand nand_229 (nand_229_out, nand_230_out, nand_230_out);
  nand nand_230 (nand_230_out, Carry_Out, out_141);
  nand nand_231 (Carry_Out, nand_232_out, nand_232_out);
  nand nand_232 (nand_232_out, C_in, Dout);
  nand nand_233 (nand_233_out, nand_222_out, nand_195_out);
  nand nand_234 (nand_234_out, nand_223_out, nand_224_out);
  nand nand_235 (nand_235_out, nand_227_out, nand_226_out);
  nand nand_236 (nand_236_out, nand_226_out, out_137);
  nand nand_237 (nand_237_out, nand_229_out, nand_228_out);
  nand nand_238 (nand_238_out, nand_228_out, out_139);
  nand nand_239 (nand_239_out, Carry_Out, nand_230_out);
  nand nand_240 (nand_240_out, nand_230_out, out_141);
  nand nand_241 (nand_241_out, C_in, nand_232_out);
  nand nand_242 (nand_242_out, nand_232_out, Dout);
  nand nand_243 (nand_243_out, CLK_2, CLK_2);
  LED Zout (.in(nand_233_out));
  nand nand_244 (nand_244_out, nand_234_out, nand_234_out);
  nand nand_245 (nand_245_out, in_64, in_64);
  nand nand_246 (nand_246_out, nand_235_out, nand_236_out);
  nand nand_247 (nand_247_out, nand_237_out, nand_238_out);
  nand nand_248 (nand_248_out, nand_239_out, nand_240_out);
  nand nand_249 (nand_249_out, nand_241_out, nand_242_out);
  nand nand_250 (nand_250_out, nand_244_out, nand_245_out);
  nand nand_251 (nand_251_out, nand_246_out, nand_243_out);
  nand nand_252 (nand_252_out, nand_251_out, nand_243_out);
  nand nand_253 (nand_253_out, nand_247_out, nand_243_out);
  nand nand_254 (nand_254_out, nand_253_out, nand_243_out);
  nand nand_255 (nand_255_out, nand_248_out, nand_243_out);
  nand nand_256 (nand_256_out, nand_255_out, nand_243_out);
  nand nand_257 (nand_257_out, nand_249_out, nand_243_out);
  nand nand_258 (nand_258_out, nand_257_out, nand_243_out);
  LED led_15 (.in(nand_250_out));
  nand nand_259 (nand_259_out, nand_251_out, nand_260_out);
  nand nand_260 (nand_260_out, nand_259_out, nand_252_out);
  nand nand_261 (nand_261_out, nand_253_out, nand_262_out);
  nand nand_262 (nand_262_out, nand_261_out, nand_254_out);
  nand nand_263 (nand_263_out, nand_255_out, nand_264_out);
  nand nand_264 (nand_264_out, nand_263_out, nand_256_out);
  nand nand_265 (nand_265_out, nand_257_out, nand_266_out);
  nand nand_266 (nand_266_out, nand_265_out, nand_258_out);
  nand nand_267 (nand_267_out, in_46, in_47);
  nand nand_268 (nand_268_out, in_48, in_49);
  nand nand_269 (nand_269_out, A_5, B_5);
  nand nand_270 (nand_270_out, in_35, in_36);
  nand nand_271 (nand_271_out, in_37, in_38);
  nand nand_272 (nand_272_out, in_21, in_22);
  nand nand_273 (nand_273_out, in_50, in_50);
  nand nand_274 (nand_274_out, in_23, in_24);
  nand nand_275 (nand_275_out, in_25, in_25);
  nand nand_276 (nand_276_out, in_26, in_26);
  nand nand_277 (nand_277_out, nand_267_out, nand_267_out);
  nand nand_278 (nand_278_out, nand_268_out, nand_268_out);
  nand nand_279 (nand_279_out, nand_269_out, EN_2);
  nand nand_280 (nand_280_out, nand_270_out, nand_270_out);
  nand nand_281 (nand_281_out, nand_271_out, nand_271_out);
  nand nand_282 (nand_282_out, nand_272_out, nand_273_out);
  nand nand_283 (nand_283_out, nand_273_out, nand_274_out);
  nand nand_284 (nand_284_out, DATAin3, Sel_Data);
  nand nand_285 (nand_285_out, nand_259_out, Sel_PC);
  nand nand_286 (nand_286_out, DATAin2, Sel_Data);
  nand nand_287 (nand_287_out, nand_261_out, Sel_PC);
  nand nand_288 (nand_288_out, DATAin1, Sel_Data);
  nand nand_289 (nand_289_out, nand_263_out, Sel_PC);
  nand nand_290 (nand_290_out, Din, Sel_Data);
  nand nand_291 (nand_291_out, nand_265_out, Sel_PC);
  nand nand_292 (nand_292_out, nand_275_out, nand_276_out);
  nand nand_293 (nand_293_out, nand_277_out, nand_278_out);
  LED led_16 (.in(nand_279_out));
  nand nand_294 (nand_294_out, nand_284_out, nand_285_out);
  nand nand_295 (nand_295_out, nand_286_out, nand_287_out);
  nand nand_296 (nand_296_out, nand_288_out, nand_289_out);
  nand nand_297 (nand_297_out, nand_290_out, nand_291_out);
  nand nand_298 (nand_298_out, nand_280_out, nand_281_out);
  nand nand_299 (nand_299_out, nand_282_out, nand_283_out);
  LED led_17 (.in(nand_292_out));
  LED led_18 (.in(nand_293_out));
  LED led_19 (.in(nand_298_out));
  LED led_20 (.in(nand_299_out));
  nand nand_300 (nand_300_out, nand_294_out, CLK_2);
  nand nand_301 (nand_301_out, nand_300_out, CLK_2);
  nand nand_302 (nand_302_out, nand_295_out, CLK_2);
  nand nand_303 (nand_303_out, nand_302_out, CLK_2);
  nand nand_304 (nand_304_out, nand_296_out, CLK_2);
  nand nand_305 (nand_305_out, nand_304_out, CLK_2);
  nand nand_306 (nand_306_out, nand_297_out, CLK_2);
  nand nand_307 (nand_307_out, nand_306_out, CLK_2);
  nand nand_308 (out_137, nand_300_out, nand_309_out);
  nand nand_309 (nand_309_out, out_137, nand_301_out);
  nand nand_310 (out_139, nand_302_out, nand_311_out);
  nand nand_311 (nand_311_out, out_139, nand_303_out);
  nand nand_312 (out_141, nand_304_out, nand_313_out);
  nand nand_313 (nand_313_out, out_141, nand_305_out);
  nand nand_314 (Dout, nand_306_out, nand_315_out);
  nand nand_315 (nand_315_out, Dout, nand_307_out);
  nand nand_316 (nand_316_out, in_126, in_127);
  nand nand_317 (nand_317_out, in_128, in_129);
  nand nand_318 (nand_318_out, in_131, in_132);
  nand nand_319 (nand_319_out, in_133, in_134);
  LED Q (.in(out_137));
  LED Q_2 (.in(out_139));
  LED Q_3 (.in(out_141));
  nand nand_320 (nand_320_out, in_53, in_53);
  nand nand_321 (nand_321_out, in_54, in_54);
  nand nand_322 (nand_322_out, in_51, in_51);
  nand nand_323 (nand_323_out, in_52, in_52);
  nand nand_324 (nand_324_out, A_3, A_3);
  nand nand_325 (nand_325_out, B_3, B_3);
  nand nand_326 (nand_326_out, A_4, B_4);
  nand nand_327 (nand_327_out, A_9, A_9);
  nand nand_328 (nand_328_out, B_7, B_7);
  nand nand_329 (nand_329_out, nand_316_out, nand_316_out);
  nand nand_330 (nand_330_out, nand_317_out, nand_317_out);
  nand nand_331 (nand_331_out, nand_318_out, nand_319_out);
  nor nor_1 (nor_1_out, in_1, in_3, in_5, in_7);
  xor xor_1 (xor_1_out, in_1, in_2);
  xor xor_2 (xor_2_out, in_3, in_4);
  xor xor_3 (xor_3_out, in_5, in_6);
  xor xor_4 (xor_4_out, in_7, in_8);
  nand nand_332 (nand_332_out, nand_320_out, nand_321_out);
  nand nand_333 (nand_333_out, nand_322_out, nand_323_out);
  nand nand_334 (out_112, nand_324_out, nand_325_out);
  nand nand_335 (out_113, nand_326_out, nand_326_out);
  nand nand_336 (nand_336_out, nand_327_out, nand_328_out);
  nand nand_337 (nand_337_out, nand_329_out, nand_329_out);
  nand nand_338 (nand_338_out, nand_330_out, nand_330_out);
  nand nand_339 (out_135, nand_331_out, nand_331_out);
  nand nand_340 (nand_340_out, nand_332_out, nand_332_out);
  nand nand_341 (nand_341_out, nand_333_out, nand_333_out);
  nand nand_342 (out_125, nand_336_out, nand_336_out);
  nand nand_343 (nand_343_out, nand_337_out, nand_338_out);
  nor nor_2 (nor_2_out, xor_1_out, xor_2_out, xor_3_out, xor_4_out);
  nand nand_344 (nand_344_out, nand_340_out, nand_341_out);
  nand nand_345 (out_130, nand_343_out, nand_343_out);
  LED led_21 (.in(nor_1_out));
  LED led_22 (.in(nor_2_out));
  LED led_23 (.in(nand_344_out));
  nand nand_346 (nand_346_out, A, B);
  nand nand_347 (nand_347_out, A_6, Invert_A_nA);
  nand nand_348 (nand_348_out, Select_A_nB, Select_A_nB);
  nand nand_349 (nand_349_out, A, nand_346_out);
  nand nand_350 (nand_350_out, nand_346_out, B);
  nand nand_351 (nand_351_out, A_6, nand_347_out);
  nand nand_352 (nand_352_out, nand_347_out, Invert_A_nA);
  nand nand_353 (nand_353_out, A_7, Select_A_nB);
  nand nand_354 (nand_354_out, nand_348_out, B_6);
  nand nand_355 (nand_355_out, in_17, in_17);
  nand nand_356 (nand_356_out, nand_398_out, nand_398_out);
  nand nand_357 (nand_357_out, DAT_2, DAT_2);
  nand nand_358 (nand_358_out, in_15, in_15);
  nand nand_359 (nand_359_out, nand_349_out, nand_350_out);
  nand nand_360 (nand_360_out, nand_351_out, nand_352_out);
  nand nand_361 (nand_361_out, nand_353_out, nand_354_out);
  nand nand_362 (nand_362_out, nand_401_out, DAT, in_13);
  nand nand_363 (nand_363_out, in_13, DAT, nand_400_out);
  nand nand_364 (nand_364_out, in_13, in_13);
  nand nand_365 (nand_365_out, DAT_2, in_15);
  nand nand_366 (nand_366_out, in_15, nand_357_out);
  nand nand_367 (nand_367_out, nand_398_out, nand_355_out);
  nand nand_368 (nand_368_out, nand_355_out, nand_356_out);
  LED led_24 (.in(nand_359_out));
  LED led_25 (.in(nand_360_out));
  LED led_26 (.in(nand_361_out));
  nand nand_369 (nand_369_out, nand_362_out, nand_370_out);
  nand nand_370 (nand_370_out, nand_369_out, nand_363_out);
  nand nand_371 (nand_371_out, nand_365_out, nand_372_out);
  nand nand_372 (nand_372_out, nand_371_out, nand_366_out);
  nand nand_373 (nand_373_out, nand_367_out, nand_374_out);
  nand nand_374 (nand_374_out, nand_373_out, nand_368_out);
  nand nand_375 (nand_375_out, in_77, nand_513_out);
  nand nand_376 (nand_376_out, nand_387_out, nand_515_out);
  nand nand_377 (nand_377_out, nand_390_out, nand_517_out);
  nand nand_378 (nand_378_out, nand_393_out, nand_519_out);
  nand nand_379 (nand_379_out, nand_369_out, nand_364_out);
  nand nand_380 (nand_380_out, nand_364_out, nand_370_out);
  nand nand_381 (nand_381_out, nand_371_out, nand_358_out);
  nand nand_382 (nand_382_out, nand_358_out, nand_372_out);
  nand nand_383 (nand_383_out, nand_373_out, in_17);
  nand nand_384 (nand_384_out, in_17, nand_374_out);
  nand nand_385 (nand_385_out, in_77, nand_375_out);
  nand nand_386 (nand_386_out, nand_375_out, nand_513_out);
  nand nand_387 (nand_387_out, nand_375_out, nand_375_out);
  nand nand_388 (nand_388_out, nand_387_out, nand_376_out);
  nand nand_389 (nand_389_out, nand_376_out, nand_515_out);
  nand nand_390 (nand_390_out, nand_376_out, nand_376_out);
  nand nand_391 (nand_391_out, nand_390_out, nand_377_out);
  nand nand_392 (nand_392_out, nand_377_out, nand_517_out);
  nand nand_393 (nand_393_out, nand_377_out, nand_377_out);
  nand nand_394 (nand_394_out, nand_393_out, nand_378_out);
  nand nand_395 (nand_395_out, nand_378_out, nand_519_out);
  nand nand_396 (nand_396_out, nand_378_out, nand_378_out);
  nand nand_397 (nand_397_out, nand_383_out, nand_398_out);
  nand nand_398 (nand_398_out, nand_397_out, nand_384_out);
  nand nand_399 (nand_399_out, in_120, in_120);
  nand nand_400 (nand_400_out, nand_379_out, nand_401_out);
  nand nand_401 (nand_401_out, nand_400_out, nand_380_out);
  nand nand_402 (nand_402_out, nand_381_out, nand_403_out);
  nand nand_403 (nand_403_out, nand_402_out, nand_382_out);
  nand nand_404 (nand_404_out, nand_385_out, nand_386_out);
  nand nand_405 (nand_405_out, nand_388_out, nand_389_out);
  nand nand_406 (nand_406_out, nand_391_out, nand_392_out);
  nand nand_407 (nand_407_out, nand_394_out, nand_395_out);
  nand nand_408 (nand_408_out, A_8, in_120);
  nand nand_409 (nand_409_out, nand_399_out, A_8);
  LED Q_4 (.in(nand_400_out));
  LED nQ (.in(nand_401_out));
  LED Q_5 (.in(nand_402_out));
  LED nQ_2 (.in(nand_403_out));
  LED Q_6 (.in(nand_397_out));
  LED nQ_3 (.in(nand_398_out));
  LED led_27 (.in(nand_408_out));
  LED led_28 (.in(nand_409_out));
  nand nand_410 (nand_410_out, D_2, LD);
  nand nand_411 (nand_411_out, nand_410_out, LD);
  nand nand_412 (nand_412_out, nLD_2, nLD_2);
  nand nand_413 (nand_413_out, nLD, nLD);
  nand nand_414 (nand_414_out, nLD, nLD);
  nand nand_415 (nand_415_out, nLD, nLD);
  nand nand_416 (nand_416_out, nLD, nLD);
  nand nand_417 (nand_417_out, nand_495_out, nLD_2);
  nand nand_418 (nand_418_out, nand_412_out, DATA);
  nand nand_419 (nand_419_out, nand_404_out, nLD);
  nand nand_420 (nand_420_out, nand_413_out, DATA_0);
  nand nand_421 (nand_421_out, nand_405_out, nLD);
  nand nand_422 (nand_422_out, nand_414_out, DATA_1);
  nand nand_423 (nand_423_out, nand_406_out, nLD);
  nand nand_424 (nand_424_out, nand_415_out, DATA_2);
  nand nand_425 (nand_425_out, nand_407_out, nLD);
  nand nand_426 (nand_426_out, nand_416_out, DATA_3);
  nand nand_427 (nand_427_out, nand_410_out, nand_428_out);
  nand nand_428 (nand_428_out, nand_427_out, nand_411_out);
  nand nand_429 (nand_429_out, nand_417_out, nand_418_out);
  nand nand_430 (nand_430_out, nand_419_out, nand_420_out);
  nand nand_431 (nand_431_out, RES, RES);
  nand nand_432 (nand_432_out, nand_421_out, nand_422_out);
  nand nand_433 (nand_433_out, nand_423_out, nand_424_out);
  nand nand_434 (nand_434_out, nand_425_out, nand_426_out);
  LED Q_7 (.in(nand_427_out));
  LED nQ_4 (.in(nand_428_out));
  nand nand_435 (nand_435_out, CK_2, CK_2);
  nand nand_436 (nand_436_out, nand_429_out, nand_429_out);
  nand nand_437 (nand_437_out, nand_430_out, nand_431_out);
  nand nand_438 (nand_438_out, nand_432_out, nand_431_out);
  nand nand_439 (nand_439_out, nand_433_out, nand_431_out);
  nand nand_440 (nand_440_out, nand_434_out, nand_431_out);
  nand nand_441 (nand_441_out, A_nB, A_nB);
  nand nand_442 (nand_442_out, A_nB, A_nB);
  nand nand_443 (nand_443_out, A_nB, A_nB);
  nand nand_444 (nand_444_out, A_nB, A_nB);
  nand nand_445 (nand_445_out, A_nB, A_nB);
  nand nand_446 (nand_446_out, A_nB, A_nB);
  nand nand_447 (nand_447_out, A_nB, A_nB);
  nand nand_448 (nand_448_out, A_nB, A_nB);
  nand nand_449 (nand_449_out, nand_429_out, nand_435_out);
  nand nand_450 (nand_450_out, nand_435_out, nand_436_out);
  nand nand_451 (nand_451_out, A0, A_nB);
  nand nand_452 (nand_452_out, nand_441_out, B0);
  nand nand_453 (nand_453_out, A1, A_nB);
  nand nand_454 (nand_454_out, nand_442_out, B1);
  nand nand_455 (nand_455_out, A2, A_nB);
  nand nand_456 (nand_456_out, nand_443_out, B2);
  nand nand_457 (nand_457_out, A3, A_nB);
  nand nand_458 (nand_458_out, nand_444_out, B3);
  nand nand_459 (nand_459_out, A4, A_nB);
  nand nand_460 (nand_460_out, nand_445_out, B4);
  nand nand_461 (nand_461_out, A5, A_nB);
  nand nand_462 (nand_462_out, nand_446_out, B5);
  nand nand_463 (nand_463_out, A6, A_nB);
  nand nand_464 (nand_464_out, nand_447_out, B6);
  nand nand_465 (nand_465_out, A7, A_nB);
  nand nand_466 (nand_466_out, nand_448_out, B7);
  nand nand_467 (nand_467_out, nand_449_out, nand_468_out);
  nand nand_468 (nand_468_out, nand_467_out, nand_450_out);
  nand nand_469 (out_104, nand_451_out, nand_452_out);
  nand nand_470 (out_105, nand_453_out, nand_454_out);
  nand nand_471 (out_106, nand_455_out, nand_456_out);
  nand nand_472 (out_107, nand_457_out, nand_458_out);
  nand nand_473 (out_108, nand_459_out, nand_460_out);
  nand nand_474 (out_109, nand_461_out, nand_462_out);
  nand nand_475 (out_110, nand_463_out, nand_464_out);
  nand nand_476 (out_111, nand_465_out, nand_466_out);
  nand nand_477 (nand_477_out, CK, CK);
  nand nand_478 (nand_478_out, nand_437_out, nand_437_out);
  nand nand_479 (nand_479_out, CK, CK);
  nand nand_480 (nand_480_out, nand_438_out, nand_438_out);
  nand nand_481 (nand_481_out, CK, CK);
  nand nand_482 (nand_482_out, nand_439_out, nand_439_out);
  nand nand_483 (nand_483_out, CK, CK);
  nand nand_484 (nand_484_out, nand_440_out, nand_440_out);
  nand nand_485 (nand_485_out, nand_467_out, CK_2);
  nand nand_486 (nand_486_out, CK_2, nand_468_out);
  nand nand_487 (nand_487_out, nand_437_out, nand_477_out);
  nand nand_488 (nand_488_out, nand_477_out, nand_478_out);
  nand nand_489 (nand_489_out, nand_438_out, nand_479_out);
  nand nand_490 (nand_490_out, nand_479_out, nand_480_out);
  nand nand_491 (nand_491_out, nand_439_out, nand_481_out);
  nand nand_492 (nand_492_out, nand_481_out, nand_482_out);
  nand nand_493 (nand_493_out, nand_440_out, nand_483_out);
  nand nand_494 (nand_494_out, nand_483_out, nand_484_out);
  nand nand_495 (nand_495_out, nand_485_out, nand_496_out);
  nand nand_496 (nand_496_out, nand_495_out, nand_486_out);
  nand nand_497 (nand_497_out, nand_487_out, nand_498_out);
  nand nand_498 (nand_498_out, nand_497_out, nand_488_out);
  nand nand_499 (nand_499_out, nand_489_out, nand_500_out);
  nand nand_500 (nand_500_out, nand_499_out, nand_490_out);
  nand nand_501 (nand_501_out, nand_491_out, nand_502_out);
  nand nand_502 (nand_502_out, nand_501_out, nand_492_out);
  nand nand_503 (nand_503_out, nand_493_out, nand_504_out);
  nand nand_504 (nand_504_out, nand_503_out, nand_494_out);
  LED Q_8 (.in(nand_495_out));
  LED nQ_5 (.in(nand_496_out));
  nand nand_505 (nand_505_out, nand_497_out, CK);
  nand nand_506 (nand_506_out, CK, nand_498_out);
  nand nand_507 (nand_507_out, nand_499_out, CK);
  nand nand_508 (nand_508_out, CK, nand_500_out);
  nand nand_509 (nand_509_out, nand_501_out, CK);
  nand nand_510 (nand_510_out, CK, nand_502_out);
  nand nand_511 (nand_511_out, nand_503_out, CK);
  nand nand_512 (nand_512_out, CK, nand_504_out);
  nand nand_513 (nand_513_out, nand_505_out, nand_514_out);
  nand nand_514 (nand_514_out, nand_513_out, nand_506_out);
  nand nand_515 (nand_515_out, nand_507_out, nand_516_out);
  nand nand_516 (nand_516_out, nand_515_out, nand_508_out);
  nand nand_517 (nand_517_out, nand_509_out, nand_518_out);
  nand nand_518 (nand_518_out, nand_517_out, nand_510_out);
  nand nand_519 (nand_519_out, nand_511_out, nand_520_out);
  nand nand_520 (nand_520_out, nand_519_out, nand_512_out);
  LED Q_9 (.in(nand_513_out));
  LED nQ_6 (.in(nand_514_out));
  LED Q_10 (.in(nand_515_out));
  LED nQ_7 (.in(nand_516_out));
  LED Q_11 (.in(nand_517_out));
  LED nQ_8 (.in(nand_518_out));
  LED Q_12 (.in(nand_519_out));
  LED nQ_9 (.in(nand_520_out));

  // Notes on the sheet:
  //   1 of 8 decoder ('138)
  //   2 to 4 line decoder with enable ('139)
  //   4:1 Multiplexer with Enable
  //   4:1 Multiplexer
  //   Multi-Input OR Chain - for zero detection
  //   Half Adder
  //   PC Latch
  //   PC
  //   2-Input AND with enable
  //   4 Input AND-OR
  //   2-Input OR
  //   4-Input Nand
  //   MUX
  //   ADDR Latch
  //   4-Input A-O-I Gate simplified
  //   4-bit Comparator A=B and Zero Detect A=0
  //   2-Input NOR
  //   4-Input A-O-I Gate
  //   2-Input AND
  //   4 Input OR
  //   4002
  //   A=0
  //   A=B
  //   XOR used as Invert Stage
  //   2 Input XOR
  //   2 Input Mux
  //   Master-Slave JK Flipflop
  //   D-Type Flipflop
  //   Toggle -Type Flipflop
  //   1 of 2 Decoder/Demux (Inverting)
  //   4-bit Program Counter Slice
  //   Gated D-Latch
  //   Register Stage in 14 Gates
endmodule
