// Digital circuit 4_bitslice_2.dig as structural Verilog
module _4_bitslice_2 (
  input  clk,
  input  A_nM,
  input  Mout0,
  input  Mout1,
  input  Mout2,
  input  Mout3,
  input  in_7,
  input  in_8,
  input  in_9,
  input  in_10,
  input  in_11,
  input  in_12,
  input  in_13,
  input  in_14,
  input  in_15,
  input  in_16,
  input  in_17,
  input  in_18,
  input  in_19,
  input  in_20
);

  wire _74157_1_pin4, _74157_1_pin7, _74157_1_pin9, _74157_1_pin12, _74173_1_pin3, _74173_1_pin4,
       _74173_1_pin5, _74173_1_pin6, _74173_1_pin13, _74173_2_pin11, _74173_2_pin12, _74173_2_pin13,
       _74173_2_pin14;
  wire [3:0] _74157_1_pin10, _74173_1_pin11;

  Seven_Seg_Hex seven_seg_hex_1 (.d(_74157_1_pin10), .dp(1'b0));
  _74157 _74157_1 (
    .pin1(A_nM), .pin2(Mout0), .pin3(_74157_1_pin10[0]), .pin4(_74157_1_pin4), .pin5(Mout1),
    .pin6(_74157_1_pin10[1]), .pin7(_74157_1_pin7), .pin8(1'b0), .pin9(_74157_1_pin9),
    .pin10(_74157_1_pin10[2]), .pin11(Mout2), .pin12(_74157_1_pin12), .pin13(_74157_1_pin10[3]),
    .pin14(Mout3), .pin15(in_13), .pin16(1'b1));
  _74173 _74173_1 (
    .pin1(in_9), .pin2(in_9), .pin3(_74173_1_pin3), .pin4(_74173_1_pin4), .pin5(_74173_1_pin5),
    .pin6(_74173_1_pin6), .pin7(clk), .pin8(1'b0), .pin9(in_11), .pin10(in_11), .pin11(_74173_1_pin11[3]),
    .pin12(_74173_1_pin11[2]), .pin13(_74173_1_pin13), .pin14(_74173_1_pin11[0]), .pin15(in_14), .pin16(1'b1));
  _74173 _74173_2 (
    .pin1(in_8), .pin2(in_8), .pin3(_74157_1_pin10[0]), .pin4(_74157_1_pin10[1]), .pin5(_74157_1_pin10[2]),
    .pin6(_74157_1_pin10[3]), .pin7(clk), .pin8(1'b0), .pin9(in_10), .pin10(in_10), .pin11(_74173_2_pin11),
    .pin12(_74173_2_pin12), .pin13(_74173_2_pin13), .pin14(_74173_2_pin14), .pin15(in_12), .pin16(1'b1));
  _74157 _74157_2 (
    .pin1(in_16), .pin2(_74173_1_pin11[0]), .pin3(in_17), .pin4(_74173_2_pin14), .pin5(_74173_1_pin13),
    .pin6(in_18), .pin7(_74173_2_pin13), .pin8(1'b0), .pin9(_74173_2_pin12), .pin10(in_19),
    .pin11(_74173_1_pin11[2]), .pin12(_74173_2_pin11), .pin13(in_20), .pin14(_74173_1_pin11[3]),
    .pin15(in_15), .pin16(1'b1));
  _74283 _74283_1 (
    .pin1(_74173_1_pin13), .pin2(_74157_1_pin7), .pin3(_74173_1_pin4), .pin4(_74173_1_pin11[0]),
    .pin5(_74173_1_pin3), .pin6(_74157_1_pin4), .pin7(in_7), .pin8(1'b0), .pin10(_74173_1_pin11[3]),
    .pin11(_74157_1_pin12), .pin12(_74173_1_pin6), .pin13(_74173_1_pin11[2]), .pin14(_74173_1_pin5),
    .pin15(_74157_1_pin9), .pin16(1'b1));  // open: pin9
  Seven_Seg_Hex seven_seg_hex_2 (.d({_74173_1_pin11[3:2], _74173_1_pin11[2], _74173_1_pin11[0]}), .dp(1'b0));

  // Notes on the sheet:
  //   ADDRESS
  //   A-REG
  //   ACC
  //   A-MUX
  //   ADD
  //   ALU OUT
endmodule
