// Digital circuit 8_bit_MCPU_ALU.dig as structural Verilog
module _8_bit_MCPU_ALU (
  input  C,
  input  D,
  input  A,
  input  B,
  input  Din0,
  input  EN,
  input  Cin,
  input  clk,
  input  Din1,
  input  Din2,
  input  Din3,
  input  Din4,
  input  Din5,
  input  Din6,
  input  Din7,
  input  DATAin3,
  input  DATAin2,
  input  DATAin1,
  input  DATAin0,
  input  C_in,
  input  Sel_Data,
  input  Sel_PC,
  input  CLK_2,
  input  DATAin7,
  input  DATAin6,
  input  DATAin5,
  input  DATAin4,
  output Dout0,
  output Dout1,
  output Dout2,
  output Dout3,
  output Dout4,
  output Dout5,
  output Dout6,
  output Dout7,
  output A3,
  output A2,
  output A1,
  output A0,
  output Carry_Out,
  output A7,
  output A6,
  output A5,
  output A4,
  output Carry_Out_2
);

  wire nand_1_out, nand_2_out, nand_3_out, nand_4_out, nand_5_out, nand_6_out, nand_7_out, nand_8_out,
       nand_9_out, nand_10_out, nand_11_out, nand_12_out, nand_13_out, nand_14_out, nand_15_out, nand_16_out,
       nand_17_out, nand_18_out, nand_19_out, nand_20_out, nand_21_out, nand_22_out, nand_23_out,
       nand_24_out, nand_25_out, nand_26_out, nand_27_out, nand_28_out, nand_29_out, nand_30_out,
       nand_31_out, nand_32_out, nand_33_out, nand_34_out, nand_35_out, nand_36_out, nand_37_out,
       nand_38_out, nand_39_out, nand_40_out, nand_41_out, nand_42_out, nand_43_out, nand_44_out,
       nand_45_out, nand_46_out, nand_47_out, nand_48_out, nand_49_out, nand_50_out, nand_51_out,
       nand_52_out, nand_53_out, nand_54_out, nand_55_out, nand_56_out, nand_57_out, nand_58_out,
       nand_59_out, nand_60_out, nand_61_out, nand_62_out, nand_63_out, nand_64_out, nand_65_out,
       nand_66_out, nand_67_out, nand_68_out, nand_69_out, nand_70_out, nand_71_out, nand_72_out,
       nand_73_out, nand_74_out, nand_75_out, nand_76_out, nand_77_out, nand_78_out, nand_79_out,
       nand_80_out, nand_81_out, nand_82_out, nand_83_out, nand_84_out, nand_85_out, nand_86_out,
       nand_87_out, nand_88_out, nand_89_out, nand_90_out, nand_91_out, nand_92_out, nand_93_out,
       nand_94_out, nand_95_out, nand_96_out, nand_97_out, nand_98_out, nand_99_out, nand_100_out,
       nand_101_out, nand_102_out, nand_103_out, nand_104_out, nand_105_out, nand_106_out, nand_107_out,
       nand_108_out, nand_109_out, nand_110_out, nand_111_out, nand_112_out, nand_113_out, nand_114_out,
       nand_115_out, nand_116_out, nand_117_out, nand_118_out, nand_119_out, nand_120_out, nand_121_out,
       nand_122_out, nand_123_out, nand_124_out, nand_125_out, nand_126_out, nand_127_out, nand_128_out,
       nand_129_out, nand_130_out, nand_131_out, nand_132_out, nand_133_out, nand_134_out, nand_135_out,
       nand_136_out, nand_137_out, nand_138_out, nand_139_out, nand_140_out, nand_141_out, nand_142_out,
       nand_143_out, nand_144_out, nand_145_out, nand_146_out, nand_147_out, nand_148_out, nand_149_out,
       nand_150_out, nand_151_out, nand_152_out, nand_153_out, nand_154_out, nand_155_out, nand_156_out,
       nand_157_out, nand_158_out, nand_159_out, nand_160_out, nand_161_out, nand_162_out, nand_163_out,
       nand_164_out, nand_165_out, nand_166_out, nand_167_out, nand_168_out, nand_169_out, nand_170_out,
       nand_171_out, nand_172_out, nand_173_out, nand_174_out, nand_175_out, nand_176_out, nand_177_out,
       nand_178_out, nand_179_out, nand_180_out, nand_181_out, nand_182_out, nand_183_out, nand_184_out,
       nand_185_out, nand_186_out, nand_187_out, nand_188_out, nand_189_out, nand_190_out, nand_191_out,
       nand_192_out, nand_193_out, nand_194_out, nand_195_out, nand_196_out, nand_197_out, nand_198_out,
       nand_199_out, nand_200_out, nand_201_out, nand_202_out, nand_203_out, nand_204_out, nand_205_out,
       nand_206_out, nand_207_out, nand_208_out, nand_209_out, nand_210_out, nand_211_out, nand_212_out,
       nand_213_out, nand_214_out, nand_215_out, nand_216_out, nand_217_out, nand_218_out, nand_219_out,
       nand_220_out, nand_221_out, nand_222_out, nand_223_out, nand_224_out, nand_226_out, nand_228_out,
       nand_230_out, nand_232_out, nand_234_out, nand_236_out, nand_238_out, nand_240_out, nand_241_out,
       nand_242_out, nand_243_out, nand_244_out, nand_245_out, nand_246_out, nand_248_out, nand_249_out,
       nand_250_out, nand_251_out, nand_252_out, nand_253_out, nand_254_out, nand_256_out, nand_257_out,
       nand_258_out, nand_259_out, nand_260_out, nand_261_out, nand_262_out, nand_263_out, nand_264_out,
       nand_265_out, nand_266_out, nand_267_out, nand_268_out, nand_269_out, nand_270_out, nand_271_out,
       nand_272_out, nand_273_out, nand_274_out, nand_275_out, nand_276_out, nand_277_out, nand_278_out,
       nand_279_out, nand_280_out, nand_281_out, nand_282_out, nand_283_out, nand_284_out, nand_285_out,
       nand_286_out, nand_287_out, nand_288_out, nand_289_out, nand_290_out, nand_291_out, nand_292_out,
       nand_293_out, nand_294_out, nand_295_out, nand_296_out, nand_297_out, nand_298_out, nand_299_out,
       nand_300_out, nand_301_out, nand_302_out, nand_303_out, nand_304_out, nand_305_out, nand_306_out,
       nand_307_out, nand_308_out, nand_309_out, nand_310_out, nand_311_out, nand_312_out, nand_313_out,
       nand_314_out, nand_315_out, nand_316_out, nand_317_out, nand_318_out, nand_319_out, nand_320_out,
       nand_321_out, nand_322_out, nand_323_out, nand_324_out, nand_325_out, nand_326_out, nand_327_out,
       nand_328_out, nand_329_out, nand_330_out, nand_331_out, nand_332_out, nand_333_out, nand_334_out,
       nand_335_out, nand_336_out, nand_337_out, nand_338_out, nand_339_out, nand_340_out, nand_341_out,
       nand_342_out, nand_343_out, nand_344_out, nand_345_out, nand_346_out, nand_347_out, nand_348_out,
       nand_349_out, nand_350_out, nand_351_out, nand_352_out, nand_353_out, nand_355_out, nand_357_out,
       nand_359_out, nand_361_out, nand_363_out, nand_365_out, nand_367_out, nand_369_out;

  nand nand_1 (nand_1_out, clk, clk);
  nand nand_2 (nand_2_out, clk, clk);
  nand nand_3 (nand_3_out, clk, clk);
  nand nand_4 (nand_4_out, clk, clk);
  nand nand_5 (nand_5_out, clk, clk);
  nand nand_6 (nand_6_out, clk, clk);
  nand nand_7 (nand_7_out, clk, clk);
  nand nand_8 (nand_8_out, clk, clk);
  nand nand_9 (nand_9_out, Dout7, nand_1_out);
  nand nand_10 (nand_10_out, nand_9_out, nand_1_out);
  nand nand_11 (nand_11_out, Dout6, nand_2_out);
  nand nand_12 (nand_12_out, nand_11_out, nand_2_out);
  nand nand_13 (nand_13_out, Dout5, nand_3_out);
  nand nand_14 (nand_14_out, nand_13_out, nand_3_out);
  nand nand_15 (nand_15_out, Dout4, nand_4_out);
  nand nand_16 (nand_16_out, nand_15_out, nand_4_out);
  nand nand_17 (nand_17_out, Dout3, nand_5_out);
  nand nand_18 (nand_18_out, nand_17_out, nand_5_out);
  nand nand_19 (nand_19_out, Dout2, nand_6_out);
  nand nand_20 (nand_20_out, nand_19_out, nand_6_out);
  nand nand_21 (nand_21_out, Dout1, nand_7_out);
  nand nand_22 (nand_22_out, nand_21_out, nand_7_out);
  nand nand_23 (nand_23_out, Dout0, nand_8_out);
  nand nand_24 (nand_24_out, nand_23_out, nand_8_out);
  nand nand_25 (nand_25_out, nand_9_out, nand_26_out);
  nand nand_26 (nand_26_out, nand_25_out, nand_10_out);
  nand nand_27 (nand_27_out, nand_11_out, nand_28_out);
  nand nand_28 (nand_28_out, nand_27_out, nand_12_out);
  nand nand_29 (nand_29_out, nand_13_out, nand_30_out);
  nand nand_30 (nand_30_out, nand_29_out, nand_14_out);
  nand nand_31 (nand_31_out, nand_15_out, nand_32_out);
  nand nand_32 (nand_32_out, nand_31_out, nand_16_out);
  nand nand_33 (nand_33_out, nand_17_out, nand_34_out);
  nand nand_34 (nand_34_out, nand_33_out, nand_18_out);
  nand nand_35 (nand_35_out, nand_19_out, nand_36_out);
  nand nand_36 (nand_36_out, nand_35_out, nand_20_out);
  nand nand_37 (nand_37_out, nand_21_out, nand_38_out);
  nand nand_38 (nand_38_out, nand_37_out, nand_22_out);
  nand nand_39 (nand_39_out, nand_23_out, nand_40_out);
  nand nand_40 (nand_40_out, nand_39_out, nand_24_out);
  LED Dout (.in(Dout7));
  LED u_A (.in(nand_25_out));
  LED u_B (.in(Din7));
  LED Dout_2 (.in(Dout6));
  LED A_2 (.in(nand_27_out));
  LED B_2 (.in(Din6));
  LED Dout_3 (.in(Dout5));
  LED A_3 (.in(nand_29_out));
  LED B_3 (.in(Din5));
  LED Dout_4 (.in(Dout4));
  LED A_4 (.in(nand_31_out));
  LED B_4 (.in(Din4));
  LED Dout_5 (.in(Dout3));
  LED A_5 (.in(nand_33_out));
  LED B_5 (.in(Din3));
  LED Dout_6 (.in(Dout2));
  LED A_6 (.in(nand_35_out));
  LED B_6 (.in(Din2));
  LED Dout_7 (.in(Dout1));
  LED A_7 (.in(nand_37_out));
  LED B_7 (.in(Din1));
  LED Dout_8 (.in(Dout0));
  LED A_8 (.in(nand_39_out));
  LED B_8 (.in(Din0));
  nand nand_41 (nand_41_out, D, nand_25_out);
  nand nand_42 (nand_42_out, C, nand_26_out);
  nand nand_43 (nand_43_out, B, nand_25_out);
  nand nand_44 (nand_44_out, A, nand_26_out);
  nand nand_45 (nand_45_out, D, nand_27_out);
  nand nand_46 (nand_46_out, C, nand_28_out);
  nand nand_47 (nand_47_out, B, nand_27_out);
  nand nand_48 (nand_48_out, A, nand_28_out);
  nand nand_49 (nand_49_out, D, nand_29_out);
  nand nand_50 (nand_50_out, C, nand_30_out);
  nand nand_51 (nand_51_out, B, nand_29_out);
  nand nand_52 (nand_52_out, A, nand_30_out);
  nand nand_53 (nand_53_out, D, nand_31_out);
  nand nand_54 (nand_54_out, C, nand_32_out);
  nand nand_55 (nand_55_out, B, nand_31_out);
  nand nand_56 (nand_56_out, A, nand_32_out);
  nand nand_57 (nand_57_out, D, nand_33_out);
  nand nand_58 (nand_58_out, C, nand_34_out);
  nand nand_59 (nand_59_out, B, nand_33_out);
  nand nand_60 (nand_60_out, A, nand_34_out);
  nand nand_61 (nand_61_out, D, nand_35_out);
  nand nand_62 (nand_62_out, C, nand_36_out);
  nand nand_63 (nand_63_out, B, nand_35_out);
  nand nand_64 (nand_64_out, A, nand_36_out);
  nand nand_65 (nand_65_out, D, nand_37_out);
  nand nand_66 (nand_66_out, C, nand_38_out);
  nand nand_67 (nand_67_out, B, nand_37_out);
  nand nand_68 (nand_68_out, A, nand_38_out);
  nand nand_69 (nand_69_out, D, nand_39_out);
  nand nand_70 (nand_70_out, C, nand_40_out);
  nand nand_71 (nand_71_out, B, nand_39_out);
  nand nand_72 (nand_72_out, A, nand_40_out);
  nand nand_73 (nand_73_out, nand_41_out, nand_42_out);
  nand nand_74 (nand_74_out, nand_43_out, nand_44_out);
  nand nand_75 (nand_75_out, Din7, Din7);
  nand nand_76 (nand_76_out, nand_45_out, nand_46_out);
  nand nand_77 (nand_77_out, nand_47_out, nand_48_out);
  nand nand_78 (nand_78_out, Din6, Din6);
  nand nand_79 (nand_79_out, nand_49_out, nand_50_out);
  nand nand_80 (nand_80_out, nand_51_out, nand_52_out);
  nand nand_81 (nand_81_out, Din5, Din5);
  nand nand_82 (nand_82_out, nand_53_out, nand_54_out);
  nand nand_83 (nand_83_out, nand_55_out, nand_56_out);
  nand nand_84 (nand_84_out, Din4, Din4);
  nand nand_85 (nand_85_out, nand_57_out, nand_58_out);
  nand nand_86 (nand_86_out, nand_59_out, nand_60_out);
  nand nand_87 (nand_87_out, Din3, Din3);
  nand nand_88 (nand_88_out, nand_61_out, nand_62_out);
  nand nand_89 (nand_89_out, nand_63_out, nand_64_out);
  nand nand_90 (nand_90_out, Din2, Din2);
  nand nand_91 (nand_91_out, nand_65_out, nand_66_out);
  nand nand_92 (nand_92_out, nand_67_out, nand_68_out);
  nand nand_93 (nand_93_out, Din1, Din1);
  nand nand_94 (nand_94_out, nand_69_out, nand_70_out);
  nand nand_95 (nand_95_out, nand_71_out, nand_72_out);
  nand nand_96 (nand_96_out, Din0, Din0);
  nand nand_97 (nand_97_out, Din7, nand_73_out);
  nand nand_98 (nand_98_out, nand_74_out, nand_75_out);
  nand nand_99 (nand_99_out, Din6, nand_76_out);
  nand nand_100 (nand_100_out, nand_77_out, nand_78_out);
  nand nand_101 (nand_101_out, Din5, nand_79_out);
  nand nand_102 (nand_102_out, nand_80_out, nand_81_out);
  nand nand_103 (nand_103_out, Din4, nand_82_out);
  nand nand_104 (nand_104_out, nand_83_out, nand_84_out);
  nand nand_105 (nand_105_out, Din3, nand_85_out);
  nand nand_106 (nand_106_out, nand_86_out, nand_87_out);
  nand nand_107 (nand_107_out, Din2, nand_88_out);
  nand nand_108 (nand_108_out, nand_89_out, nand_90_out);
  nand nand_109 (nand_109_out, Din1, nand_91_out);
  nand nand_110 (nand_110_out, nand_92_out, nand_93_out);
  nand nand_111 (nand_111_out, Din0, nand_94_out);
  nand nand_112 (nand_112_out, nand_95_out, nand_96_out);
  nand nand_113 (nand_113_out, nand_97_out, nand_98_out);
  nand nand_114 (nand_114_out, nand_99_out, nand_100_out);
  nand nand_115 (nand_115_out, nand_101_out, nand_102_out);
  nand nand_116 (nand_116_out, nand_103_out, nand_104_out);
  nand nand_117 (nand_117_out, nand_105_out, nand_106_out);
  nand nand_118 (nand_118_out, nand_107_out, nand_108_out);
  nand nand_119 (nand_119_out, nand_109_out, nand_110_out);
  nand nand_120 (nand_120_out, nand_111_out, nand_112_out);
  LED F (.in(nand_113_out));
  LED F_2 (.in(nand_114_out));
  LED F_3 (.in(nand_115_out));
  LED F_4 (.in(nand_116_out));
  LED F_5 (.in(nand_117_out));
  LED F_6 (.in(nand_118_out));
  LED F_7 (.in(nand_119_out));
  LED F_8 (.in(nand_120_out));
  nand nand_121 (nand_121_out, Din7, EN);
  nand nand_122 (nand_122_out, Din6, EN);
  nand nand_123 (nand_123_out, Din5, EN);
  nand nand_124 (nand_124_out, Din4, EN);
  nand nand_125 (nand_125_out, Din3, EN);
  nand nand_126 (nand_126_out, Din2, EN);
  nand nand_127 (nand_127_out, Din1, EN);
  nand nand_128 (nand_128_out, Din0, EN);
  nand nand_129 (nand_129_out, nand_121_out, nand_121_out);
  nand nand_130 (nand_130_out, nand_122_out, nand_122_out);
  nand nand_131 (nand_131_out, nand_123_out, nand_123_out);
  nand nand_132 (nand_132_out, nand_124_out, nand_124_out);
  nand nand_133 (nand_133_out, nand_125_out, nand_125_out);
  nand nand_134 (nand_134_out, nand_126_out, nand_126_out);
  nand nand_135 (nand_135_out, nand_127_out, nand_127_out);
  nand nand_136 (nand_136_out, nand_128_out, nand_128_out);
  nand nand_137 (nand_137_out, nand_113_out, nand_129_out);
  nand nand_138 (nand_138_out, nand_114_out, nand_130_out);
  nand nand_139 (nand_139_out, nand_115_out, nand_131_out);
  nand nand_140 (nand_140_out, nand_116_out, nand_132_out);
  nand nand_141 (nand_141_out, nand_117_out, nand_133_out);
  nand nand_142 (nand_142_out, nand_118_out, nand_134_out);
  nand nand_143 (nand_143_out, nand_119_out, nand_135_out);
  nand nand_144 (nand_144_out, nand_120_out, nand_136_out);
  nand nand_145 (nand_145_out, nand_113_out, nand_137_out);
  nand nand_146 (nand_146_out, nand_137_out, nand_129_out);
  nand nand_147 (nand_147_out, nand_114_out, nand_138_out);
  nand nand_148 (nand_148_out, nand_138_out, nand_130_out);
  nand nand_149 (nand_149_out, nand_115_out, nand_139_out);
  nand nand_150 (nand_150_out, nand_139_out, nand_131_out);
  nand nand_151 (nand_151_out, nand_116_out, nand_140_out);
  nand nand_152 (nand_152_out, nand_140_out, nand_132_out);
  nand nand_153 (nand_153_out, nand_117_out, nand_141_out);
  nand nand_154 (nand_154_out, nand_141_out, nand_133_out);
  nand nand_155 (nand_155_out, nand_118_out, nand_142_out);
  nand nand_156 (nand_156_out, nand_142_out, nand_134_out);
  nand nand_157 (nand_157_out, nand_119_out, nand_143_out);
  nand nand_158 (nand_158_out, nand_143_out, nand_135_out);
  nand nand_159 (nand_159_out, nand_120_out, nand_144_out);
  nand nand_160 (nand_160_out, nand_144_out, nand_136_out);
  nand nand_161 (nand_161_out, nand_145_out, nand_146_out);
  nand nand_162 (nand_162_out, nand_147_out, nand_148_out);
  nand nand_163 (nand_163_out, nand_149_out, nand_150_out);
  nand nand_164 (nand_164_out, nand_151_out, nand_152_out);
  nand nand_165 (nand_165_out, nand_153_out, nand_154_out);
  nand nand_166 (nand_166_out, nand_155_out, nand_156_out);
  nand nand_167 (nand_167_out, nand_157_out, nand_158_out);
  nand nand_168 (nand_168_out, nand_159_out, nand_160_out);
  nand nand_169 (nand_169_out, nand_161_out, nand_182_out);
  nand nand_170 (nand_170_out, nand_162_out, nand_185_out);
  nand nand_171 (nand_171_out, nand_163_out, nand_188_out);
  nand nand_172 (nand_172_out, nand_164_out, nand_191_out);
  nand nand_173 (nand_173_out, nand_165_out, nand_194_out);
  nand nand_174 (nand_174_out, nand_166_out, nand_197_out);
  nand nand_175 (nand_175_out, nand_167_out, nand_200_out);
  nand nand_176 (nand_176_out, nand_168_out, Cin);
  nand nand_177 (nand_177_out, nand_161_out, nand_169_out);
  nand nand_178 (nand_178_out, nand_169_out, nand_182_out);
  nand nand_179 (nand_179_out, nand_169_out, nand_137_out);
  nand nand_180 (nand_180_out, nand_162_out, nand_170_out);
  nand nand_181 (nand_181_out, nand_170_out, nand_185_out);
  nand nand_182 (nand_182_out, nand_170_out, nand_138_out);
  nand nand_183 (nand_183_out, nand_163_out, nand_171_out);
  nand nand_184 (nand_184_out, nand_171_out, nand_188_out);
  nand nand_185 (nand_185_out, nand_171_out, nand_139_out);
  nand nand_186 (nand_186_out, nand_164_out, nand_172_out);
  nand nand_187 (nand_187_out, nand_172_out, nand_191_out);
  nand nand_188 (nand_188_out, nand_172_out, nand_140_out);
  nand nand_189 (nand_189_out, nand_165_out, nand_173_out);
  nand nand_190 (nand_190_out, nand_173_out, nand_194_out);
  nand nand_191 (nand_191_out, nand_173_out, nand_141_out);
  nand nand_192 (nand_192_out, nand_166_out, nand_174_out);
  nand nand_193 (nand_193_out, nand_174_out, nand_197_out);
  nand nand_194 (nand_194_out, nand_174_out, nand_142_out);
  nand nand_195 (nand_195_out, nand_167_out, nand_175_out);
  nand nand_196 (nand_196_out, nand_175_out, nand_200_out);
  nand nand_197 (nand_197_out, nand_175_out, nand_143_out);
  nand nand_198 (nand_198_out, nand_168_out, nand_176_out);
  nand nand_199 (nand_199_out, nand_176_out, Cin);
  nand nand_200 (nand_200_out, nand_176_out, nand_144_out);
  nand nand_201 (nand_201_out, nand_177_out, nand_178_out);
  nand nand_202 (nand_202_out, nand_180_out, nand_181_out);
  nand nand_203 (nand_203_out, nand_183_out, nand_184_out);
  nand nand_204 (nand_204_out, nand_186_out, nand_187_out);
  nand nand_205 (nand_205_out, nand_189_out, nand_190_out);
  nand nand_206 (nand_206_out, nand_192_out, nand_193_out);
  nand nand_207 (nand_207_out, nand_195_out, nand_196_out);
  nand nand_208 (nand_208_out, nand_198_out, nand_199_out);
  LED Cout (.in(nand_179_out));
  LED Cout_2 (.in(nand_182_out));
  LED Cout_3 (.in(nand_185_out));
  LED Cout_4 (.in(nand_188_out));
  LED Cout_5 (.in(nand_191_out));
  LED Cout_6 (.in(nand_194_out));
  LED Cout_7 (.in(nand_197_out));
  LED Cout_8 (.in(nand_200_out));
  nand nand_209 (nand_209_out, nand_201_out, clk);
  nand nand_210 (nand_210_out, nand_209_out, clk);
  nand nand_211 (nand_211_out, nand_202_out, clk);
  nand nand_212 (nand_212_out, nand_211_out, clk);
  nand nand_213 (nand_213_out, nand_203_out, clk);
  nand nand_214 (nand_214_out, nand_213_out, clk);
  nand nand_215 (nand_215_out, nand_204_out, clk);
  nand nand_216 (nand_216_out, nand_215_out, clk);
  nand nand_217 (nand_217_out, nand_205_out, clk);
  nand nand_218 (nand_218_out, nand_217_out, clk);
  nand nand_219 (nand_219_out, nand_206_out, clk);
  nand nand_220 (nand_220_out, nand_219_out, clk);
  nand nand_221 (nand_221_out, nand_207_out, clk);
  nand nand_222 (nand_222_out, nand_221_out, clk);
  nand nand_223 (nand_223_out, nand_208_out, clk);
  nand nand_224 (nand_224_out, nand_223_out, clk);
  nand nand_225 (Dout7, nand_209_out, nand_226_out);
  nand nand_226 (nand_226_out, Dout7, nand_210_out);
  nand nand_227 (Dout6, nand_211_out, nand_228_out);
  nand nand_228 (nand_228_out, Dout6, nand_212_out);
  nand nand_229 (Dout5, nand_213_out, nand_230_out);
  nand nand_230 (nand_230_out, Dout5, nand_214_out);
  nand nand_231 (Dout4, nand_215_out, nand_232_out);
  nand nand_232 (nand_232_out, Dout4, nand_216_out);
  nand nand_233 (Dout3, nand_217_out, nand_234_out);
  nand nand_234 (nand_234_out, Dout3, nand_218_out);
  nand nand_235 (Dout2, nand_219_out, nand_236_out);
  nand nand_236 (nand_236_out, Dout2, nand_220_out);
  nand nand_237 (Dout1, nand_221_out, nand_238_out);
  nand nand_238 (nand_238_out, Dout1, nand_222_out);
  nand nand_239 (Dout0, nand_223_out, nand_240_out);
  nand nand_240 (nand_240_out, Dout0, nand_224_out);
  Seven_Seg_Hex seven_seg_hex_1 (.d({Dout7, Dout6, Dout5, Dout4}), .dp(1'b0));
  Seven_Seg_Hex seven_seg_hex_2 (.d({Dout3, Dout2, Dout1, Dout0}), .dp(1'b0));
  nand nand_241 (nand_241_out, nand_242_out, nand_242_out);
  nand nand_242 (nand_242_out, nand_243_out, A7);
  nand nand_243 (nand_243_out, nand_244_out, nand_244_out);
  nand nand_244 (nand_244_out, nand_245_out, A6);
  nand nand_245 (nand_245_out, nand_246_out, nand_246_out);
  nand nand_246 (nand_246_out, Carry_Out_2, A5);
  nand nand_247 (Carry_Out_2, nand_248_out, nand_248_out);
  nand nand_248 (nand_248_out, nand_249_out, A4);
  nand nand_249 (nand_249_out, nand_250_out, nand_250_out);
  nand nand_250 (nand_250_out, nand_251_out, A3);
  nand nand_251 (nand_251_out, nand_252_out, nand_252_out);
  nand nand_252 (nand_252_out, nand_253_out, A2);
  nand nand_253 (nand_253_out, nand_254_out, nand_254_out);
  nand nand_254 (nand_254_out, Carry_Out, A1);
  nand nand_255 (Carry_Out, nand_256_out, nand_256_out);
  nand nand_256 (nand_256_out, C_in, A0);
  nand nand_257 (nand_257_out, nand_243_out, nand_242_out);
  nand nand_258 (nand_258_out, nand_242_out, A7);
  nand nand_259 (nand_259_out, nand_245_out, nand_244_out);
  nand nand_260 (nand_260_out, nand_244_out, A6);
  nand nand_261 (nand_261_out, Carry_Out_2, nand_246_out);
  nand nand_262 (nand_262_out, nand_246_out, A5);
  nand nand_263 (nand_263_out, nand_249_out, nand_248_out);
  nand nand_264 (nand_264_out, nand_248_out, A4);
  nand nand_265 (nand_265_out, nand_251_out, nand_250_out);
  nand nand_266 (nand_266_out, nand_250_out, A3);
  nand nand_267 (nand_267_out, nand_253_out, nand_252_out);
  nand nand_268 (nand_268_out, nand_252_out, A2);
  nand nand_269 (nand_269_out, Carry_Out, nand_254_out);
  nand nand_270 (nand_270_out, nand_254_out, A1);
  nand nand_271 (nand_271_out, C_in, nand_256_out);
  nand nand_272 (nand_272_out, nand_256_out, A0);
  nand nand_273 (nand_273_out, CLK_2, CLK_2);
  nand nand_274 (nand_274_out, nand_257_out, nand_258_out);
  nand nand_275 (nand_275_out, nand_259_out, nand_260_out);
  nand nand_276 (nand_276_out, nand_261_out, nand_262_out);
  nand nand_277 (nand_277_out, nand_263_out, nand_264_out);
  nand nand_278 (nand_278_out, nand_265_out, nand_266_out);
  nand nand_279 (nand_279_out, nand_267_out, nand_268_out);
  nand nand_280 (nand_280_out, nand_269_out, nand_270_out);
  nand nand_281 (nand_281_out, nand_271_out, nand_272_out);
  nand nand_282 (nand_282_out, nand_274_out, nand_273_out);
  nand nand_283 (nand_283_out, nand_282_out, nand_273_out);
  nand nand_284 (nand_284_out, nand_275_out, nand_273_out);
  nand nand_285 (nand_285_out, nand_284_out, nand_273_out);
  nand nand_286 (nand_286_out, nand_276_out, nand_273_out);
  nand nand_287 (nand_287_out, nand_286_out, nand_273_out);
  nand nand_288 (nand_288_out, nand_277_out, nand_273_out);
  nand nand_289 (nand_289_out, nand_288_out, nand_273_out);
  nand nand_290 (nand_290_out, nand_278_out, nand_273_out);
  nand nand_291 (nand_291_out, nand_290_out, nand_273_out);
  nand nand_292 (nand_292_out, nand_279_out, nand_273_out);
  nand nand_293 (nand_293_out, nand_292_out, nand_273_out);
  nand nand_294 (nand_294_out, nand_280_out, nand_273_out);
  nand nand_295 (nand_295_out, nand_294_out, nand_273_out);
  nand nand_296 (nand_296_out, nand_281_out, nand_273_out);
  nand nand_297 (nand_297_out, nand_296_out, nand_273_out);
  nand nand_298 (nand_298_out, nand_282_out, nand_299_out);
  nand nand_299 (nand_299_out, nand_298_out, nand_283_out);
  nand nand_300 (nand_300_out, nand_284_out, nand_301_out);
  nand nand_301 (nand_301_out, nand_300_out, nand_285_out);
  nand nand_302 (nand_302_out, nand_286_out, nand_303_out);
  nand nand_303 (nand_303_out, nand_302_out, nand_287_out);
  nand nand_304 (nand_304_out, nand_288_out, nand_305_out);
  nand nand_305 (nand_305_out, nand_304_out, nand_289_out);
  nand nand_306 (nand_306_out, nand_290_out, nand_307_out);
  nand nand_307 (nand_307_out, nand_306_out, nand_291_out);
  nand nand_308 (nand_308_out, nand_292_out, nand_309_out);
  nand nand_309 (nand_309_out, nand_308_out, nand_293_out);
  nand nand_310 (nand_310_out, nand_294_out, nand_311_out);
  nand nand_311 (nand_311_out, nand_310_out, nand_295_out);
  nand nand_312 (nand_312_out, nand_296_out, nand_313_out);
  nand nand_313 (nand_313_out, nand_312_out, nand_297_out);
  nand nand_314 (nand_314_out, DATAin7, Sel_Data);
  nand nand_315 (nand_315_out, nand_298_out, Sel_PC);
  nand nand_316 (nand_316_out, DATAin6, Sel_Data);
  nand nand_317 (nand_317_out, nand_300_out, Sel_PC);
  nand nand_318 (nand_318_out, DATAin5, Sel_Data);
  nand nand_319 (nand_319_out, nand_302_out, Sel_PC);
  nand nand_320 (nand_320_out, DATAin4, Sel_Data);
  nand nand_321 (nand_321_out, nand_304_out, Sel_PC);
  nand nand_322 (nand_322_out, DATAin3, Sel_Data);
  nand nand_323 (nand_323_out, nand_306_out, Sel_PC);
  nand nand_324 (nand_324_out, DATAin2, Sel_Data);
  nand nand_325 (nand_325_out, nand_308_out, Sel_PC);
  nand nand_326 (nand_326_out, DATAin1, Sel_Data);
  nand nand_327 (nand_327_out, nand_310_out, Sel_PC);
  nand nand_328 (nand_328_out, DATAin0, Sel_Data);
  nand nand_329 (nand_329_out, nand_312_out, Sel_PC);
  nand nand_330 (nand_330_out, nand_314_out, nand_315_out);
  nand nand_331 (nand_331_out, nand_316_out, nand_317_out);
  nand nand_332 (nand_332_out, nand_318_out, nand_319_out);
  nand nand_333 (nand_333_out, nand_320_out, nand_321_out);
  nand nand_334 (nand_334_out, nand_322_out, nand_323_out);
  nand nand_335 (nand_335_out, nand_324_out, nand_325_out);
  nand nand_336 (nand_336_out, nand_326_out, nand_327_out);
  nand nand_337 (nand_337_out, nand_328_out, nand_329_out);
  nand nand_338 (nand_338_out, nand_330_out, CLK_2);
  nand nand_339 (nand_339_out, nand_338_out, CLK_2);
  nand nand_340 (nand_340_out, nand_331_out, CLK_2);
  nand nand_341 (nand_341_out, nand_340_out, CLK_2);
  nand nand_342 (nand_342_out, nand_332_out, CLK_2);
  nand nand_343 (nand_343_out, nand_342_out, CLK_2);
  nand nand_344 (nand_344_out, nand_333_out, CLK_2);
  nand nand_345 (nand_345_out, nand_344_out, CLK_2);
  nand nand_346 (nand_346_out, nand_334_out, CLK_2);
  nand nand_347 (nand_347_out, nand_346_out, CLK_2);
  nand nand_348 (nand_348_out, nand_335_out, CLK_2);
  nand nand_349 (nand_349_out, nand_348_out, CLK_2);
  nand nand_350 (nand_350_out, nand_336_out, CLK_2);
  nand nand_351 (nand_351_out, nand_350_out, CLK_2);
  nand nand_352 (nand_352_out, nand_337_out, CLK_2);
  nand nand_353 (nand_353_out, nand_352_out, CLK_2);
  nand nand_354 (A7, nand_338_out, nand_355_out);
  nand nand_355 (nand_355_out, A7, nand_339_out);
  nand nand_356 (A6, nand_340_out, nand_357_out);
  nand nand_357 (nand_357_out, A6, nand_341_out);
  nand nand_358 (A5, nand_342_out, nand_359_out);
  nand nand_359 (nand_359_out, A5, nand_343_out);
  nand nand_360 (A4, nand_344_out, nand_361_out);
  nand nand_361 (nand_361_out, A4, nand_345_out);
  nand nand_362 (A3, nand_346_out, nand_363_out);
  nand nand_363 (nand_363_out, A3, nand_347_out);
  nand nand_364 (A2, nand_348_out, nand_365_out);
  nand nand_365 (nand_365_out, A2, nand_349_out);
  nand nand_366 (A1, nand_350_out, nand_367_out);
  nand nand_367 (nand_367_out, A1, nand_351_out);
  nand nand_368 (A0, nand_352_out, nand_369_out);
  nand nand_369 (nand_369_out, A0, nand_353_out);

  // Notes on the sheet:
  //   clk: Hz: 4
  //   Half Adder
  //   PC Latch
  //   PC
  //   MUX
  //   ADDR Latch
endmodule
