// Digital circuit 8_bit_shift_reg.dig as structural Verilog
module _8_bit_shift_reg (
  input  Din,
  input  clk
);

  wire nand_3_out, nand_4_out, nand_5_out, nand_6_out, nand_7_out, nand_8_out, nand_9_out, nand_10_out,
       nand_11_out, nand_12_out, nand_13_out, nand_14_out, nand_15_out, nand_16_out, nand_17_out,
       nand_18_out, nand_19_out, nand_20_out, nand_21_out, nand_22_out, nand_23_out, nand_24_out,
       nand_25_out, nand_26_out, nand_27_out, nand_28_out, nand_29_out, nand_30_out, nand_31_out,
       nand_32_out, nand_33_out, nand_34_out, nand_35_out, nand_36_out, nand_37_out, nand_38_out,
       nand_39_out, nand_40_out, nand_41_out, nand_42_out, nand_43_out, nand_44_out, nand_45_out,
       nand_46_out, nand_47_out, nand_48_out, nand_49_out, nand_50_out, nand_51_out, nand_52_out,
       nand_53_out, nand_54_out, nand_55_out, nand_56_out, nand_57_out, nand_58_out, nand_59_out,
       nand_60_out, nand_61_out, nand_62_out, nand_63_out, nand_64_out, nand_65_out, nand_66_out, PH0, PH1;

  nand nand_1 (PH1, clk, clk);
  nand nand_2 (PH0, PH1, PH1);
  nand nand_3 (nand_3_out, nand_53_out, PH1);
  nand nand_4 (nand_4_out, nand_3_out, PH1);
  nand nand_5 (nand_5_out, nand_55_out, PH1);
  nand nand_6 (nand_6_out, nand_5_out, PH1);
  nand nand_7 (nand_7_out, nand_57_out, PH1);
  nand nand_8 (nand_8_out, nand_7_out, PH1);
  nand nand_9 (nand_9_out, nand_59_out, PH1);
  nand nand_10 (nand_10_out, nand_9_out, PH1);
  nand nand_11 (nand_11_out, nand_61_out, PH1);
  nand nand_12 (nand_12_out, nand_11_out, PH1);
  nand nand_13 (nand_13_out, nand_63_out, PH1);
  nand nand_14 (nand_14_out, nand_13_out, PH1);
  nand nand_15 (nand_15_out, nand_65_out, PH1);
  nand nand_16 (nand_16_out, nand_15_out, PH1);
  nand nand_17 (nand_17_out, Din, PH1);
  nand nand_18 (nand_18_out, nand_17_out, PH1);
  nand nand_19 (nand_19_out, nand_3_out, nand_20_out);
  nand nand_20 (nand_20_out, nand_19_out, nand_4_out);
  nand nand_21 (nand_21_out, nand_5_out, nand_22_out);
  nand nand_22 (nand_22_out, nand_21_out, nand_6_out);
  nand nand_23 (nand_23_out, nand_7_out, nand_24_out);
  nand nand_24 (nand_24_out, nand_23_out, nand_8_out);
  nand nand_25 (nand_25_out, nand_9_out, nand_26_out);
  nand nand_26 (nand_26_out, nand_25_out, nand_10_out);
  nand nand_27 (nand_27_out, nand_11_out, nand_28_out);
  nand nand_28 (nand_28_out, nand_27_out, nand_12_out);
  nand nand_29 (nand_29_out, nand_13_out, nand_30_out);
  nand nand_30 (nand_30_out, nand_29_out, nand_14_out);
  nand nand_31 (nand_31_out, nand_15_out, nand_32_out);
  nand nand_32 (nand_32_out, nand_31_out, nand_16_out);
  nand nand_33 (nand_33_out, nand_17_out, nand_34_out);
  nand nand_34 (nand_34_out, nand_33_out, nand_18_out);
  nand nand_35 (nand_35_out, nand_19_out, PH0);
  nand nand_36 (nand_36_out, nand_35_out, PH0);
  nand nand_37 (nand_37_out, nand_21_out, PH0);
  nand nand_38 (nand_38_out, nand_37_out, PH0);
  nand nand_39 (nand_39_out, nand_23_out, PH0);
  nand nand_40 (nand_40_out, nand_39_out, PH0);
  nand nand_41 (nand_41_out, nand_25_out, PH0);
  nand nand_42 (nand_42_out, nand_41_out, PH0);
  nand nand_43 (nand_43_out, nand_27_out, PH0);
  nand nand_44 (nand_44_out, nand_43_out, PH0);
  nand nand_45 (nand_45_out, nand_29_out, PH0);
  nand nand_46 (nand_46_out, nand_45_out, PH0);
  nand nand_47 (nand_47_out, nand_31_out, PH0);
  nand nand_48 (nand_48_out, nand_47_out, PH0);
  nand nand_49 (nand_49_out, nand_33_out, PH0);
  nand nand_50 (nand_50_out, nand_49_out, PH0);
  nand nand_51 (nand_51_out, nand_35_out, nand_52_out);
  nand nand_52 (nand_52_out, nand_51_out, nand_36_out);
  nand nand_53 (nand_53_out, nand_37_out, nand_54_out);
  nand nand_54 (nand_54_out, nand_53_out, nand_38_out);
  nand nand_55 (nand_55_out, nand_39_out, nand_56_out);
  nand nand_56 (nand_56_out, nand_55_out, nand_40_out);
  nand nand_57 (nand_57_out, nand_41_out, nand_58_out);
  nand nand_58 (nand_58_out, nand_57_out, nand_42_out);
  nand nand_59 (nand_59_out, nand_43_out, nand_60_out);
  nand nand_60 (nand_60_out, nand_59_out, nand_44_out);
  nand nand_61 (nand_61_out, nand_45_out, nand_62_out);
  nand nand_62 (nand_62_out, nand_61_out, nand_46_out);
  nand nand_63 (nand_63_out, nand_47_out, nand_64_out);
  nand nand_64 (nand_64_out, nand_63_out, nand_48_out);
  nand nand_65 (nand_65_out, nand_49_out, nand_66_out);
  nand nand_66 (nand_66_out, nand_65_out, nand_50_out);
  LED led_1 (.in(nand_51_out));
  LED led_2 (.in(nand_53_out));
  LED led_3 (.in(nand_55_out));
  LED led_4 (.in(nand_57_out));
  LED led_5 (.in(nand_59_out));
  LED led_6 (.in(nand_61_out));
  LED led_7 (.in(nand_63_out));
  LED led_8 (.in(nand_65_out));

  // Notes on the sheet:
  //   Master
  //   Slave
endmodule
