// Digital circuit ALU_8_W_Zero.dig as structural Verilog
module ALU_8_W_Zero (
  input  C,
  input  A0,
  input  D,
  input  A,
  input  B,
  input  B0,
  input  A1,
  input  B1,
  input  A2,
  input  B2,
  input  A3,
  input  B3,
  input  Cin,
  input  AL,
  input  A4,
  input  B4,
  input  A5,
  input  B5,
  input  A6,
  input  B6,
  input  A7,
  input  B7,
  input  VCC,
  input  GND2,
  input  GND,
  input  nZin,
  output C7,
  output F0,
  output F1,
  output F2,
  output F3,
  output F4,
  output F5,
  output F6,
  output F7,
  output nZout
);

  wire nand_1_out, nand_2_out, nand_3_out, nand_4_out, nand_5_out, nand_6_out, nand_7_out, nand_8_out,
       nand_9_out, nand_10_out, nand_11_out, nand_12_out, nand_13_out, nand_14_out, nand_15_out, nand_16_out,
       nand_17_out, nand_18_out, nand_19_out, nand_20_out, nand_21_out, nand_22_out, nand_23_out,
       nand_24_out, nand_25_out, nand_26_out, nand_27_out, nand_28_out, nand_29_out, nand_30_out,
       nand_31_out, nand_32_out, nand_33_out, nand_34_out, nand_35_out, nand_36_out, nand_37_out,
       nand_38_out, nand_39_out, nand_40_out, nand_41_out, nand_42_out, nand_43_out, nand_44_out,
       nand_45_out, nand_46_out, nand_47_out, nand_48_out, nand_49_out, nand_50_out, nand_51_out,
       nand_52_out, nand_53_out, nand_54_out, nand_55_out, nand_56_out, nand_57_out, nand_58_out,
       nand_59_out, nand_60_out, nand_61_out, nand_62_out, nand_63_out, nand_64_out, nand_65_out,
       nand_66_out, nand_67_out, nand_68_out, nand_69_out, nand_70_out, nand_71_out, nand_72_out,
       nand_73_out, nand_74_out, nand_75_out, nand_76_out, nand_77_out, nand_78_out, nand_79_out,
       nand_80_out, nand_81_out, nand_82_out, nand_83_out, nand_84_out, nand_85_out, nand_86_out,
       nand_87_out, nand_88_out, nand_89_out, nand_90_out, nand_91_out, nand_92_out, nand_93_out,
       nand_94_out, nand_95_out, nand_96_out, nand_97_out, nand_98_out, nand_99_out, nand_100_out,
       nand_101_out, nand_102_out, nand_103_out, nand_104_out, nand_105_out, nand_106_out, nand_107_out,
       nand_108_out, nand_109_out, nand_110_out, nand_111_out, nand_112_out, nand_113_out, nand_114_out,
       nand_115_out, nand_116_out, nand_117_out, nand_118_out, nand_119_out, nand_120_out, nand_121_out,
       nand_122_out, nand_123_out, nand_124_out, nand_125_out, nand_126_out, nand_127_out, nand_128_out,
       nand_129_out, nand_130_out, nand_131_out, nand_132_out, nand_133_out, nand_134_out, nand_135_out,
       nand_136_out, nand_137_out, nand_138_out, nand_139_out, nand_140_out, nand_141_out, nand_142_out,
       nand_143_out, nand_144_out, nand_145_out, nand_146_out, nand_147_out, nand_148_out, nand_149_out,
       nand_150_out, nand_151_out, nand_152_out, nand_153_out, nand_154_out, nand_155_out, nand_156_out,
       nand_157_out, nand_158_out, nand_159_out, nand_160_out, nand_161_out, nand_162_out, nand_163_out,
       nand_164_out, nand_165_out, nand_166_out, nand_167_out, nand_177_out, nand_178_out, nand_179_out,
       nand_180_out, nand_181_out, nand_182_out, nand_183_out, nand_184_out, nand_185_out, nand_186_out,
       nand_187_out, nand_188_out, nand_189_out, nand_190_out, nand_191_out, nand_192_out, nand_193_out,
       nand_194_out, nand_195_out, nand_196_out, nand_197_out, nand_198_out, nand_199_out;

  PowerSupply powersupply_1 (.VDD(VCC), .GND(GND));
  nand nand_1 (nand_1_out, A0, A0);
  nand nand_2 (nand_2_out, B0, B0);
  nand nand_3 (nand_3_out, A1, A1);
  nand nand_4 (nand_4_out, B1, B1);
  nand nand_5 (nand_5_out, A2, A2);
  nand nand_6 (nand_6_out, B2, B2);
  nand nand_7 (nand_7_out, A3, A3);
  nand nand_8 (nand_8_out, B3, B3);
  nand nand_9 (nand_9_out, A4, A4);
  nand nand_10 (nand_10_out, B4, B4);
  nand nand_11 (nand_11_out, A5, A5);
  nand nand_12 (nand_12_out, B5, B5);
  nand nand_13 (nand_13_out, A6, A6);
  nand nand_14 (nand_14_out, B6, B6);
  nand nand_15 (nand_15_out, A7, A7);
  nand nand_16 (nand_16_out, B7, B7);
  nand nand_17 (nand_17_out, D, A0);
  nand nand_18 (nand_18_out, C, nand_1_out);
  nand nand_19 (nand_19_out, B, A0);
  nand nand_20 (nand_20_out, A, nand_1_out);
  nand nand_21 (nand_21_out, D, A1);
  nand nand_22 (nand_22_out, C, nand_3_out);
  nand nand_23 (nand_23_out, B, A1);
  nand nand_24 (nand_24_out, A, nand_3_out);
  nand nand_25 (nand_25_out, D, A2);
  nand nand_26 (nand_26_out, C, nand_5_out);
  nand nand_27 (nand_27_out, B, A2);
  nand nand_28 (nand_28_out, A, nand_5_out);
  nand nand_29 (nand_29_out, D, A3);
  nand nand_30 (nand_30_out, C, nand_7_out);
  nand nand_31 (nand_31_out, B, A3);
  nand nand_32 (nand_32_out, A, nand_7_out);
  nand nand_33 (nand_33_out, D, A4);
  nand nand_34 (nand_34_out, C, nand_9_out);
  nand nand_35 (nand_35_out, B, A4);
  nand nand_36 (nand_36_out, A, nand_9_out);
  nand nand_37 (nand_37_out, D, A5);
  nand nand_38 (nand_38_out, C, nand_11_out);
  nand nand_39 (nand_39_out, B, A5);
  nand nand_40 (nand_40_out, A, nand_11_out);
  nand nand_41 (nand_41_out, D, A6);
  nand nand_42 (nand_42_out, C, nand_13_out);
  nand nand_43 (nand_43_out, B, A6);
  nand nand_44 (nand_44_out, A, nand_13_out);
  nand nand_45 (nand_45_out, D, A7);
  nand nand_46 (nand_46_out, C, nand_15_out);
  nand nand_47 (nand_47_out, B, A7);
  nand nand_48 (nand_48_out, A, nand_15_out);
  nand nand_49 (nand_49_out, nand_17_out, nand_18_out);
  nand nand_50 (nand_50_out, nand_19_out, nand_20_out);
  nand nand_51 (nand_51_out, nand_21_out, nand_22_out);
  nand nand_52 (nand_52_out, nand_23_out, nand_24_out);
  nand nand_53 (nand_53_out, nand_25_out, nand_26_out);
  nand nand_54 (nand_54_out, nand_27_out, nand_28_out);
  nand nand_55 (nand_55_out, nand_29_out, nand_30_out);
  nand nand_56 (nand_56_out, nand_31_out, nand_32_out);
  nand nand_57 (nand_57_out, nand_33_out, nand_34_out);
  nand nand_58 (nand_58_out, nand_35_out, nand_36_out);
  nand nand_59 (nand_59_out, nand_37_out, nand_38_out);
  nand nand_60 (nand_60_out, nand_39_out, nand_40_out);
  nand nand_61 (nand_61_out, nand_41_out, nand_42_out);
  nand nand_62 (nand_62_out, nand_43_out, nand_44_out);
  nand nand_63 (nand_63_out, nand_45_out, nand_46_out);
  nand nand_64 (nand_64_out, nand_47_out, nand_48_out);
  nand nand_65 (nand_65_out, B0, nand_49_out);
  nand nand_66 (nand_66_out, nand_50_out, nand_2_out);
  nand nand_67 (nand_67_out, B1, nand_51_out);
  nand nand_68 (nand_68_out, nand_52_out, nand_4_out);
  nand nand_69 (nand_69_out, B2, nand_53_out);
  nand nand_70 (nand_70_out, nand_54_out, nand_6_out);
  nand nand_71 (nand_71_out, B3, nand_55_out);
  nand nand_72 (nand_72_out, nand_56_out, nand_8_out);
  nand nand_73 (nand_73_out, B4, nand_57_out);
  nand nand_74 (nand_74_out, nand_58_out, nand_10_out);
  nand nand_75 (nand_75_out, B5, nand_59_out);
  nand nand_76 (nand_76_out, nand_60_out, nand_12_out);
  nand nand_77 (nand_77_out, B6, nand_61_out);
  nand nand_78 (nand_78_out, nand_62_out, nand_14_out);
  nand nand_79 (nand_79_out, B7, nand_63_out);
  nand nand_80 (nand_80_out, nand_64_out, nand_16_out);
  nand nand_81 (nand_81_out, A0, AL);
  nand nand_82 (nand_82_out, A1, AL);
  nand nand_83 (nand_83_out, A2, AL);
  nand nand_84 (nand_84_out, A3, AL);
  nand nand_85 (nand_85_out, A4, AL);
  nand nand_86 (nand_86_out, A5, AL);
  nand nand_87 (nand_87_out, A6, AL);
  nand nand_88 (nand_88_out, A7, AL);
  nand nand_89 (nand_89_out, nand_65_out, nand_66_out);
  nand nand_90 (nand_90_out, nand_81_out, nand_81_out);
  nand nand_91 (nand_91_out, nand_67_out, nand_68_out);
  nand nand_92 (nand_92_out, nand_82_out, nand_82_out);
  nand nand_93 (nand_93_out, nand_69_out, nand_70_out);
  nand nand_94 (nand_94_out, nand_83_out, nand_83_out);
  nand nand_95 (nand_95_out, nand_71_out, nand_72_out);
  nand nand_96 (nand_96_out, nand_84_out, nand_84_out);
  nand nand_97 (nand_97_out, nand_73_out, nand_74_out);
  nand nand_98 (nand_98_out, nand_85_out, nand_85_out);
  nand nand_99 (nand_99_out, nand_75_out, nand_76_out);
  nand nand_100 (nand_100_out, nand_86_out, nand_86_out);
  nand nand_101 (nand_101_out, nand_77_out, nand_78_out);
  nand nand_102 (nand_102_out, nand_87_out, nand_87_out);
  nand nand_103 (nand_103_out, nand_79_out, nand_80_out);
  nand nand_104 (nand_104_out, nand_88_out, nand_88_out);
  nand nand_105 (nand_105_out, nand_89_out, nand_90_out);
  nand nand_106 (nand_106_out, nand_91_out, nand_92_out);
  nand nand_107 (nand_107_out, nand_93_out, nand_94_out);
  nand nand_108 (nand_108_out, nand_95_out, nand_96_out);
  nand nand_109 (nand_109_out, nand_97_out, nand_98_out);
  nand nand_110 (nand_110_out, nand_99_out, nand_100_out);
  nand nand_111 (nand_111_out, nand_101_out, nand_102_out);
  nand nand_112 (nand_112_out, nand_103_out, nand_104_out);
  nand nand_113 (nand_113_out, nand_89_out, nand_105_out);
  nand nand_114 (nand_114_out, nand_105_out, nand_90_out);
  nand nand_115 (nand_115_out, nand_91_out, nand_106_out);
  nand nand_116 (nand_116_out, nand_106_out, nand_92_out);
  nand nand_117 (nand_117_out, nand_93_out, nand_107_out);
  nand nand_118 (nand_118_out, nand_107_out, nand_94_out);
  nand nand_119 (nand_119_out, nand_95_out, nand_108_out);
  nand nand_120 (nand_120_out, nand_108_out, nand_96_out);
  nand nand_121 (nand_121_out, nand_97_out, nand_109_out);
  nand nand_122 (nand_122_out, nand_109_out, nand_98_out);
  nand nand_123 (nand_123_out, nand_99_out, nand_110_out);
  nand nand_124 (nand_124_out, nand_110_out, nand_100_out);
  nand nand_125 (nand_125_out, nand_101_out, nand_111_out);
  nand nand_126 (nand_126_out, nand_111_out, nand_102_out);
  nand nand_127 (nand_127_out, nand_103_out, nand_112_out);
  nand nand_128 (nand_128_out, nand_112_out, nand_104_out);
  nand nand_129 (nand_129_out, nand_113_out, nand_114_out);
  nand nand_130 (nand_130_out, nand_115_out, nand_116_out);
  nand nand_131 (nand_131_out, nand_117_out, nand_118_out);
  nand nand_132 (nand_132_out, nand_119_out, nand_120_out);
  nand nand_133 (nand_133_out, nand_121_out, nand_122_out);
  nand nand_134 (nand_134_out, nand_123_out, nand_124_out);
  nand nand_135 (nand_135_out, nand_125_out, nand_126_out);
  nand nand_136 (nand_136_out, nand_127_out, nand_128_out);
  nand nand_137 (nand_137_out, nand_129_out, Cin);
  nand nand_138 (nand_138_out, nand_130_out, nand_147_out);
  nand nand_139 (nand_139_out, nand_131_out, nand_150_out);
  nand nand_140 (nand_140_out, nand_132_out, nand_153_out);
  nand nand_141 (nand_141_out, nand_133_out, nand_156_out);
  nand nand_142 (nand_142_out, nand_134_out, nand_159_out);
  nand nand_143 (nand_143_out, nand_135_out, nand_162_out);
  nand nand_144 (nand_144_out, nand_136_out, nand_165_out);
  nand nand_145 (nand_145_out, nand_129_out, nand_137_out);
  nand nand_146 (nand_146_out, nand_137_out, Cin);
  nand nand_147 (nand_147_out, nand_137_out, nand_105_out);
  nand nand_148 (nand_148_out, nand_130_out, nand_138_out);
  nand nand_149 (nand_149_out, nand_138_out, nand_147_out);
  nand nand_150 (nand_150_out, nand_138_out, nand_106_out);
  nand nand_151 (nand_151_out, nand_131_out, nand_139_out);
  nand nand_152 (nand_152_out, nand_139_out, nand_150_out);
  nand nand_153 (nand_153_out, nand_139_out, nand_107_out);
  nand nand_154 (nand_154_out, nand_132_out, nand_140_out);
  nand nand_155 (nand_155_out, nand_140_out, nand_153_out);
  nand nand_156 (nand_156_out, nand_140_out, nand_108_out);
  nand nand_157 (nand_157_out, nand_133_out, nand_141_out);
  nand nand_158 (nand_158_out, nand_141_out, nand_156_out);
  nand nand_159 (nand_159_out, nand_141_out, nand_109_out);
  nand nand_160 (nand_160_out, nand_134_out, nand_142_out);
  nand nand_161 (nand_161_out, nand_142_out, nand_159_out);
  nand nand_162 (nand_162_out, nand_142_out, nand_110_out);
  nand nand_163 (nand_163_out, nand_135_out, nand_143_out);
  nand nand_164 (nand_164_out, nand_143_out, nand_162_out);
  nand nand_165 (nand_165_out, nand_143_out, nand_111_out);
  nand nand_166 (nand_166_out, nand_136_out, nand_144_out);
  nand nand_167 (nand_167_out, nand_144_out, nand_165_out);
  nand nand_168 (C7, nand_144_out, nand_112_out);
  nand nand_169 (F0, nand_145_out, nand_146_out);
  nand nand_170 (F1, nand_148_out, nand_149_out);
  nand nand_171 (F2, nand_151_out, nand_152_out);
  nand nand_172 (F3, nand_154_out, nand_155_out);
  nand nand_173 (F4, nand_157_out, nand_158_out);
  nand nand_174 (F5, nand_160_out, nand_161_out);
  nand nand_175 (F6, nand_163_out, nand_164_out);
  nand nand_176 (F7, nand_166_out, nand_167_out);
  nand nand_177 (nand_177_out, nZin, nZin);
  nand nand_178 (nand_178_out, F0, F0);
  nand nand_179 (nand_179_out, nand_193_out, nand_193_out);
  nand nand_180 (nand_180_out, F1, F1);
  nand nand_181 (nand_181_out, nand_194_out, nand_194_out);
  nand nand_182 (nand_182_out, F2, F2);
  nand nand_183 (nand_183_out, nand_195_out, nand_195_out);
  nand nand_184 (nand_184_out, F3, F3);
  nand nand_185 (nand_185_out, nand_196_out, nand_196_out);
  nand nand_186 (nand_186_out, F4, F4);
  nand nand_187 (nand_187_out, nand_197_out, nand_197_out);
  nand nand_188 (nand_188_out, F5, F5);
  nand nand_189 (nand_189_out, nand_198_out, nand_198_out);
  nand nand_190 (nand_190_out, F6, F6);
  nand nand_191 (nand_191_out, nand_199_out, nand_199_out);
  nand nand_192 (nand_192_out, F7, F7);
  nand nand_193 (nand_193_out, nand_177_out, nand_178_out);
  nand nand_194 (nand_194_out, nand_179_out, nand_180_out);
  nand nand_195 (nand_195_out, nand_181_out, nand_182_out);
  nand nand_196 (nand_196_out, nand_183_out, nand_184_out);
  nand nand_197 (nand_197_out, nand_185_out, nand_186_out);
  nand nand_198 (nand_198_out, nand_187_out, nand_188_out);
  nand nand_199 (nand_199_out, nand_189_out, nand_190_out);
  nand nand_200 (nZout, nand_191_out, nand_192_out);

  assign GND2 = GND;

  // Notes on the sheet:
  //   C: pin 36
  //   A0: pin 3
  //   D: pin 37
  //   A: pin 34
  //   B: pin 35
  //   B0: pin 12
  //   A1: pin 4
  //   B1: pin 13
  //   A2: pin 5
  //   B2: pin 14
  //   A3: pin 6
  //   B3: pin 15
  //   Cin: pin 2
  //   AL: pin 38
  //   A4: pin 7
  //   B4: pin 16
  //   A5: pin 8
  //   B5: pin 17
  //   A6: pin 9
  //   B6: pin 18
  //   A7: pin 10
  //   B7: pin 19
  //   C7: pin 21
  //   VCC: pin 40
  //   GND2: pin 20
  //   GND: pin 11
  //   F0: pin 29
  //   F1: pin 28
  //   F2: pin 27
  //   F3: pin 26
  //   F4: pin 25
  //   F5: pin 24
  //   F6: pin 23
  //   F7: pin 22
  //   nZin: pin 1
  //   nZout: pin 39
  //   Carry
endmodule
