// Digital circuit ALU_Gates_Decoders_etc.dig as structural Verilog
module ALU_Gates_Decoders_etc (
  input  in_1,
  input  in_2,
  input  in_3,
  input  in_4,
  input  in_5,
  input  in_6,
  input  in_7,
  input  in_8,
  input  A,
  input  B,
  input  DAT,
  input  CLK,
  input  in_13,
  input  DAT_2,
  input  in_15,
  input  DAT_3,
  input  in_17,
  input  DATA_0,
  input  CK,
  input  nLD,
  input  in_21,
  input  in_22,
  input  in_23,
  input  in_24,
  input  in_25,
  input  in_26,
  input  D3,
  input  D2,
  input  D1,
  input  D0,
  input  S1,
  input  S0,
  input  E1,
  input  E0,
  input  in_35,
  input  in_36,
  input  in_37,
  input  in_38,
  input  C,
  input  S0_2,
  input  D,
  input  A_2,
  input  B_2,
  input  S1_2,
  input  EN,
  input  in_46,
  input  in_47,
  input  in_48,
  input  in_49,
  input  in_50,
  input  in_51,
  input  in_52,
  input  in_53,
  input  in_54,
  input  A_3,
  input  B_3,
  input  A_4,
  input  B_4,
  input  in_59,
  input  in_60,
  input  in_61,
  input  in_62,
  input  in_63,
  input  in_64,
  input  Zin,
  input  I0,
  input  I1,
  input  I2,
  input  I3,
  input  DATA_1,
  input  DATA_2,
  input  DATA_3,
  input  DATA,
  input  CK_2,
  input  nLD_2,
  input  RES,
  input  in_77,
  input  A_5,
  input  B_5,
  input  EN_2,
  input  S0_3,
  input  S1_3,
  input  EN_3,
  input  S0_4,
  input  S1_4,
  input  S2,
  input  B0,
  input  A_nB,
  input  A0,
  input  B1,
  input  A1,
  input  B2,
  input  A2,
  input  B3,
  input  A3,
  input  B4,
  input  A4,
  input  B5,
  input  A5,
  input  B6,
  input  A6,
  input  B7,
  input  A7,
  input  A_6,
  input  Invert_A_nA,
  input  B_6,
  input  Select_A_nB,
  input  A_7,
  input  A_8,
  input  in_120,
  input  D_2,
  input  LD,
  input  A_9,
  input  B_7,
  input  in_126,
  input  in_127,
  input  in_128,
  input  in_129,
  input  in_131,
  input  in_132,
  input  in_133,
  input  in_134,
  input  DATAin3,
  input  DATAin2,
  input  DATAin1,
  input  Din,
  input  C_in,
  input  Sel_Data,
  input  Sel_PC,
  input  CLK_2,
  input  C_2,
  input  D_3,
  input  A_10,
  input  B_8,
  input  Din0,
  input  EN_4,
  input  Cin,
  input  clk_3,
  input  Din1,
  input  Din2,
  input  Din3,
  input  B8,
  input  A_nB_2,
  input  A8,
  input  B9,
  input  A9,
  input  B10,
  input  A10,
  input  B11,
  input  A11,
  input  B12,
  input  A12,
  input  B13,
  input  A13,
  input  B14,
  input  A14,
  input  B15,
  input  A15,
  input  SEL_B,
  input  Bin,
  input  Ain,
  input  SEL_A,
  input  A_11,
  input  B_9,
  input  DATA_4,
  input  CLK_4,
  input  A_12,
  input  AL,
  input  B_10,
  input  nC,
  input  I7,
  input  I6,
  input  I5,
  input  I4,
  input  B_11,
  input  A_13,
  input  I5_2,
  input  A_14,
  input  B_12,
  input  C_3,
  input  in_220,
  input  I4_2,
  input  A_15,
  input  B_13,
  input  C_4,
  input  I5_3,
  input  I4_3,
  input  A_16,
  input  B_14,
  input  C_5,
  input  I5_4,
  input  I4_4,
  input  I7_2,
  input  I6_2,
  input  A_17,
  input  B_15,
  input  C_6,
  input  I5_5,
  input  I4_5,
  input  I7_3,
  input  I6_3,
  input  AL_2,
  input  A_18,
  input  B_16,
  input  C_7,
  input  I5_6,
  input  I4_6,
  input  AL_3,
  input  XOR,
  input  AND,
  input  A_19,
  input  B_17,
  input  C_8,
  input  I5_7,
  input  I4_7,
  input  AL_4,
  input  I6_4,
  output out_104,
  output out_105,
  output out_106,
  output out_107,
  output out_108,
  output out_109,
  output out_110,
  output out_111,
  output out_112,
  output out_113,
  output out_125,
  output out_130,
  output out_135,
  output out_137,
  output out_139,
  output out_141,
  output Dout,
  output Carry_Out,
  output Dout_2,
  output Dout_3,
  output Dout_4,
  output Dout_5,
  output out_181,
  output out_182,
  output out_183,
  output out_184,
  output out_185,
  output out_186,
  output out_187,
  output out_188,
  output Dout_6,
  output Sum,
  output Q,
  output nQ,
  output Carry,
  output out_206,
  output F,
  output Sum_2,
  output Carry_2,
  output Sum_3,
  output Carry_3,
  output Sum_4,
  output Carry_4,
  output Sum_5,
  output Carry_5,
  output Sum_6,
  output Carry_6,
  output Sum_7,
  output Carry_7
);

  wire nand_1_out, nand_2_out, nand_3_out, nand_4_out, nand_5_out, nand_6_out, nand_7_out, nand_8_out,
       nand_9_out, nand_10_out, nand_11_out, nand_12_out, nand_13_out, nand_14_out, nand_15_out, nand_16_out,
       nand_17_out, nand_18_out, nand_19_out, nand_20_out, nand_21_out, nand_22_out, nand_23_out,
       nand_24_out, nand_25_out, nand_26_out, nand_27_out, nand_28_out, nand_29_out, nand_30_out,
       nand_31_out, nand_32_out, nand_33_out, nand_34_out, nand_35_out, nand_36_out, nand_37_out,
       nand_38_out, nand_39_out, nand_40_out, nand_41_out, nand_42_out, nand_43_out, nand_44_out,
       nand_45_out, nand_46_out, nand_47_out, nand_48_out, nand_49_out, nand_50_out, nand_51_out,
       nand_52_out, nand_53_out, nand_54_out, nand_55_out, nand_56_out, nand_57_out, nand_58_out,
       nand_59_out, nand_60_out, nand_61_out, nand_62_out, nand_63_out, nand_64_out, nand_65_out,
       nand_66_out, nand_67_out, nand_68_out, nand_69_out, nand_70_out, nand_71_out, nand_72_out,
       nand_73_out, nand_74_out, nand_75_out, nand_76_out, nand_77_out, nand_78_out, nand_79_out,
       nand_80_out, nand_81_out, nand_82_out, nand_83_out, nand_84_out, nand_85_out, nand_86_out,
       nand_87_out, nand_88_out, nand_89_out, nand_90_out, nand_91_out, nand_92_out, nand_93_out,
       nand_94_out, nand_95_out, nand_96_out, nand_97_out, nand_98_out, nand_99_out, nand_100_out,
       nand_101_out, nand_102_out, nand_103_out, nand_104_out, nand_105_out, nand_106_out, nand_107_out,
       nand_108_out, nand_109_out, nand_110_out, nand_111_out, nand_112_out, nand_117_out, nand_118_out,
       nand_119_out, nand_121_out, nand_122_out, nand_123_out, nand_124_out, nand_128_out, nand_129_out,
       nand_130_out, nand_131_out, nand_132_out, nand_133_out, nand_134_out, nand_135_out, nand_136_out,
       nand_137_out, nand_138_out, nand_139_out, nand_140_out, nand_141_out, nand_142_out, nand_143_out,
       nand_144_out, nand_145_out, nand_146_out, nand_147_out, nand_148_out, nand_149_out, nand_150_out,
       nand_151_out, nand_152_out, nand_153_out, nand_154_out, nand_155_out, nand_156_out, nand_157_out,
       nand_158_out, nand_159_out, nand_160_out, nand_161_out, nand_162_out, nand_163_out, nand_164_out,
       nand_165_out, nand_166_out, nand_167_out, nand_168_out, nand_169_out, nand_170_out, nand_171_out,
       nand_172_out, nand_173_out, nand_174_out, nand_175_out, nand_176_out, nand_177_out, nand_178_out,
       nand_179_out, nand_180_out, nand_181_out, nand_182_out, nand_183_out, nand_184_out, nand_185_out,
       nand_186_out, nand_187_out, nand_188_out, nand_189_out, nand_190_out, nand_191_out, nand_192_out,
       nand_193_out, nand_194_out, nand_197_out, nand_198_out, nand_200_out, nand_201_out, nand_202_out,
       nand_203_out, nand_204_out, nand_205_out, nand_206_out, nand_207_out, nand_208_out, nand_212_out,
       nand_213_out, nand_215_out, nand_217_out, nand_219_out, nand_221_out, nand_223_out, nand_224_out,
       nand_225_out, nand_228_out, nand_229_out, nand_230_out, nand_231_out, nand_232_out, nand_233_out,
       nand_234_out, nand_235_out, nand_236_out, nand_237_out, nand_238_out, nand_239_out, nand_240_out,
       nand_241_out, nand_242_out, nand_243_out, nand_244_out, nand_246_out, nand_247_out, nand_248_out,
       nand_249_out, nand_250_out, nand_251_out, nand_252_out, nand_253_out, nand_254_out, nand_255_out,
       nand_256_out, nand_257_out, nand_258_out, nand_259_out, nand_260_out, nand_261_out, nand_262_out,
       nand_263_out, nand_264_out, nand_265_out, nand_266_out, nand_267_out, nand_268_out, nand_269_out,
       nand_270_out, nand_271_out, nand_272_out, nand_273_out, nand_274_out, nand_275_out, nand_276_out,
       nand_277_out, nand_278_out, nand_279_out, nand_280_out, nand_281_out, nand_282_out, nand_283_out,
       nand_284_out, nand_285_out, nand_286_out, nand_287_out, nand_288_out, nand_289_out, nand_290_out,
       nand_291_out, nand_292_out, nand_293_out, nand_294_out, nand_295_out, nand_296_out, nand_297_out,
       nand_298_out, nand_299_out, nand_300_out, nand_301_out, nand_302_out, nand_303_out, nand_304_out,
       nand_305_out, nand_306_out, nand_307_out, nand_308_out, nand_309_out, nand_310_out, nand_311_out,
       nand_312_out, nand_313_out, nand_314_out, nand_315_out, nand_316_out, nand_317_out, nand_318_out,
       nand_319_out, nand_320_out, nand_321_out, nand_322_out, nand_323_out, nand_324_out, nand_325_out,
       nand_326_out, nand_327_out, nand_328_out, nand_329_out, nand_330_out, nand_331_out, nand_332_out,
       nand_333_out, nand_334_out, nand_335_out, nand_336_out, nand_337_out, nand_338_out, nand_339_out,
       nand_340_out, nand_341_out, nand_342_out, nand_343_out, nand_344_out, nand_345_out, nand_346_out,
       nand_347_out, nand_348_out, nand_349_out, nand_350_out, nand_351_out, nand_352_out, nand_354_out,
       nand_356_out, nand_358_out, nand_360_out, nand_361_out, nand_362_out, nand_363_out, nand_364_out,
       nand_365_out, nand_366_out, nand_367_out, nand_368_out, nand_369_out, nand_370_out, nand_371_out,
       nand_372_out, nand_373_out, nand_374_out, nand_375_out, nand_376_out, nand_377_out, nand_378_out,
       nand_379_out, nand_380_out, nand_381_out, nand_382_out, nand_383_out, nand_384_out, nand_385_out,
       nand_386_out, nand_387_out, nand_388_out, nand_389_out, nand_390_out, nand_391_out, nand_392_out,
       nand_393_out, nand_394_out, nand_395_out, nand_396_out, nand_397_out, nand_398_out, nand_399_out,
       nand_400_out, nand_401_out, nand_402_out, nand_403_out, nand_404_out, nand_405_out, nand_406_out,
       nand_407_out, nand_408_out, nand_409_out, nand_410_out, nand_411_out, nand_412_out, nand_413_out,
       nand_414_out, nand_415_out, nand_416_out, nand_417_out, nand_418_out, nand_419_out, nand_420_out,
       nand_421_out, nand_422_out, nand_423_out, nand_424_out, nand_425_out, nand_426_out, nand_427_out,
       nand_428_out, nand_429_out, nand_430_out, nand_431_out, nand_432_out, nand_433_out, nand_434_out,
       nand_435_out, nand_436_out, nand_437_out, nand_438_out, nand_439_out, nand_440_out, nand_441_out,
       nand_442_out, nand_443_out, nand_444_out, nand_445_out, nand_446_out, nand_447_out, nand_448_out,
       nand_449_out, nand_450_out, nand_451_out, nand_452_out, nand_455_out, nand_456_out, nand_457_out,
       nand_459_out, nand_460_out, nand_461_out, nand_462_out, nand_463_out, nand_465_out, nand_466_out,
       nand_468_out, nand_469_out, nand_470_out, nand_471_out, nand_472_out, nand_473_out, nand_474_out,
       nand_475_out, nand_476_out, nand_477_out, nand_478_out, nand_479_out, nand_480_out, nand_481_out,
       nand_482_out, nand_483_out, nand_484_out, nand_485_out, nand_486_out, nand_487_out, nand_488_out,
       nand_489_out, nand_490_out, nand_491_out, nand_492_out, nand_493_out, nand_494_out, nand_495_out,
       nand_496_out, nand_497_out, nand_498_out, nand_499_out, nand_500_out, nand_501_out, nand_502_out,
       nand_503_out, nand_504_out, nand_505_out, nand_506_out, nand_507_out, nand_508_out, nand_509_out,
       nand_510_out, nand_511_out, nand_512_out, nand_513_out, nand_514_out, nand_515_out, nand_516_out,
       nand_517_out, nand_518_out, nand_519_out, nand_520_out, nand_521_out, nand_522_out, nand_523_out,
       nand_524_out, nand_525_out, nand_526_out, nand_527_out, nand_528_out, nand_529_out, nand_530_out,
       nand_531_out, nand_532_out, nand_533_out, nand_534_out, nand_535_out, nand_536_out, nand_537_out,
       nand_538_out, nand_539_out, nand_540_out, nand_541_out, nand_542_out, nand_543_out, nand_544_out,
       nand_545_out, nand_546_out, nand_547_out, nand_548_out, nand_549_out, nand_550_out, nand_551_out,
       nand_552_out, nand_553_out, nand_554_out, nand_555_out, nand_556_out, nand_557_out, nand_558_out,
       nand_559_out, nand_560_out, nand_561_out, nand_562_out, nand_563_out, nand_564_out, nand_565_out,
       nand_566_out, nand_567_out, nand_568_out, nand_569_out, nand_570_out, nand_571_out, nand_572_out,
       nand_573_out, nand_574_out, nand_575_out, nand_584_out, nand_585_out, nand_586_out, nand_587_out,
       nand_588_out, nand_589_out, nand_590_out, nand_591_out, nand_592_out, nand_593_out, nand_594_out,
       nand_595_out, nand_596_out, nand_597_out, nand_598_out, nand_599_out, nand_600_out, nand_601_out,
       nand_602_out, nand_603_out, nand_604_out, nand_605_out, nand_606_out, nand_607_out, nand_608_out,
       nand_609_out, nand_610_out, nand_611_out, nand_612_out, nand_613_out, nand_614_out, nand_615_out,
       nand_616_out, nand_617_out, nand_618_out, nand_619_out, nand_620_out, nand_622_out, nand_623_out,
       nand_624_out, nand_625_out, nand_626_out, nand_627_out, nand_628_out, nand_629_out, nand_630_out,
       nand_631_out, nand_632_out, nand_633_out, nand_634_out, nand_635_out, nand_636_out, nand_637_out,
       nand_638_out, nand_639_out, nand_640_out, nand_641_out, nand_642_out, nand_643_out, nand_644_out,
       nand_645_out, nand_646_out, nand_647_out, nand_648_out, nand_649_out, nand_650_out, nand_651_out,
       nand_652_out, nand_653_out, nand_654_out, nand_655_out, nand_656_out, nand_657_out, nor_1_out,
       nor_2_out, undriven, undriven_2, undriven_3, xor_1_out, xor_2_out, xor_3_out, xor_4_out;

  nand nand_1 (nand_1_out, A_18, B_16);
  nand nand_2 (nand_2_out, A_16, B_14);
  nand nand_3 (nand_3_out, A_17, B_15);
  nand nand_4 (nand_4_out, A_19, B_17);
  nand nand_5 (nand_5_out, clk_3, clk_3);
  nand nand_6 (nand_6_out, clk_3, clk_3);
  nand nand_7 (nand_7_out, clk_3, clk_3);
  nand nand_8 (nand_8_out, clk_3, clk_3);
  nand nand_9 (nand_9_out, A_18, nand_1_out);
  nand nand_10 (nand_10_out, nand_1_out, B_16);
  nand nand_11 (nand_11_out, A_16, nand_2_out);
  nand nand_12 (nand_12_out, nand_2_out, B_14);
  nand nand_13 (nand_13_out, A_17, nand_3_out);
  nand nand_14 (nand_14_out, nand_3_out, B_15);
  nand nand_15 (nand_15_out, A_19, nand_4_out);
  nand nand_16 (nand_16_out, nand_4_out, B_17);
  nand nand_17 (nand_17_out, nand_9_out, nand_10_out);
  nand nand_18 (nand_18_out, nand_11_out, nand_12_out);
  nand nand_19 (nand_19_out, nand_13_out, nand_14_out);
  nand nand_20 (nand_20_out, nand_15_out, nand_16_out);
  nand nand_21 (nand_21_out, Dout_5, nand_5_out);
  nand nand_22 (nand_22_out, nand_21_out, nand_5_out);
  nand nand_23 (nand_23_out, Dout_4, nand_6_out);
  nand nand_24 (nand_24_out, nand_23_out, nand_6_out);
  nand nand_25 (nand_25_out, Dout_3, nand_7_out);
  nand nand_26 (nand_26_out, nand_25_out, nand_7_out);
  nand nand_27 (nand_27_out, Dout_2, nand_8_out);
  nand nand_28 (nand_28_out, nand_27_out, nand_8_out);
  nand nand_29 (nand_29_out, I5_6, nand_17_out);
  nand nand_30 (nand_30_out, B_16, I4_6);
  nand nand_31 (nand_31_out, I5_4, nand_18_out);
  nand nand_32 (nand_32_out, B_14, I4_4);
  nand nand_33 (nand_33_out, I5_5, nand_19_out);
  nand nand_34 (nand_34_out, B_15, I4_5);
  nand nand_35 (nand_35_out, I5_7, nand_20_out);
  nand nand_36 (nand_36_out, B_17, I4_7);
  nand nand_37 (nand_37_out, nand_21_out, nand_38_out);
  nand nand_38 (nand_38_out, nand_37_out, nand_22_out);
  nand nand_39 (nand_39_out, nand_23_out, nand_40_out);
  nand nand_40 (nand_40_out, nand_39_out, nand_24_out);
  nand nand_41 (nand_41_out, nand_25_out, nand_42_out);
  nand nand_42 (nand_42_out, nand_41_out, nand_26_out);
  nand nand_43 (nand_43_out, nand_27_out, nand_44_out);
  nand nand_44 (nand_44_out, nand_43_out, nand_28_out);
  nand nand_45 (nand_45_out, nand_29_out, nand_30_out);
  nand nand_46 (nand_46_out, nand_31_out, nand_32_out);
  nand nand_47 (nand_47_out, nand_33_out, nand_34_out);
  nand nand_48 (nand_48_out, nand_35_out, nand_36_out);
  nand nand_49 (nand_49_out, I6_4, I6_4);
  LED u_Dout (.in(Dout_5));
  LED u_A (.in(nand_37_out));
  LED u_B (.in(undriven));
  LED u_Dout_2 (.in(Dout_4));
  LED u_A_2 (.in(nand_39_out));
  LED u_B_2 (.in(undriven_2));
  LED u_Dout_3 (.in(Dout_3));
  LED u_A_3 (.in(nand_41_out));
  LED u_B_3 (.in(undriven_3));
  LED u_Dout_4 (.in(Dout_2));
  LED u_A_4 (.in(nand_43_out));
  LED u_B_4 (.in(Din0));
  nand nand_50 (nand_50_out, nand_45_out, C_7);
  nand nand_51 (nand_51_out, nand_46_out, C_5);
  nand nand_52 (nand_52_out, nand_47_out, C_6);
  nand nand_53 (nand_53_out, nand_48_out, C_8);
  nand nand_54 (nand_54_out, nand_2_out, nand_51_out);
  nand nand_55 (nand_55_out, nand_46_out, nand_51_out);
  nand nand_56 (nand_56_out, nand_51_out, C_5);
  nand nand_57 (nand_57_out, nand_3_out, nand_52_out);
  nand nand_58 (nand_58_out, nand_47_out, nand_52_out);
  nand nand_59 (nand_59_out, nand_52_out, C_6);
  nand nand_60 (nand_60_out, nand_1_out, nand_50_out);
  nand nand_61 (nand_61_out, nand_45_out, nand_50_out);
  nand nand_62 (nand_62_out, nand_50_out, C_7);
  nand nand_63 (nand_63_out, nand_4_out, nand_53_out);
  nand nand_64 (nand_64_out, nand_48_out, nand_53_out);
  nand nand_65 (nand_65_out, nand_53_out, C_8);
  nand nand_66 (nand_66_out, D_3, nand_37_out);
  nand nand_67 (nand_67_out, C_2, nand_38_out);
  nand nand_68 (nand_68_out, B_8, nand_37_out);
  nand nand_69 (nand_69_out, A_10, nand_38_out);
  nand nand_70 (nand_70_out, D_3, nand_39_out);
  nand nand_71 (nand_71_out, C_2, nand_40_out);
  nand nand_72 (nand_72_out, B_8, nand_39_out);
  nand nand_73 (nand_73_out, A_10, nand_40_out);
  nand nand_74 (nand_74_out, D_3, nand_41_out);
  nand nand_75 (nand_75_out, C_2, nand_42_out);
  nand nand_76 (nand_76_out, B_8, nand_41_out);
  nand nand_77 (nand_77_out, A_10, nand_42_out);
  nand nand_78 (nand_78_out, D_3, nand_43_out);
  nand nand_79 (nand_79_out, C_2, nand_44_out);
  nand nand_80 (nand_80_out, B_8, nand_43_out);
  nand nand_81 (nand_81_out, A_10, nand_44_out);
  LED led_1 (.in(nand_54_out));
  nand nand_82 (nand_82_out, nand_55_out, nand_56_out);
  nand nand_83 (nand_83_out, nand_58_out, nand_59_out);
  nand nand_84 (nand_84_out, nand_61_out, nand_62_out);
  nand nand_85 (nand_85_out, nand_54_out, I7_2);
  nand nand_86 (nand_86_out, nand_64_out, nand_65_out);
  nand nand_87 (nand_87_out, nand_66_out, nand_67_out);
  nand nand_88 (nand_88_out, nand_68_out, nand_69_out);
  nand nand_89 (nand_89_out, Din3, Din3);
  nand nand_90 (nand_90_out, nand_70_out, nand_71_out);
  nand nand_91 (nand_91_out, nand_72_out, nand_73_out);
  nand nand_92 (nand_92_out, Din2, Din2);
  nand nand_93 (nand_93_out, nand_74_out, nand_75_out);
  nand nand_94 (nand_94_out, nand_76_out, nand_77_out);
  nand nand_95 (nand_95_out, Din1, Din1);
  nand nand_96 (nand_96_out, nand_78_out, nand_79_out);
  nand nand_97 (nand_97_out, nand_80_out, nand_81_out);
  nand nand_98 (nand_98_out, Din0, Din0);
  nand nand_99 (nand_99_out, nand_82_out, I6_2);
  nand nand_100 (nand_100_out, nand_57_out, I7_3);
  nand nand_101 (nand_101_out, nand_83_out, I6_3);
  nand nand_102 (nand_102_out, Din3, nand_87_out);
  nand nand_103 (nand_103_out, nand_88_out, nand_89_out);
  nand nand_104 (nand_104_out, Din2, nand_90_out);
  nand nand_105 (nand_105_out, nand_91_out, nand_92_out);
  nand nand_106 (nand_106_out, Din1, nand_93_out);
  nand nand_107 (nand_107_out, nand_94_out, nand_95_out);
  nand nand_108 (nand_108_out, Din0, nand_96_out);
  nand nand_109 (nand_109_out, nand_97_out, nand_98_out);
  nand nand_110 (nand_110_out, nand_60_out, AL_3);
  LED led_2 (.in(nand_86_out));
  nand nand_111 (nand_111_out, nand_84_out, XOR);
  nand nand_112 (nand_112_out, AND, nand_60_out);
  nand nand_113 (Carry_4, nand_85_out, nand_85_out);
  nand nand_114 (Sum_4, nand_85_out, nand_99_out);
  nand nand_115 (Carry_5, nand_100_out, nand_100_out);
  nand nand_116 (Sum_5, nand_101_out, nand_101_out);
  nand nand_117 (nand_117_out, nand_63_out, AL_4);
  nand nand_118 (nand_118_out, nand_86_out, nand_49_out);
  nand nand_119 (nand_119_out, nand_63_out, I6_4);
  nand nand_120 (Carry_6, nand_110_out, nand_110_out);
  nand nand_121 (nand_121_out, nand_102_out, nand_103_out);
  nand nand_122 (nand_122_out, nand_104_out, nand_105_out);
  nand nand_123 (nand_123_out, nand_106_out, nand_107_out);
  nand nand_124 (nand_124_out, nand_108_out, nand_109_out);
  nand nand_125 (Sum_6, nand_111_out, nand_112_out);
  nand nand_126 (Carry_7, nand_117_out, nand_117_out);
  nand nand_127 (Sum_7, nand_118_out, nand_119_out);
  LED u_F (.in(nand_122_out));
  LED F_2 (.in(nand_123_out));
  LED F_3 (.in(nand_124_out));
  LED led_3 (.in(Carry_5));
  LED F_4 (.in(nand_121_out));
  nand nand_128 (nand_128_out, nand_121_out, EN_4);
  nand nand_129 (nand_129_out, nand_122_out, EN_4);
  nand nand_130 (nand_130_out, nand_123_out, EN_4);
  nand nand_131 (nand_131_out, nand_124_out, EN_4);
  nand nand_132 (nand_132_out, nand_128_out, nand_128_out);
  nand nand_133 (nand_133_out, nand_129_out, nand_129_out);
  nand nand_134 (nand_134_out, nand_130_out, nand_130_out);
  nand nand_135 (nand_135_out, nand_131_out, nand_131_out);
  nand nand_136 (nand_136_out, nand_132_out, Din3);
  nand nand_137 (nand_137_out, nand_133_out, Din2);
  nand nand_138 (nand_138_out, nand_134_out, Din1);
  nand nand_139 (nand_139_out, nand_135_out, Din0);
  nand nand_140 (nand_140_out, nand_132_out, nand_136_out);
  nand nand_141 (nand_141_out, nand_136_out, Din3);
  nand nand_142 (nand_142_out, nand_133_out, nand_137_out);
  nand nand_143 (nand_143_out, nand_137_out, Din2);
  nand nand_144 (nand_144_out, nand_134_out, nand_138_out);
  nand nand_145 (nand_145_out, nand_138_out, Din1);
  nand nand_146 (nand_146_out, nand_135_out, nand_139_out);
  nand nand_147 (nand_147_out, nand_139_out, Din0);
  nand nand_148 (nand_148_out, A_14, B_12);
  nand nand_149 (nand_149_out, nand_140_out, nand_141_out);
  nand nand_150 (nand_150_out, nand_142_out, nand_143_out);
  nand nand_151 (nand_151_out, nand_144_out, nand_145_out);
  nand nand_152 (nand_152_out, nand_146_out, nand_147_out);
  nand nand_153 (nand_153_out, A_14, nand_148_out);
  nand nand_154 (nand_154_out, nand_148_out, B_12);
  nand nand_155 (nand_155_out, nand_149_out, nand_169_out);
  nand nand_156 (nand_156_out, nand_150_out, nand_172_out);
  nand nand_157 (nand_157_out, nand_151_out, nand_175_out);
  nand nand_158 (nand_158_out, nand_152_out, Cin);
  nand nand_159 (nand_159_out, B_10, A_12);
  nand nand_160 (nand_160_out, B_11, B_11);
  nand nand_161 (nand_161_out, A_13, A_13);
  nand nand_162 (nand_162_out, B_12, nand_148_out);
  nand nand_163 (nand_163_out, nand_153_out, nand_154_out);
  nand nand_164 (nand_164_out, nand_149_out, nand_155_out);
  nand nand_165 (nand_165_out, nand_155_out, nand_169_out);
  nand nand_166 (nand_166_out, nand_155_out, nand_136_out);
  nand nand_167 (nand_167_out, nand_150_out, nand_156_out);
  nand nand_168 (nand_168_out, nand_156_out, nand_172_out);
  nand nand_169 (nand_169_out, nand_156_out, nand_137_out);
  nand nand_170 (nand_170_out, nand_151_out, nand_157_out);
  nand nand_171 (nand_171_out, nand_157_out, nand_175_out);
  nand nand_172 (nand_172_out, nand_157_out, nand_138_out);
  nand nand_173 (nand_173_out, nand_152_out, nand_158_out);
  nand nand_174 (nand_174_out, nand_158_out, Cin);
  nand nand_175 (nand_175_out, nand_158_out, nand_139_out);
  nand nand_176 (nand_176_out, A_11, B_9);
  nand nand_177 (nand_177_out, CLK_4, nand_178_out);
  nand nand_178 (nand_178_out, DATA_4, CLK_4);
  nand nand_179 (nand_179_out, nC, nand_159_out);
  nand nand_180 (nand_180_out, I7, A_13);
  nand nand_181 (nand_181_out, I6, nand_161_out);
  nand nand_182 (nand_182_out, I5, A_13);
  nand nand_183 (nand_183_out, I4, nand_161_out);
  nand nand_184 (nand_184_out, nand_164_out, nand_165_out);
  nand nand_185 (nand_185_out, nand_167_out, nand_168_out);
  nand nand_186 (nand_186_out, nand_170_out, nand_171_out);
  nand nand_187 (nand_187_out, nand_173_out, nand_174_out);
  nand nand_188 (nand_188_out, nand_179_out, AL);
  nand nand_189 (nand_189_out, I5_2, nand_162_out);
  nand nand_190 (nand_190_out, nand_163_out, I4_2);
  nand nand_191 (nand_191_out, SEL_B, Bin);
  nand nand_192 (nand_192_out, SEL_A, Ain);
  nand nand_193 (nand_193_out, A_11, nand_176_out);
  nand nand_194 (nand_194_out, nand_176_out, B_9);
  nand nand_195 (nQ, nand_177_out, Q);
  nand nand_196 (Q, nQ, nand_178_out);
  nand nand_197 (nand_197_out, nand_180_out, nand_181_out);
  nand nand_198 (nand_198_out, nand_182_out, nand_183_out);
  LED Cout (.in(nand_166_out));
  LED Cout_2 (.in(nand_169_out));
  LED Cout_3 (.in(nand_172_out));
  LED Cout_4 (.in(nand_175_out));
  nand nand_199 (out_206, nand_188_out, nand_188_out);
  nand nand_200 (nand_200_out, nand_189_out, nand_190_out);
  nand nand_201 (nand_201_out, nand_184_out, clk_3);
  nand nand_202 (nand_202_out, nand_201_out, clk_3);
  nand nand_203 (nand_203_out, nand_185_out, clk_3);
  nand nand_204 (nand_204_out, nand_203_out, clk_3);
  nand nand_205 (nand_205_out, nand_186_out, clk_3);
  nand nand_206 (nand_206_out, nand_205_out, clk_3);
  nand nand_207 (nand_207_out, nand_187_out, clk_3);
  nand nand_208 (nand_208_out, nand_207_out, clk_3);
  nand nand_209 (Dout_6, nand_191_out, nand_192_out);
  nand nand_210 (Carry, nand_176_out, nand_176_out);
  nand nand_211 (Sum, nand_193_out, nand_194_out);
  nand nand_212 (nand_212_out, B_11, nand_197_out);
  nand nand_213 (nand_213_out, nand_198_out, nand_160_out);
  nand nand_214 (F, nand_212_out, nand_213_out);
  nand nand_215 (nand_215_out, nand_200_out, C_3);
  nand nand_216 (Dout_5, nand_201_out, nand_217_out);
  nand nand_217 (nand_217_out, Dout_5, nand_202_out);
  nand nand_218 (Dout_4, nand_203_out, nand_219_out);
  nand nand_219 (nand_219_out, Dout_4, nand_204_out);
  nand nand_220 (Dout_3, nand_205_out, nand_221_out);
  nand nand_221 (nand_221_out, Dout_3, nand_206_out);
  nand nand_222 (Dout_2, nand_207_out, nand_223_out);
  nand nand_223 (nand_223_out, Dout_2, nand_208_out);
  nand nand_224 (nand_224_out, nand_200_out, nand_215_out);
  nand nand_225 (nand_225_out, nand_215_out, C_3);
  nand nand_226 (Carry_2, nand_148_out, nand_215_out);
  nand nand_227 (Sum_2, nand_224_out, nand_225_out);
  nand nand_228 (nand_228_out, Zin, Zin);
  nand nand_229 (nand_229_out, I0, I0);
  nand nand_230 (nand_230_out, I1, I1);
  nand nand_231 (nand_231_out, I2, I2);
  nand nand_232 (nand_232_out, I3, I3);
  nand nand_233 (nand_233_out, in_59, in_59);
  nand nand_234 (nand_234_out, in_60, in_60);
  nand nand_235 (nand_235_out, S0_2, S0_2);
  nand nand_236 (nand_236_out, S1_2, S1_2);
  nand nand_237 (nand_237_out, nand_233_out, nand_234_out);
  nand nand_238 (nand_238_out, nand_228_out, nand_229_out);
  nand nand_239 (nand_239_out, nand_240_out, nand_240_out);
  nand nand_240 (nand_240_out, nand_241_out, out_137);
  nand nand_241 (nand_241_out, nand_242_out, nand_242_out);
  nand nand_242 (nand_242_out, nand_243_out, out_139);
  nand nand_243 (nand_243_out, nand_244_out, nand_244_out);
  nand nand_244 (nand_244_out, Carry_Out, out_141);
  nand nand_245 (Carry_Out, nand_246_out, nand_246_out);
  nand nand_246 (nand_246_out, C_in, Dout);
  nand nand_247 (nand_247_out, nand_237_out, nand_237_out);
  nand nand_248 (nand_248_out, in_61, in_61);
  nand nand_249 (nand_249_out, D, S0_2);
  nand nand_250 (nand_250_out, C, nand_235_out);
  nand nand_251 (nand_251_out, B_2, S0_2);
  nand nand_252 (nand_252_out, A_2, nand_235_out);
  nand nand_253 (nand_253_out, nand_238_out, nand_238_out);
  nand nand_254 (nand_254_out, S0, S0);
  nand nand_255 (nand_255_out, E1, E0);
  nand nand_256 (nand_256_out, nand_241_out, nand_240_out);
  nand nand_257 (nand_257_out, nand_240_out, out_137);
  nand nand_258 (nand_258_out, nand_243_out, nand_242_out);
  nand nand_259 (nand_259_out, nand_242_out, out_139);
  nand nand_260 (nand_260_out, Carry_Out, nand_244_out);
  nand nand_261 (nand_261_out, nand_244_out, out_141);
  nand nand_262 (nand_262_out, C_in, nand_246_out);
  nand nand_263 (nand_263_out, nand_246_out, Dout);
  nand nand_264 (nand_264_out, CLK_2, CLK_2);
  nand nand_265 (nand_265_out, nand_247_out, nand_248_out);
  nand nand_266 (nand_266_out, S1, S1);
  nand nand_267 (nand_267_out, nand_253_out, nand_230_out);
  nand nand_268 (nand_268_out, nand_256_out, nand_257_out);
  nand nand_269 (nand_269_out, nand_258_out, nand_259_out);
  nand nand_270 (nand_270_out, nand_260_out, nand_261_out);
  nand nand_271 (nand_271_out, nand_262_out, nand_263_out);
  nand nand_272 (nand_272_out, nand_249_out, nand_250_out);
  nand nand_273 (nand_273_out, nand_251_out, nand_252_out);
  nand nand_274 (nand_274_out, D3, nand_255_out);
  nand nand_275 (nand_275_out, S1, S0);
  nand nand_276 (nand_276_out, D2, nand_255_out);
  nand nand_277 (nand_277_out, nand_254_out, S1);
  nand nand_278 (nand_278_out, D1, nand_255_out);
  nand nand_279 (nand_279_out, S0, nand_266_out);
  nand nand_280 (nand_280_out, D0, nand_255_out);
  nand nand_281 (nand_281_out, nand_254_out, nand_266_out);
  nand nand_282 (nand_282_out, nand_267_out, nand_267_out);
  nand nand_283 (nand_283_out, nand_265_out, nand_265_out);
  nand nand_284 (nand_284_out, in_62, in_62);
  nand nand_285 (nand_285_out, S1_2, nand_272_out);
  nand nand_286 (nand_286_out, nand_273_out, nand_236_out);
  nand nand_287 (nand_287_out, nand_282_out, nand_231_out);
  nand nand_288 (nand_288_out, nand_268_out, nand_264_out);
  nand nand_289 (nand_289_out, nand_288_out, nand_264_out);
  nand nand_290 (nand_290_out, nand_269_out, nand_264_out);
  nand nand_291 (nand_291_out, nand_290_out, nand_264_out);
  nand nand_292 (nand_292_out, nand_270_out, nand_264_out);
  nand nand_293 (nand_293_out, nand_292_out, nand_264_out);
  nand nand_294 (nand_294_out, nand_271_out, nand_264_out);
  nand nand_295 (nand_295_out, nand_294_out, nand_264_out);
  nand nand_296 (nand_296_out, nand_283_out, nand_284_out);
  nand nand_297 (nand_297_out, nand_274_out, nand_274_out);
  nand nand_298 (nand_298_out, nand_275_out, nand_275_out);
  nand nand_299 (nand_299_out, nand_276_out, nand_276_out);
  nand nand_300 (nand_300_out, nand_277_out, nand_277_out);
  nand nand_301 (nand_301_out, nand_278_out, nand_278_out);
  nand nand_302 (nand_302_out, nand_279_out, nand_279_out);
  nand nand_303 (nand_303_out, nand_280_out, nand_280_out);
  nand nand_304 (nand_304_out, nand_281_out, nand_281_out);
  nand nand_305 (nand_305_out, nand_285_out, nand_286_out);
  nand nand_306 (nand_306_out, nand_287_out, nand_287_out);
  nand nand_307 (nand_307_out, nand_288_out, nand_308_out);
  nand nand_308 (nand_308_out, nand_307_out, nand_289_out);
  nand nand_309 (nand_309_out, nand_290_out, nand_310_out);
  nand nand_310 (nand_310_out, nand_309_out, nand_291_out);
  nand nand_311 (nand_311_out, nand_292_out, nand_312_out);
  nand nand_312 (nand_312_out, nand_311_out, nand_293_out);
  nand nand_313 (nand_313_out, nand_294_out, nand_314_out);
  nand nand_314 (nand_314_out, nand_313_out, nand_295_out);
  nand nand_315 (nand_315_out, nand_296_out, nand_296_out);
  nand nand_316 (nand_316_out, in_63, in_63);
  nand nand_317 (nand_317_out, nand_305_out, EN);
  nand nand_318 (nand_318_out, nand_306_out, nand_232_out);
  nand nand_319 (nand_319_out, nand_297_out, nand_298_out);
  nand nand_320 (nand_320_out, nand_299_out, nand_300_out);
  nand nand_321 (nand_321_out, nand_301_out, nand_302_out);
  nand nand_322 (nand_322_out, nand_303_out, nand_304_out);
  nand nand_323 (nand_323_out, nand_315_out, nand_316_out);
  nand nand_324 (nand_324_out, nand_317_out, nand_317_out);
  LED Zout (.in(nand_318_out));
  nand nand_325 (nand_325_out, DATAin3, Sel_Data);
  nand nand_326 (nand_326_out, nand_307_out, Sel_PC);
  nand nand_327 (nand_327_out, DATAin2, Sel_Data);
  nand nand_328 (nand_328_out, nand_309_out, Sel_PC);
  nand nand_329 (nand_329_out, DATAin1, Sel_Data);
  nand nand_330 (nand_330_out, nand_311_out, Sel_PC);
  nand nand_331 (nand_331_out, Din, Sel_Data);
  nand nand_332 (nand_332_out, nand_313_out, Sel_PC);
  nand nand_333 (nand_333_out, nand_323_out, nand_323_out);
  nand nand_334 (nand_334_out, in_64, in_64);
  nand nand_335 (nand_335_out, nand_319_out, nand_320_out);
  nand nand_336 (nand_336_out, nand_321_out, nand_322_out);
  LED led_4 (.in(nand_324_out));
  nand nand_337 (nand_337_out, nand_325_out, nand_326_out);
  nand nand_338 (nand_338_out, nand_327_out, nand_328_out);
  nand nand_339 (nand_339_out, nand_329_out, nand_330_out);
  nand nand_340 (nand_340_out, nand_331_out, nand_332_out);
  nand nand_341 (nand_341_out, nand_333_out, nand_334_out);
  nand nand_342 (nand_342_out, nand_335_out, nand_335_out);
  nand nand_343 (nand_343_out, nand_336_out, nand_336_out);
  nand nand_344 (nand_344_out, nand_337_out, CLK_2);
  nand nand_345 (nand_345_out, nand_344_out, CLK_2);
  nand nand_346 (nand_346_out, nand_338_out, CLK_2);
  nand nand_347 (nand_347_out, nand_346_out, CLK_2);
  nand nand_348 (nand_348_out, nand_339_out, CLK_2);
  nand nand_349 (nand_349_out, nand_348_out, CLK_2);
  nand nand_350 (nand_350_out, nand_340_out, CLK_2);
  nand nand_351 (nand_351_out, nand_350_out, CLK_2);
  nand nand_352 (nand_352_out, nand_342_out, nand_343_out);
  LED led_5 (.in(nand_341_out));
  LED led_6 (.in(nand_352_out));
  nand nand_353 (out_137, nand_344_out, nand_354_out);
  nand nand_354 (nand_354_out, out_137, nand_345_out);
  nand nand_355 (out_139, nand_346_out, nand_356_out);
  nand nand_356 (nand_356_out, out_139, nand_347_out);
  nand nand_357 (out_141, nand_348_out, nand_358_out);
  nand nand_358 (nand_358_out, out_141, nand_349_out);
  nand nand_359 (Dout, nand_350_out, nand_360_out);
  nand nand_360 (nand_360_out, Dout, nand_351_out);
  LED u_Q (.in(out_137));
  LED Q_2 (.in(out_139));
  LED Q_3 (.in(out_141));
  nand nand_361 (nand_361_out, S0_4, S0_4);
  nand nand_362 (nand_362_out, S1_4, S1_4);
  nand nand_363 (nand_363_out, S2, S2);
  nand nand_364 (nand_364_out, S0_3, S0_3);
  nand nand_365 (nand_365_out, S1_3, S1_3);
  nand nand_366 (nand_366_out, nand_361_out, nand_362_out);
  nand nand_367 (nand_367_out, S0_4, nand_362_out);
  nand nand_368 (nand_368_out, nand_361_out, S1_4);
  nand nand_369 (nand_369_out, S0_4, S1_4);
  nand nand_370 (nand_370_out, nand_361_out, nand_362_out);
  nand nand_371 (nand_371_out, S0_4, nand_362_out);
  nand nand_372 (nand_372_out, nand_361_out, S1_4);
  nand nand_373 (nand_373_out, S0_4, S1_4);
  nand nand_374 (nand_374_out, in_46, in_47);
  nand nand_375 (nand_375_out, in_48, in_49);
  nand nand_376 (nand_376_out, A_5, B_5);
  nand nand_377 (nand_377_out, nand_366_out, nand_366_out);
  nand nand_378 (nand_378_out, nand_367_out, nand_367_out);
  nand nand_379 (nand_379_out, nand_368_out, nand_368_out);
  nand nand_380 (nand_380_out, nand_369_out, nand_369_out);
  nand nand_381 (nand_381_out, nand_370_out, nand_370_out);
  nand nand_382 (nand_382_out, nand_371_out, nand_371_out);
  nand nand_383 (nand_383_out, nand_372_out, nand_372_out);
  nand nand_384 (nand_384_out, nand_373_out, nand_373_out);
  nand nand_385 (nand_385_out, nand_364_out, nand_365_out);
  nand nand_386 (nand_386_out, S0_3, nand_365_out);
  nand nand_387 (nand_387_out, nand_364_out, S1_3);
  nand nand_388 (nand_388_out, S0_3, S1_3);
  nand nand_389 (nand_389_out, in_35, in_36);
  nand nand_390 (nand_390_out, in_37, in_38);
  nand nand_391 (nand_391_out, in_21, in_22);
  nand nand_392 (nand_392_out, in_50, in_50);
  nand nand_393 (nand_393_out, in_23, in_24);
  nand nand_394 (nand_394_out, in_25, in_25);
  nand nand_395 (nand_395_out, in_26, in_26);
  nand nand_396 (nand_396_out, nand_385_out, nand_385_out);
  nand nand_397 (nand_397_out, nand_386_out, nand_386_out);
  nand nand_398 (nand_398_out, nand_387_out, nand_387_out);
  nand nand_399 (nand_399_out, nand_388_out, nand_388_out);
  nand nand_400 (nand_400_out, nand_374_out, nand_374_out);
  nand nand_401 (nand_401_out, nand_375_out, nand_375_out);
  nand nand_402 (nand_402_out, nand_376_out, EN_2);
  nand nand_403 (nand_403_out, nand_389_out, nand_389_out);
  nand nand_404 (nand_404_out, nand_390_out, nand_390_out);
  nand nand_405 (nand_405_out, nand_391_out, nand_392_out);
  nand nand_406 (nand_406_out, nand_392_out, nand_393_out);
  nand nand_407 (nand_407_out, nand_377_out, nand_363_out);
  nand nand_408 (nand_408_out, nand_378_out, nand_363_out);
  nand nand_409 (nand_409_out, nand_379_out, nand_363_out);
  nand nand_410 (nand_410_out, nand_380_out, nand_363_out);
  nand nand_411 (nand_411_out, nand_381_out, S2);
  nand nand_412 (nand_412_out, nand_382_out, S2);
  nand nand_413 (nand_413_out, nand_383_out, S2);
  nand nand_414 (nand_414_out, nand_384_out, S2);
  nand nand_415 (nand_415_out, nand_396_out, EN_3);
  nand nand_416 (nand_416_out, nand_397_out, EN_3);
  nand nand_417 (nand_417_out, nand_398_out, EN_3);
  nand nand_418 (nand_418_out, nand_399_out, EN_3);
  nand nand_419 (nand_419_out, nand_394_out, nand_395_out);
  nand nand_420 (nand_420_out, nand_400_out, nand_401_out);
  LED led_7 (.in(nand_402_out));
  nand nand_421 (nand_421_out, nand_403_out, nand_404_out);
  nand nand_422 (nand_422_out, nand_405_out, nand_406_out);
  LED led_8 (.in(nand_407_out));
  LED led_9 (.in(nand_408_out));
  LED led_10 (.in(nand_409_out));
  LED led_11 (.in(nand_410_out));
  LED led_12 (.in(nand_411_out));
  LED led_13 (.in(nand_412_out));
  LED led_14 (.in(nand_413_out));
  LED led_15 (.in(nand_414_out));
  LED led_16 (.in(nand_415_out));
  LED led_17 (.in(nand_416_out));
  LED led_18 (.in(nand_417_out));
  LED led_19 (.in(nand_418_out));
  LED led_20 (.in(nand_419_out));
  LED led_21 (.in(nand_420_out));
  LED led_22 (.in(nand_421_out));
  LED led_23 (.in(nand_422_out));
  nand nand_423 (nand_423_out, in_126, in_127);
  nand nand_424 (nand_424_out, in_128, in_129);
  nand nand_425 (nand_425_out, in_131, in_132);
  nand nand_426 (nand_426_out, in_133, in_134);
  nand nand_427 (nand_427_out, A, B);
  nand nand_428 (nand_428_out, A_6, Invert_A_nA);
  nand nand_429 (nand_429_out, Select_A_nB, Select_A_nB);
  nand nand_430 (nand_430_out, in_120, in_120);
  nand nand_431 (nand_431_out, A, nand_427_out);
  nand nand_432 (nand_432_out, nand_427_out, B);
  nand nand_433 (nand_433_out, A_6, nand_428_out);
  nand nand_434 (nand_434_out, nand_428_out, Invert_A_nA);
  nand nand_435 (nand_435_out, A_7, Select_A_nB);
  nand nand_436 (nand_436_out, nand_429_out, B_6);
  nand nand_437 (nand_437_out, in_53, in_53);
  nand nand_438 (nand_438_out, in_54, in_54);
  nand nand_439 (nand_439_out, in_51, in_51);
  nand nand_440 (nand_440_out, in_52, in_52);
  nand nand_441 (nand_441_out, A_3, A_3);
  nand nand_442 (nand_442_out, B_3, B_3);
  nand nand_443 (nand_443_out, A_4, B_4);
  nand nand_444 (nand_444_out, A_9, A_9);
  nand nand_445 (nand_445_out, B_7, B_7);
  nand nand_446 (nand_446_out, nand_423_out, nand_423_out);
  nand nand_447 (nand_447_out, nand_424_out, nand_424_out);
  nand nand_448 (nand_448_out, nand_425_out, nand_426_out);
  nand nand_449 (nand_449_out, A_8, in_120);
  nand nand_450 (nand_450_out, nand_430_out, A_8);
  nor nor_1 (nor_1_out, in_1, in_3, in_5, in_7);
  xor xor_1 (xor_1_out, in_1, in_2);
  xor xor_2 (xor_2_out, in_3, in_4);
  xor xor_3 (xor_3_out, in_5, in_6);
  xor xor_4 (xor_4_out, in_7, in_8);
  nand nand_451 (nand_451_out, nand_437_out, nand_438_out);
  nand nand_452 (nand_452_out, nand_439_out, nand_440_out);
  nand nand_453 (out_112, nand_441_out, nand_442_out);
  nand nand_454 (out_113, nand_443_out, nand_443_out);
  nand nand_455 (nand_455_out, nand_444_out, nand_445_out);
  nand nand_456 (nand_456_out, nand_446_out, nand_446_out);
  nand nand_457 (nand_457_out, nand_447_out, nand_447_out);
  nand nand_458 (out_135, nand_448_out, nand_448_out);
  LED led_24 (.in(nand_449_out));
  LED led_25 (.in(nand_450_out));
  nand nand_459 (nand_459_out, nand_431_out, nand_432_out);
  nand nand_460 (nand_460_out, nand_433_out, nand_434_out);
  nand nand_461 (nand_461_out, nand_435_out, nand_436_out);
  LED led_26 (.in(nand_459_out));
  LED led_27 (.in(nand_460_out));
  LED led_28 (.in(nand_461_out));
  nand nand_462 (nand_462_out, nand_451_out, nand_451_out);
  nand nand_463 (nand_463_out, nand_452_out, nand_452_out);
  nand nand_464 (out_125, nand_455_out, nand_455_out);
  nand nand_465 (nand_465_out, nand_456_out, nand_457_out);
  nor nor_2 (nor_2_out, xor_1_out, xor_2_out, xor_3_out, xor_4_out);
  nand nand_466 (nand_466_out, nand_462_out, nand_463_out);
  nand nand_467 (out_130, nand_465_out, nand_465_out);
  LED led_29 (.in(nor_1_out));
  LED led_30 (.in(nor_2_out));
  LED led_31 (.in(nand_466_out));
  nand nand_468 (nand_468_out, in_17, in_17);
  nand nand_469 (nand_469_out, nand_516_out, nand_516_out);
  nand nand_470 (nand_470_out, DAT_2, DAT_2);
  nand nand_471 (nand_471_out, in_15, in_15);
  nand nand_472 (nand_472_out, nand_518_out, DAT, in_13);
  nand nand_473 (nand_473_out, in_13, DAT, nand_517_out);
  nand nand_474 (nand_474_out, in_13, in_13);
  nand nand_475 (nand_475_out, DAT_2, in_15);
  nand nand_476 (nand_476_out, in_15, nand_470_out);
  nand nand_477 (nand_477_out, nand_516_out, nand_468_out);
  nand nand_478 (nand_478_out, nand_468_out, nand_469_out);
  nand nand_479 (nand_479_out, in_77, nand_633_out);
  nand nand_480 (nand_480_out, nand_493_out, nand_635_out);
  nand nand_481 (nand_481_out, nand_496_out, nand_637_out);
  nand nand_482 (nand_482_out, nand_499_out, nand_639_out);
  nand nand_483 (nand_483_out, nand_472_out, nand_484_out);
  nand nand_484 (nand_484_out, nand_483_out, nand_473_out);
  nand nand_485 (nand_485_out, nand_475_out, nand_486_out);
  nand nand_486 (nand_486_out, nand_485_out, nand_476_out);
  nand nand_487 (nand_487_out, nand_477_out, nand_488_out);
  nand nand_488 (nand_488_out, nand_487_out, nand_478_out);
  nand nand_489 (nand_489_out, D_2, LD);
  nand nand_490 (nand_490_out, nand_489_out, LD);
  nand nand_491 (nand_491_out, in_77, nand_479_out);
  nand nand_492 (nand_492_out, nand_479_out, nand_633_out);
  nand nand_493 (nand_493_out, nand_479_out, nand_479_out);
  nand nand_494 (nand_494_out, nand_493_out, nand_480_out);
  nand nand_495 (nand_495_out, nand_480_out, nand_635_out);
  nand nand_496 (nand_496_out, nand_480_out, nand_480_out);
  nand nand_497 (nand_497_out, nand_496_out, nand_481_out);
  nand nand_498 (nand_498_out, nand_481_out, nand_637_out);
  nand nand_499 (nand_499_out, nand_481_out, nand_481_out);
  nand nand_500 (nand_500_out, nand_499_out, nand_482_out);
  nand nand_501 (nand_501_out, nand_482_out, nand_639_out);
  nand nand_502 (nand_502_out, nand_482_out, nand_482_out);
  nand nand_503 (nand_503_out, nand_489_out, nand_504_out);
  nand nand_504 (nand_504_out, nand_503_out, nand_490_out);
  nand nand_505 (nand_505_out, nand_491_out, nand_492_out);
  nand nand_506 (nand_506_out, nand_494_out, nand_495_out);
  nand nand_507 (nand_507_out, nand_497_out, nand_498_out);
  nand nand_508 (nand_508_out, nand_500_out, nand_501_out);
  nand nand_509 (nand_509_out, nand_483_out, nand_474_out);
  nand nand_510 (nand_510_out, nand_474_out, nand_484_out);
  nand nand_511 (nand_511_out, nand_485_out, nand_471_out);
  nand nand_512 (nand_512_out, nand_471_out, nand_486_out);
  nand nand_513 (nand_513_out, nand_487_out, in_17);
  nand nand_514 (nand_514_out, in_17, nand_488_out);
  LED Q_4 (.in(nand_503_out));
  LED u_nQ (.in(nand_504_out));
  nand nand_515 (nand_515_out, nand_513_out, nand_516_out);
  nand nand_516 (nand_516_out, nand_515_out, nand_514_out);
  nand nand_517 (nand_517_out, nand_509_out, nand_518_out);
  nand nand_518 (nand_518_out, nand_517_out, nand_510_out);
  nand nand_519 (nand_519_out, nand_511_out, nand_520_out);
  nand nand_520 (nand_520_out, nand_519_out, nand_512_out);
  LED Q_5 (.in(nand_517_out));
  LED nQ_2 (.in(nand_518_out));
  LED Q_6 (.in(nand_519_out));
  LED nQ_3 (.in(nand_520_out));
  LED Q_7 (.in(nand_515_out));
  LED nQ_4 (.in(nand_516_out));
  nand nand_521 (nand_521_out, nLD, nLD);
  nand nand_522 (nand_522_out, nLD, nLD);
  nand nand_523 (nand_523_out, nLD, nLD);
  nand nand_524 (nand_524_out, nLD, nLD);
  nand nand_525 (nand_525_out, nand_505_out, nLD);
  nand nand_526 (nand_526_out, nand_521_out, DATA_0);
  nand nand_527 (nand_527_out, nand_506_out, nLD);
  nand nand_528 (nand_528_out, nand_522_out, DATA_1);
  nand nand_529 (nand_529_out, nand_507_out, nLD);
  nand nand_530 (nand_530_out, nand_523_out, DATA_2);
  nand nand_531 (nand_531_out, nand_508_out, nLD);
  nand nand_532 (nand_532_out, nand_524_out, DATA_3);
  nand nand_533 (nand_533_out, A_15, B_13);
  nand nand_534 (nand_534_out, nLD_2, nLD_2);
  nand nand_535 (nand_535_out, nand_525_out, nand_526_out);
  nand nand_536 (nand_536_out, RES, RES);
  nand nand_537 (nand_537_out, nand_527_out, nand_528_out);
  nand nand_538 (nand_538_out, nand_529_out, nand_530_out);
  nand nand_539 (nand_539_out, nand_531_out, nand_532_out);
  nand nand_540 (nand_540_out, A_nB, A_nB);
  nand nand_541 (nand_541_out, A_nB, A_nB);
  nand nand_542 (nand_542_out, A_nB, A_nB);
  nand nand_543 (nand_543_out, A_nB, A_nB);
  nand nand_544 (nand_544_out, A_nB, A_nB);
  nand nand_545 (nand_545_out, A_nB, A_nB);
  nand nand_546 (nand_546_out, A_nB, A_nB);
  nand nand_547 (nand_547_out, A_nB, A_nB);
  nand nand_548 (nand_548_out, A_15, nand_533_out);
  nand nand_549 (nand_549_out, nand_533_out, B_13);
  nand nand_550 (nand_550_out, nand_622_out, nLD_2);
  nand nand_551 (nand_551_out, nand_534_out, DATA);
  nand nand_552 (nand_552_out, nand_535_out, nand_536_out);
  nand nand_553 (nand_553_out, nand_537_out, nand_536_out);
  nand nand_554 (nand_554_out, nand_538_out, nand_536_out);
  nand nand_555 (nand_555_out, nand_539_out, nand_536_out);
  nand nand_556 (nand_556_out, A0, A_nB);
  nand nand_557 (nand_557_out, nand_540_out, B0);
  nand nand_558 (nand_558_out, A1, A_nB);
  nand nand_559 (nand_559_out, nand_541_out, B1);
  nand nand_560 (nand_560_out, A2, A_nB);
  nand nand_561 (nand_561_out, nand_542_out, B2);
  nand nand_562 (nand_562_out, A3, A_nB);
  nand nand_563 (nand_563_out, nand_543_out, B3);
  nand nand_564 (nand_564_out, A4, A_nB);
  nand nand_565 (nand_565_out, nand_544_out, B4);
  nand nand_566 (nand_566_out, A5, A_nB);
  nand nand_567 (nand_567_out, nand_545_out, B5);
  nand nand_568 (nand_568_out, A6, A_nB);
  nand nand_569 (nand_569_out, nand_546_out, B6);
  nand nand_570 (nand_570_out, A7, A_nB);
  nand nand_571 (nand_571_out, nand_547_out, B7);
  nand nand_572 (nand_572_out, nand_548_out, nand_549_out);
  nand nand_573 (nand_573_out, nand_550_out, nand_551_out);
  nand nand_574 (nand_574_out, I5_3, nand_572_out);
  nand nand_575 (nand_575_out, B_13, I4_3);
  nand nand_576 (out_104, nand_556_out, nand_557_out);
  nand nand_577 (out_105, nand_558_out, nand_559_out);
  nand nand_578 (out_106, nand_560_out, nand_561_out);
  nand nand_579 (out_107, nand_562_out, nand_563_out);
  nand nand_580 (out_108, nand_564_out, nand_565_out);
  nand nand_581 (out_109, nand_566_out, nand_567_out);
  nand nand_582 (out_110, nand_568_out, nand_569_out);
  nand nand_583 (out_111, nand_570_out, nand_571_out);
  nand nand_584 (nand_584_out, CK_2, CK_2);
  nand nand_585 (nand_585_out, nand_573_out, nand_573_out);
  nand nand_586 (nand_586_out, nand_574_out, nand_575_out);
  nand nand_587 (nand_587_out, CK, CK);
  nand nand_588 (nand_588_out, nand_552_out, nand_552_out);
  nand nand_589 (nand_589_out, CK, CK);
  nand nand_590 (nand_590_out, nand_553_out, nand_553_out);
  nand nand_591 (nand_591_out, CK, CK);
  nand nand_592 (nand_592_out, nand_554_out, nand_554_out);
  nand nand_593 (nand_593_out, CK, CK);
  nand nand_594 (nand_594_out, nand_555_out, nand_555_out);
  nand nand_595 (nand_595_out, nand_573_out, nand_584_out);
  nand nand_596 (nand_596_out, nand_584_out, nand_585_out);
  nand nand_597 (nand_597_out, nand_586_out, C_4);
  nand nand_598 (nand_598_out, nand_552_out, nand_587_out);
  nand nand_599 (nand_599_out, nand_587_out, nand_588_out);
  nand nand_600 (nand_600_out, nand_553_out, nand_589_out);
  nand nand_601 (nand_601_out, nand_589_out, nand_590_out);
  nand nand_602 (nand_602_out, nand_554_out, nand_591_out);
  nand nand_603 (nand_603_out, nand_591_out, nand_592_out);
  nand nand_604 (nand_604_out, nand_555_out, nand_593_out);
  nand nand_605 (nand_605_out, nand_593_out, nand_594_out);
  nand nand_606 (nand_606_out, nand_595_out, nand_607_out);
  nand nand_607 (nand_607_out, nand_606_out, nand_596_out);
  nand nand_608 (nand_608_out, nand_533_out, nand_597_out);
  nand nand_609 (nand_609_out, nand_586_out, nand_597_out);
  nand nand_610 (nand_610_out, nand_597_out, C_4);
  nand nand_611 (nand_611_out, nand_598_out, nand_612_out);
  nand nand_612 (nand_612_out, nand_611_out, nand_599_out);
  nand nand_613 (nand_613_out, nand_600_out, nand_614_out);
  nand nand_614 (nand_614_out, nand_613_out, nand_601_out);
  nand nand_615 (nand_615_out, nand_602_out, nand_616_out);
  nand nand_616 (nand_616_out, nand_615_out, nand_603_out);
  nand nand_617 (nand_617_out, nand_604_out, nand_618_out);
  nand nand_618 (nand_618_out, nand_617_out, nand_605_out);
  nand nand_619 (nand_619_out, nand_606_out, CK_2);
  nand nand_620 (nand_620_out, CK_2, nand_607_out);
  nand nand_621 (Sum_3, nand_609_out, nand_610_out);
  nand nand_622 (nand_622_out, nand_619_out, nand_623_out);
  nand nand_623 (nand_623_out, nand_622_out, nand_620_out);
  nand nand_624 (nand_624_out, nand_611_out, CK);
  nand nand_625 (nand_625_out, CK, nand_612_out);
  nand nand_626 (nand_626_out, nand_613_out, CK);
  nand nand_627 (nand_627_out, CK, nand_614_out);
  nand nand_628 (nand_628_out, nand_615_out, CK);
  nand nand_629 (nand_629_out, CK, nand_616_out);
  nand nand_630 (nand_630_out, nand_617_out, CK);
  nand nand_631 (nand_631_out, CK, nand_618_out);
  nand nand_632 (nand_632_out, A_nB_2, A_nB_2);
  nand nand_633 (nand_633_out, nand_624_out, nand_634_out);
  nand nand_634 (nand_634_out, nand_633_out, nand_625_out);
  nand nand_635 (nand_635_out, nand_626_out, nand_636_out);
  nand nand_636 (nand_636_out, nand_635_out, nand_627_out);
  nand nand_637 (nand_637_out, nand_628_out, nand_638_out);
  nand nand_638 (nand_638_out, nand_637_out, nand_629_out);
  nand nand_639 (nand_639_out, nand_630_out, nand_640_out);
  nand nand_640 (nand_640_out, nand_639_out, nand_631_out);
  LED Q_8 (.in(nand_622_out));
  LED nQ_5 (.in(nand_623_out));
  nand nand_641 (nand_641_out, A8, A_nB_2);
  nand nand_642 (nand_642_out, nand_632_out, B8);
  nand nand_643 (nand_643_out, A9, A_nB_2);
  nand nand_644 (nand_644_out, nand_632_out, B9);
  nand nand_645 (nand_645_out, A10, A_nB_2);
  nand nand_646 (nand_646_out, nand_632_out, B10);
  nand nand_647 (nand_647_out, A11, A_nB_2);
  nand nand_648 (nand_648_out, nand_632_out, B11);
  nand nand_649 (nand_649_out, A12, A_nB_2);
  nand nand_650 (nand_650_out, nand_632_out, B12);
  nand nand_651 (nand_651_out, A13, A_nB_2);
  nand nand_652 (nand_652_out, nand_632_out, B13);
  nand nand_653 (nand_653_out, A14, A_nB_2);
  nand nand_654 (nand_654_out, nand_632_out, B14);
  nand nand_655 (nand_655_out, A15, A_nB_2);
  nand nand_656 (nand_656_out, nand_632_out, B15);
  nand nand_657 (nand_657_out, nand_608_out, AL_2);
  LED Q_9 (.in(nand_633_out));
  LED nQ_6 (.in(nand_634_out));
  LED Q_10 (.in(nand_635_out));
  LED nQ_7 (.in(nand_636_out));
  LED Q_11 (.in(nand_637_out));
  LED nQ_8 (.in(nand_638_out));
  LED Q_12 (.in(nand_639_out));
  LED nQ_9 (.in(nand_640_out));
  nand nand_658 (out_181, nand_641_out, nand_642_out);
  nand nand_659 (out_182, nand_643_out, nand_644_out);
  nand nand_660 (out_183, nand_645_out, nand_646_out);
  nand nand_661 (out_184, nand_647_out, nand_648_out);
  nand nand_662 (out_185, nand_649_out, nand_650_out);
  nand nand_663 (out_186, nand_651_out, nand_652_out);
  nand nand_664 (out_187, nand_653_out, nand_654_out);
  nand nand_665 (out_188, nand_655_out, nand_656_out);
  nand nand_666 (Carry_3, nand_657_out, nand_657_out);

  // Notes on the sheet:
  //   C  I1 I0
  //   0   0   0      F = 0
  //   0   0   1      F = B 
  //   0   1   0      F = A XOR B
  //   0   1   1      F = A OR B
  //   1   0   0      F = 1
  //   1   0   1      F = ~B
  //   1   1   0      F = A XNOR B
  //   1   1   1      F = A NOR B
  //   12+2 GATE ALU  - With Carry Suppression
  //   16 GATE ALU
  //   Instruction I3 I2 I1 I0
  //   0000   F = 0
  //   0001   F = A NOR B
  //   0010   F = A AND ~B
  //   0011  F = ~B
  //   0100  F = ~A AND B
  //   0101  F = ~A
  //   0110  F = A XOR B
  //   0111  F = A NAND B
  //   1000  F = A AND B
  //   1001  F = A XNOR B
  //   1010  F = A
  //   1011  F = A OR ~B
  //   1100  F = B
  //   1101 F = ~A OR B
  //   1110   F = A OR B
  //   1111  F = 1
  //   C  I1 I0
  //   0   0   0    F = 0
  //   0   0   1    F = A XOR B 
  //   0   1   0    F = A AND B
  //   0   1   1    F = A OR B
  //   1   0   0    F = 1
  //   1   0   1    F = A XNOR B
  //   1   1   0    F = A NAND B
  //   1   1   1    F = A NOR B
  //   Half Adder AND/XOR
  //   LOGIC UNIT (74HC153 4:1 MUX)
  //   Gated Latch
  //   CARRY LOGIC
  //   2 Input Mux
  //   13 Gate ALU
  //   2 Input Multiplexer
  //   Half Adder / Invert
  //   Multi-Input OR Chain - for zero detection
  //   4:1 Multiplexer with Enable
  //   Half Adder
  //   4:1 Multiplexer
  //   PC
  //   PC Latch
  //   MUX
  //   ADDR Latch
  //   2 to 4 line decoder with enable ('139)
  //   1 of 8 decoder ('138)
  //   2-Input AND with enable
  //   4 Input AND-OR
  //   2-Input OR
  //   4-Input Nand
  //   1 of 2 Decoder/Demux (Inverting)
  //   4-Input A-O-I Gate simplified
  //   XOR used as Invert Stage
  //   2 Input XOR
  //   4-bit Comparator A=B and Zero Detect A=0
  //   2-Input NOR
  //   4-Input A-O-I Gate
  //   2-Input AND
  //   4 Input OR
  //   4002
  //   A=0
  //   A=B
  //   Master-Slave JK Flipflop
  //   D-Type Flipflop
  //   Toggle -Type Flipflop
  //   Gated D-Latch
  //   4-bit Program Counter Slice
  //   Register Stage in 14 Gates
  //   Octal 2:1 selector (74157)
endmodule
