// Digital circuit ALU_datapath_3.dig as structural Verilog
module ALU_datapath_3 (
  input  C,
  input  D,
  input  A,
  input  B,
  input  Din,
  input  Cin,
  input  CLK,
  input  C_2,
  input  D_2,
  input  A_2,
  input  B_2,
  input  Din_2,
  input  Cin_2,
  input  CLK_2,
  input  Ain,
  output Dout0,
  output Dout1
);

  wire nand_1_out, nand_3_out, nand_4_out, nand_5_out, nand_6_out, nand_7_out, nand_8_out, nand_9_out,
       nand_10_out, nand_11_out, nand_12_out, nand_13_out, nand_14_out, nand_15_out, nand_16_out,
       nand_17_out, nand_18_out, nand_19_out, nand_20_out, nand_21_out, nand_22_out, nand_23_out,
       nand_24_out, nand_25_out, nand_26_out, nand_27_out, nand_28_out, nand_29_out, nand_30_out,
       nand_31_out, nand_32_out, nand_33_out, nand_34_out, nand_35_out, nand_36_out, nand_37_out,
       nand_38_out, nand_39_out, nand_40_out, nand_41_out, nand_42_out, nand_43_out, nand_45_out, nand_47_out;

  nand nand_1 (nand_1_out, CLK, CLK);
  nand nand_2 (Dout1, CLK_2, CLK_2);
  nand nand_3 (nand_3_out, Dout0, nand_1_out);
  nand nand_4 (nand_4_out, nand_3_out, nand_1_out);
  nand nand_5 (nand_5_out, nand_3_out, nand_6_out);
  nand nand_6 (nand_6_out, nand_5_out, nand_4_out);
  nand nand_7 (nand_7_out, Ain, Ain);
  LED u_A (.in(nand_5_out));
  LED u_B (.in(Din));
  LED u_A_2 (.in(Ain));
  LED u_B_2 (.in(Din_2));
  nand nand_8 (nand_8_out, D, nand_5_out);
  nand nand_9 (nand_9_out, C, nand_6_out);
  nand nand_10 (nand_10_out, B, nand_5_out);
  nand nand_11 (nand_11_out, A, nand_6_out);
  nand nand_12 (nand_12_out, D_2, Ain);
  nand nand_13 (nand_13_out, C_2, nand_7_out);
  nand nand_14 (nand_14_out, B_2, Ain);
  nand nand_15 (nand_15_out, A_2, nand_7_out);
  nand nand_16 (nand_16_out, nand_8_out, nand_9_out);
  nand nand_17 (nand_17_out, nand_10_out, nand_11_out);
  nand nand_18 (nand_18_out, Din, Din);
  nand nand_19 (nand_19_out, nand_5_out, Din);
  nand nand_20 (nand_20_out, nand_12_out, nand_13_out);
  nand nand_21 (nand_21_out, nand_14_out, nand_15_out);
  nand nand_22 (nand_22_out, Din_2, Din_2);
  nand nand_23 (nand_23_out, Ain, Din_2);
  nand nand_24 (nand_24_out, Din, nand_16_out);
  nand nand_25 (nand_25_out, nand_17_out, nand_18_out);
  LED nC (.in(nand_19_out));
  nand nand_26 (nand_26_out, Din_2, nand_20_out);
  nand nand_27 (nand_27_out, nand_21_out, nand_22_out);
  LED nC_2 (.in(nand_23_out));
  nand nand_28 (nand_28_out, nand_24_out, nand_25_out);
  nand nand_29 (nand_29_out, nand_26_out, nand_27_out);
  LED Q (.in(nand_28_out));
  nand nand_30 (nand_30_out, nand_28_out, Cin);
  LED Q_2 (.in(nand_29_out));
  nand nand_31 (nand_31_out, nand_29_out, Cin_2);
  nand nand_32 (nand_32_out, nand_28_out, nand_30_out);
  nand nand_33 (nand_33_out, nand_30_out, Cin);
  nand nand_34 (nand_34_out, nand_30_out, nand_19_out);
  LED Cout (.in(nand_34_out));
  nand nand_35 (nand_35_out, nand_29_out, nand_31_out);
  nand nand_36 (nand_36_out, nand_31_out, Cin_2);
  nand nand_37 (nand_37_out, nand_31_out, nand_23_out);
  nand nand_38 (nand_38_out, nand_32_out, nand_33_out);
  LED Cout_2 (.in(nand_37_out));
  nand nand_39 (nand_39_out, nand_38_out, CLK);
  nand nand_40 (nand_40_out, nand_39_out, CLK);
  nand nand_41 (nand_41_out, nand_35_out, nand_36_out);
  LED led_1 (.in(nand_41_out));
  nand nand_42 (nand_42_out, nand_41_out, CLK_2);
  nand nand_43 (nand_43_out, nand_42_out, CLK_2);
  nand nand_44 (Dout0, nand_39_out, nand_45_out);
  nand nand_45 (nand_45_out, Dout0, nand_40_out);
  Seven_Seg_Hex seven_seg_hex_1 (.d({3'b000, Dout0}), .dp(1'b0));
  nand nand_46 (Dout1, nand_42_out, nand_47_out);
  nand nand_47 (nand_47_out, Dout1, nand_43_out);
  Seven_Seg_Hex seven_seg_hex_2 (.d({3'b000, Dout1}), .dp(1'b0));

  // Notes on the sheet:
  //   DCBA
  //   0000    Q = 0
  //   0001    Q = A NOR B
  //   0011     Q = ~B
  //   0101     Q = ~A
  //   0110      Q = A XOR B
  //   0111      Q = A NAND B
  //   1000      Q = A AND B
  //   1010      Q = A
  //   1100      Q = B
  //   1110      Q = A OR B
  //   1111      Q = 1
  //   INSTRUCTION
  //   INPUT
  //   ACCUMULATOR
  //   ALU and Data Path in 30 NAND2 Gates
  //   ALU and Data Path in 25 NAND2 Gates
  //   BOOLEAN UNIT
  //   Carry Generator
  //   HALF ADDER
  //   DATA LATCH
endmodule
