// Digital circuit Aardvark_2.dig as structural Verilog
module Aardvark_2 (
  input  in_1,
  input  in_2,
  input  in_3,
  input  in_4,
  input  in_5,
  input  in_6,
  input  in_7,
  input  in_8,
  input  in_9,
  input  in_10,
  input  in_11,
  input  in_12,
  input  in_13,
  input  clk,
  input  in_15,
  input  in_16,
  input  in_17,
  input  in_18,
  input  in_19,
  input  in_20,
  input  in_21,
  input  in_22,
  input  in_23,
  input  in_24,
  input  in_25,
  input  in_26,
  input  in_27,
  input  in_28,
  input  in_29
);

  wire _2x157_octal_mux_1_d0, _2x157_octal_mux_1_d1, _2x157_octal_mux_1_d2, _2x157_octal_mux_1_d3,
       _2x157_octal_mux_1_d4, _2x157_octal_mux_1_d5, _2x157_octal_mux_1_d6, _2x157_octal_mux_1_d7,
       _2x157_octal_mux_2_d0, _2x157_octal_mux_2_d1, _2x157_octal_mux_2_d2, _2x157_octal_mux_2_d3,
       _2x157_octal_mux_2_d4, _2x157_octal_mux_2_d5, _2x157_octal_mux_2_d6, _2x157_octal_mux_2_d7,
       _27c1024_1_p9, _27c1024_1_p10, _27c1024_1_p11, _27c1024_1_p12, _27c1024_1_p13, _27c1024_1_p15,
       _27c1024_1_p16, _27c1024_1_p17, _27c1024_1_p18, _27c1024_1_p19, _27c1024_1_p20, _27c1024_1_p21,
       _27c1024_1_p22, _74573_2_pin2, _74573_2_pin3, _74573_2_pin4, IR0, IR1, IR2, IR3, IR4, IR5, IR6, IR7,
       reg_8_1_p11, reg_8_1_p12, reg_8_1_p13, reg_8_1_p14, reg_8_1_p15, reg_8_1_p16, reg_8_1_p17,
       reg_8_1_p18, reg_8_2_p2, reg_8_2_p3, reg_8_2_p4, reg_8_2_p5, reg_8_2_p6, reg_8_2_p7, reg_8_2_p8,
       reg_8_2_p9, reg_8_2_p10;
  wire [3:0] _74573_2_pin12, _74573_2_pin16, alu_8_40pin_1_p3, alu_8_40pin_1_p9, pc1634_1_p14, pc1634_1_p19,
       pc1634_1_p23, undriven;

  // PC1634 pc1634_1: pin names not known; wires that end beside it: 1'b0, 1'b0, 1'b0, 1'b0, 1'b0, 1'b0, 1'b0, clk, 1'b1, 1'b1, pc1634_1_p14[0], pc1634_1_p14[1], pc1634_1_p14[2], pc1634_1_p14[3], pc1634_1_p19[0], 1'b0, pc1634_1_p19[1], pc1634_1_p19[2], pc1634_1_p19[3], pc1634_1_p23[0], pc1634_1_p23[1], pc1634_1_p23[2], pc1634_1_p23[3], in_19, in_20
  Seven_Seg_Hex seven_seg_hex_1 (.d(pc1634_1_p23), .dp(1'b0));
  Seven_Seg_Hex seven_seg_hex_2 (.d(pc1634_1_p19), .dp(1'b0));
  Seven_Seg_Hex seven_seg_hex_3 (.d(pc1634_1_p14), .dp(1'b0));
  Seven_Seg_Hex seven_seg_hex_4 (.d(undriven), .dp(1'b0));
  // _27C1024 _27c1024_1: pin names not known; wires that end beside it: pc1634_1_p19[1], pc1634_1_p19[2], pc1634_1_p19[3], pc1634_1_p23[0], pc1634_1_p23[1], pc1634_1_p23[2], pc1634_1_p23[3], 1'b1, _27c1024_1_p9, _27c1024_1_p10, _27c1024_1_p11, _27c1024_1_p12, _27c1024_1_p13, 1'b0, _27c1024_1_p15, _27c1024_1_p16, _27c1024_1_p17, _27c1024_1_p18, _27c1024_1_p19, _27c1024_1_p20, _27c1024_1_p21, _27c1024_1_p22, 1'b0, 1'b1
  _74573 _74573_1 (
    .pin1(1'b0), .pin2(_27c1024_1_p15), .pin3(_27c1024_1_p16), .pin4(_27c1024_1_p17), .pin5(_27c1024_1_p18),
    .pin6(_27c1024_1_p19), .pin7(_27c1024_1_p20), .pin8(_27c1024_1_p21), .pin9(_27c1024_1_p22), .pin10(1'b0),
    .pin11(clk), .pin12(IR7), .pin13(IR6), .pin14(IR5), .pin15(IR4), .pin16(IR3), .pin17(IR2), .pin18(IR1),
    .pin19(IR0), .pin20(1'b1));
  _74573 _74573_2 (
    .pin1(1'b0), .pin2(_74573_2_pin2), .pin3(_74573_2_pin3), .pin4(_74573_2_pin4), .pin5(_27c1024_1_p9),
    .pin6(_27c1024_1_p10), .pin7(_27c1024_1_p11), .pin8(_27c1024_1_p12), .pin9(_27c1024_1_p13), .pin10(1'b0),
    .pin11(clk), .pin12(_74573_2_pin12[3]), .pin13(_74573_2_pin12[2]), .pin14(_74573_2_pin12[1]),
    .pin15(_74573_2_pin12[0]), .pin16(_74573_2_pin16[3]), .pin17(_74573_2_pin16[2]),
    .pin18(_74573_2_pin16[1]), .pin19(_74573_2_pin16[0]), .pin20(1'b1));
  Seven_Seg_Hex seven_seg_hex_5 (.d({IR7, IR6, IR5, IR4}), .dp(1'b0));
  Seven_Seg_Hex seven_seg_hex_6 (.d({IR3, IR2, IR1, IR0}), .dp(1'b0));
  Seven_Seg_Hex seven_seg_hex_7 (.d(_74573_2_pin12), .dp(1'b0));
  Seven_Seg_Hex seven_seg_hex_8 (.d(_74573_2_pin16), .dp(1'b0));
  _2x157_Octal_Mux _2x157_octal_mux_1 (
    .B0(_74573_2_pin16[0]), .A_nB(in_16), .A0(reg_8_2_p2), .B1(_74573_2_pin16[1]), .A1(reg_8_2_p3),
    .B2(_74573_2_pin16[2]), .A2(reg_8_2_p4), .B3(_74573_2_pin16[3]), .A3(reg_8_2_p5), .B4(_74573_2_pin12[0]),
    .A4(reg_8_2_p6), .B5(_74573_2_pin12[1]), .A5(reg_8_2_p6), .B6(_74573_2_pin12[2]), .A6(reg_8_2_p7),
    .B7(_74573_2_pin12[3]), .A7(reg_8_2_p8), .D0(_2x157_octal_mux_1_d0), .D1(_2x157_octal_mux_1_d1),
    .D2(_2x157_octal_mux_1_d2), .D3(_2x157_octal_mux_1_d3), .D4(_2x157_octal_mux_1_d4),
    .D5(_2x157_octal_mux_1_d5), .D6(_2x157_octal_mux_1_d6), .D7(_2x157_octal_mux_1_d7), .VCC(1'b1),
    .GND(1'b0), .VSS(1'b0), .EN(1'b1));
  // Reg_8 reg_8_1: pin names not known; wires that end beside it: in_18, _2x157_octal_mux_1_d0, _2x157_octal_mux_1_d1, _2x157_octal_mux_1_d2, _2x157_octal_mux_1_d3, _2x157_octal_mux_1_d4, _2x157_octal_mux_1_d5, _2x157_octal_mux_1_d6, _2x157_octal_mux_1_d7, 1'b1, reg_8_1_p11, reg_8_1_p12, reg_8_1_p13, reg_8_1_p14, reg_8_1_p15, reg_8_1_p16, reg_8_1_p17, reg_8_1_p18, clk
  _2x157_Octal_Mux _2x157_octal_mux_2 (
    .B0(in_21), .A_nB(in_15), .A0(reg_8_1_p11), .B1(in_22), .A1(reg_8_1_p12), .B2(in_23), .A2(reg_8_1_p13),
    .B3(in_24), .A3(reg_8_1_p14), .B4(in_25), .A4(reg_8_1_p15), .B5(in_26), .A5(reg_8_1_p16), .B6(in_27),
    .A6(reg_8_1_p17), .B7(in_28), .A7(reg_8_1_p18), .D0(_2x157_octal_mux_2_d0), .D1(_2x157_octal_mux_2_d1),
    .D2(_2x157_octal_mux_2_d2), .D3(_2x157_octal_mux_2_d3), .D4(_2x157_octal_mux_2_d4),
    .D5(_2x157_octal_mux_2_d5), .D6(_2x157_octal_mux_2_d6), .D7(_2x157_octal_mux_2_d7), .VCC(1'b1),
    .GND(1'b0), .VSS(1'b0), .EN(1'b1));
  // ALU_8_40pin alu_8_40pin_1: pin names not known; wires that end beside it: in_29, alu_8_40pin_1_p3[0], alu_8_40pin_1_p3[1], alu_8_40pin_1_p3[2], alu_8_40pin_1_p3[3], alu_8_40pin_1_p9[0], alu_8_40pin_1_p9[1], alu_8_40pin_1_p9[2], alu_8_40pin_1_p9[3], 1'b0, _2x157_octal_mux_2_d0, _2x157_octal_mux_2_d1, _2x157_octal_mux_2_d2, _2x157_octal_mux_2_d3, _2x157_octal_mux_2_d4, 1'b1, in_12, in_11, in_10, in_9, in_13
  // Reg_8 reg_8_2: pin names not known; wires that end beside it: in_17, reg_8_2_p2, reg_8_2_p3, reg_8_2_p4, reg_8_2_p5, reg_8_2_p6, reg_8_2_p7, reg_8_2_p8, reg_8_2_p9, reg_8_2_p10, 1'b1, alu_8_40pin_1_p3[0], alu_8_40pin_1_p3[1], alu_8_40pin_1_p3[2], alu_8_40pin_1_p3[3], alu_8_40pin_1_p9[0], alu_8_40pin_1_p9[1], alu_8_40pin_1_p9[2], alu_8_40pin_1_p9[3], clk
  Seven_Seg_Hex seven_seg_hex_9 (.d(alu_8_40pin_1_p9), .dp(1'b0));
  Seven_Seg_Hex seven_seg_hex_10 (.d(alu_8_40pin_1_p3), .dp(1'b0));

  // Notes on the sheet:
  //   PROGRAM COUNTER
  //   ROM ADDRESS
  //   ROM
  //   INSTRUCTION
  //   DATA
  //   ADDRESS REG
  //   ACCUMULATOR
  //   Opcode
  //   00    0
  //   01    1
  //   02
  //   03  ~B
  //   04
  //   05
  //   06    A ^ B
  //   07
  //   08    A | B
  //   09
  //   0A
  //   0B
  //   0C     ADD A+B +C
  //   0D
  //   0E
  //   0F
  //   AND
  //   OR                1000
  //   XOR              0110      
  //   ADD      AL   1100
  //   SUB
  //   INV
endmodule
