// Digital circuit Aardvark_5.dig as structural Verilog
module Aardvark_5 (
  input  clk,
  input  in_2,
  input  in_3,
  input  in_4,
  input  in_5,
  input  in_6,
  input  in_7,
  input  in_8,
  input  in_9,
  input  in_10,
  input  in_11,
  input  in_12,
  input  in_13,
  input  in_14,
  input  in_15,
  input  in_16,
  input  in_17,
  input  HOLD_LD,
  input  CLR,
  input  nOE,
  input  LOAD,
  input  INC,
  input  DEP,
  input  in_24,
  input  in_25,
  input  in_26,
  input  in_27,
  input  in_28,
  input  HOLD_LD_2,
  input  CLR_2,
  input  nOE_2,
  input  CK
);

  wire _2x157_octal_mux_1_d0, _2x157_octal_mux_1_d1, _2x157_octal_mux_1_d2, _2x157_octal_mux_1_d3,
       _2x157_octal_mux_1_d4, _2x157_octal_mux_1_d5, _2x157_octal_mux_1_d6, _2x157_octal_mux_1_d7,
       _2x157_octal_mux_2_d0, _2x157_octal_mux_2_d1, _2x157_octal_mux_2_d2, _2x157_octal_mux_2_d3,
       _2x157_octal_mux_2_d4, _2x157_octal_mux_2_d5, _2x157_octal_mux_2_d6, _2x157_octal_mux_2_d7,
       _27c1024_1_p9, _27c1024_1_p10, _27c1024_1_p11, _27c1024_1_p12, _27c1024_1_p13, _27c1024_1_p15,
       _27c1024_1_p16, _27c1024_1_p17, _27c1024_1_p18, _27c1024_1_p19, _27c1024_1_p20, _27c1024_1_p21,
       _27c1024_1_p22, _74573_2_pin2, _74573_2_pin3, _74573_2_pin4, AC7, AL, alu_8_w_zero_1_p18, AR0, AR1,
       AR2, AR3, BUS0, BUS1, BUS2, BUS3, BUS4, BUS5, BUS6, BUS7, CLK2, Cout, diodebackward_13_out,
       diodebackward_24_out, EH, EL, IC1_pin2, IC1_pin3, IC1_pin8, IC1_pin11, IC2_pin2, IC2_pin3, IC2_pin8,
       IC2_pin11, IC3_pin2, IC3_pin3, IC3_pin8, IC3_pin11, IC4_pin1, IC4_pin2, IC4_pin3, IC4_pin8, IC4_pin11,
       IC16_pin10, IC18_pin9, IC18_pin10, IC18_pin11, IC18_pin12, IC18_pin13, IC18_pin14, IC18_pin15,
       IC19_pin7, IC19_pin9, IC19_pin10, IC19_pin11, IC19_pin12, IC19_pin13, IC19_pin14, IC19_pin15,
       IC20_2_pin16, IC20_2_pin17, IC20_2_pin18, IC20_pin7, IC20_pin9, IC20_pin12, IC20_pin13, IC20_pin14,
       IC20_pin15, IC22_pin7, IR0, IR1, IR2, IR3, IR4, IR5, IR6, IR7, IX, nAE, nBF, nDE, nIE, nJMP, nLD,
       nOE_t, nOL, not_1_out, not_2_out, nPH, nPL, nWE, nXL, nYL, pullup_1_out, pullup_2_out, pullup_3_out,
       pullup_4_out, pullup_9_out, reg_8_1_p11, reg_8_1_p12, reg_8_1_p13, reg_8_1_p14, reg_8_1_p15,
       reg_8_1_p16, reg_8_1_p17, reg_8_1_p18, reg_8_2_p2, reg_8_2_p3, reg_8_2_p4, reg_8_2_p5, reg_8_2_p6,
       reg_8_2_p7, reg_8_2_p8;
  wire [3:0] _74573_2_pin12, _74573_2_pin16, alu_8_w_zero_1_p3, alu_8_w_zero_1_p10, IC13_pin6, IC13_pin12,
       IC14_pin6, IC14_pin14, IC15_pin11, IC16_pin14, pc1634_1_p14, pc1634_1_p19, pc1634_1_p23, undriven;

  _74153 IC22 (
    .pin1(nJMP), .pin2(Cout), .pin3(1'b0), .pin4(IR4), .pin5(IR3), .pin6(IR2), .pin7(IC22_pin7), .pin8(1'b0),
    .pin10(1'b1), .pin11(1'b1), .pin12(1'b1), .pin13(1'b1), .pin14(AC7), .pin15(1'b1), .pin16(1'b1));  // open: pin9
  _74139 IC21 (
    .pin1(1'b0), .pin2(IR0), .pin3(IR1), .pin4(nDE), .pin5(nOE_t), .pin6(nAE), .pin7(nIE), .pin8(1'b0),
    .pin12(nBF), .pin13(IR2), .pin14(IR3), .pin15(IR4), .pin16(1'b1));  // open: pin9, pin10, pin11
  _74138 IC20 (
    .pin1(IR2), .pin2(IR3), .pin3(IR4), .pin4(IR7), .pin5(IR7), .pin6(1'b1), .pin7(IC20_pin7), .pin8(1'b0),
    .pin9(IC20_pin9), .pin10(nYL), .pin11(nXL), .pin12(IC20_pin12), .pin13(IC20_pin13), .pin14(IC20_pin14),
    .pin15(IC20_pin15), .pin16(1'b1));
  _74138 IC18 (
    .pin1(IR4), .pin2(IR5), .pin3(IR6), .pin4(IR7), .pin5(1'b0), .pin6(1'b1), .pin7(nJMP), .pin8(1'b0),
    .pin9(IC18_pin9), .pin10(IC18_pin10), .pin11(IC18_pin11), .pin12(IC18_pin12), .pin13(IC18_pin13),
    .pin14(IC18_pin14), .pin15(IC18_pin15), .pin16(1'b1));
  _74138 IC19 (
    .pin1(IR4), .pin2(IR5), .pin3(IR6), .pin4(1'b0), .pin5(1'b0), .pin6(IR7), .pin7(IC19_pin7), .pin8(1'b0),
    .pin9(IC19_pin9), .pin10(IC19_pin10), .pin11(IC19_pin11), .pin12(IC19_pin12), .pin13(IC19_pin13),
    .pin14(IC19_pin14), .pin15(IC19_pin15), .pin16(1'b1));
  not not_1 (not_1_out, IC22_pin7);
  PullUp pullup_1 (.out(pullup_1_out));
  DiodeBackward diodebackward_1 (.in(IC20_pin15), .out(pullup_1_out));
  DiodeBackward diodebackward_2 (.in(IC20_pin14), .out(pullup_1_out));
  DiodeBackward diodebackward_3 (.in(IC20_pin13), .out(pullup_1_out));
  DiodeBackward diodebackward_4 (.in(IC20_pin12), .out(pullup_1_out));
  PullUp pullup_2 (.out(pullup_2_out));
  DiodeBackward diodebackward_5 (.in(IR6), .out(pullup_2_out));
  DiodeBackward diodebackward_6 (.in(nJMP), .out(pullup_2_out));
  // PC1634 pc1634_1: pin names not known; wires that end beside it: 1'b0, 1'b0, 1'b0, 1'b0, 1'b0, 1'b0, 1'b0, clk, 1'b1, 1'b1, pc1634_1_p14[0], pc1634_1_p14[1], pc1634_1_p14[2], pc1634_1_p14[3], pc1634_1_p19[0], 1'b0, pc1634_1_p19[1], pc1634_1_p19[2], pc1634_1_p19[3], pc1634_1_p23[0], pc1634_1_p23[1], pc1634_1_p23[2], pc1634_1_p23[3], in_6, in_7
  PullUp pullup_3 (.out(pullup_3_out));
  DiodeBackward diodebackward_7 (.in(IC20_pin14), .out(EL));
  DiodeBackward diodebackward_8 (.in(IC20_pin12), .out(EL));
  DiodeBackward diodebackward_9 (.in(IC20_pin9), .out(pullup_3_out));
  DiodeBackward diodebackward_10 (.in(IC20_pin7), .out(pullup_3_out));
  DiodeBackward diodebackward_11 (.in(IC20_pin7), .out(EL));
  PullUp pullup_4 (.out(pullup_4_out));
  DiodeBackward diodebackward_12 (.in(IC18_pin15), .out(pullup_4_out));
  DiodeBackward diodebackward_13 (.in(IC18_pin15), .out(diodebackward_13_out));
  DiodeBackward diodebackward_14 (.in(IC18_pin14), .out(pullup_4_out));
  DiodeBackward diodebackward_15 (.in(IC18_pin13), .out(pullup_4_out));
  DiodeBackward diodebackward_16 (.in(IC18_pin13), .out(diodebackward_13_out));
  DiodeBackward diodebackward_17 (.in(IC18_pin12), .out(diodebackward_13_out));
  DiodeBackward diodebackward_18 (.in(IC18_pin11), .out(pullup_4_out));
  DiodeBackward diodebackward_19 (.in(IC18_pin11), .out(diodebackward_13_out));
  DiodeBackward diodebackward_20 (.in(IC18_pin9), .out(diodebackward_13_out));
  Seven_Seg_Hex seven_seg_hex_1 (.d(pc1634_1_p23), .dp(1'b0));
  PullUp pullup_5 (.out(EL));
  DiodeBackward diodebackward_21 (.in(IC20_pin13), .out(EH));
  DiodeBackward diodebackward_22 (.in(IC20_pin12), .out(EH));
  DiodeBackward diodebackward_23 (.in(IC20_pin7), .out(EH));
  PullUp pullup_6 (.out(diodebackward_13_out));
  DiodeBackward diodebackward_24 (.in(IC18_pin13), .out(diodebackward_24_out));
  DiodeBackward diodebackward_25 (.in(IC18_pin12), .out(diodebackward_24_out));
  DiodeBackward diodebackward_26 (.in(IC18_pin10), .out(diodebackward_24_out));
  Seven_Seg_Hex seven_seg_hex_2 (.d(pc1634_1_p19), .dp(1'b0));
  or or_1 (nPH, nJMP, nBF);
  PullUp pullup_7 (.out(EH));
  PullUp pullup_8 (.out(diodebackward_24_out));
  PullUp pullup_9 (.out(pullup_9_out));
  DiodeBackward diodebackward_27 (.in(IC18_pin10), .out(pullup_9_out));
  DiodeBackward diodebackward_28 (.in(IC18_pin9), .out(pullup_9_out));
  Seven_Seg_Hex seven_seg_hex_3 (.d(pc1634_1_p14), .dp(1'b0));
  Seven_Seg_Hex seven_seg_hex_4 (.d(undriven), .dp(1'b0));
  _74540 IC20_2 (
    .pin1(1'b0), .pin2(1'b0), .pin3(1'b0), .pin4(1'b0), .pin5(pullup_9_out), .pin6(diodebackward_24_out),
    .pin7(diodebackward_13_out), .pin8(pullup_4_out), .pin9(pullup_2_out), .pin10(1'b0), .pin11(AL),
    .pin12(AR3), .pin13(AR2), .pin14(AR1), .pin15(AR0), .pin16(IC20_2_pin16), .pin17(IC20_2_pin17),
    .pin18(IC20_2_pin18), .pin19(1'b0), .pin20(1'b1));
  DiodeBackward diodebackward_29 (.in(not_1_out), .out(nPL));
  DiodeBackward diodebackward_30 (.in(nPH), .out(nPL));
  PullUp pullup_10 (.out(nPL));
  not not_2 (not_2_out, IC18_pin9);
  // _27C1024 _27c1024_1: pin names not known; wires that end beside it: pc1634_1_p19[1], pc1634_1_p19[2], pc1634_1_p19[3], pc1634_1_p23[0], pc1634_1_p23[1], pc1634_1_p23[2], pc1634_1_p23[3], 1'b1, _27c1024_1_p9, _27c1024_1_p10, _27c1024_1_p11, _27c1024_1_p12, _27c1024_1_p13, 1'b0, _27c1024_1_p15, _27c1024_1_p16, _27c1024_1_p17, _27c1024_1_p18, _27c1024_1_p19, _27c1024_1_p20, _27c1024_1_p21, _27c1024_1_p22, 1'b0, 1'b1
  not not_3 (IX, IC20_pin7);
  or or_2 (nOL, pullup_3_out, not_2_out);
  or or_3 (nLD, pullup_1_out, not_2_out);
  or or_4 (nWE, clk, IC18_pin9);
  _74573 _74573_1 (
    .pin1(1'b0), .pin2(_27c1024_1_p15), .pin3(_27c1024_1_p16), .pin4(_27c1024_1_p17), .pin5(_27c1024_1_p18),
    .pin6(_27c1024_1_p19), .pin7(_27c1024_1_p20), .pin8(_27c1024_1_p21), .pin9(_27c1024_1_p22), .pin10(1'b0),
    .pin11(clk), .pin12(IR7), .pin13(IR6), .pin14(IR5), .pin15(IR4), .pin16(IR3), .pin17(IR2), .pin18(IR1),
    .pin19(IR0), .pin20(1'b1));
  _74573 _74573_2 (
    .pin1(1'b0), .pin2(_74573_2_pin2), .pin3(_74573_2_pin3), .pin4(_74573_2_pin4), .pin5(_27c1024_1_p9),
    .pin6(_27c1024_1_p10), .pin7(_27c1024_1_p11), .pin8(_27c1024_1_p12), .pin9(_27c1024_1_p13), .pin10(1'b0),
    .pin11(clk), .pin12(_74573_2_pin12[3]), .pin13(_74573_2_pin12[2]), .pin14(_74573_2_pin12[1]),
    .pin15(_74573_2_pin12[0]), .pin16(_74573_2_pin16[3]), .pin17(_74573_2_pin16[2]),
    .pin18(_74573_2_pin16[1]), .pin19(_74573_2_pin16[0]), .pin20(1'b1));
  Seven_Seg_Hex seven_seg_hex_5 (.d({IR7, IR6, IR5, IR4}), .dp(1'b0));
  Seven_Seg_Hex seven_seg_hex_6 (.d({IR3, IR2, IR1, IR0}), .dp(1'b0));
  Seven_Seg_Hex seven_seg_hex_7 (.d(_74573_2_pin12), .dp(1'b0));
  Seven_Seg_Hex seven_seg_hex_8 (.d(_74573_2_pin16), .dp(1'b0));
  _2x157_Octal_Mux _2x157_octal_mux_1 (
    .B0(_74573_2_pin16[0]), .A_nB(in_3), .A0(reg_8_2_p2), .B1(_74573_2_pin16[1]), .A1(reg_8_2_p3),
    .B2(_74573_2_pin16[2]), .A2(reg_8_2_p4), .B3(_74573_2_pin16[3]), .A3(reg_8_2_p5), .B4(_74573_2_pin12[0]),
    .A4(reg_8_2_p6), .B5(_74573_2_pin12[1]), .A5(reg_8_2_p6), .B6(_74573_2_pin12[2]), .A6(reg_8_2_p7),
    .B7(_74573_2_pin12[3]), .A7(reg_8_2_p8), .D0(_2x157_octal_mux_1_d0), .D1(_2x157_octal_mux_1_d1),
    .D2(_2x157_octal_mux_1_d2), .D3(_2x157_octal_mux_1_d3), .D4(_2x157_octal_mux_1_d4),
    .D5(_2x157_octal_mux_1_d5), .D6(_2x157_octal_mux_1_d6), .D7(_2x157_octal_mux_1_d7), .VCC(1'b1),
    .GND(1'b0), .VSS(1'b0), .EN(1'b1));
  // Reg_8 reg_8_1: pin names not known; wires that end beside it: in_5, _2x157_octal_mux_1_d0, _2x157_octal_mux_1_d1, _2x157_octal_mux_1_d2, _2x157_octal_mux_1_d3, _2x157_octal_mux_1_d4, _2x157_octal_mux_1_d5, _2x157_octal_mux_1_d6, _2x157_octal_mux_1_d7, 1'b1, reg_8_1_p11, reg_8_1_p12, reg_8_1_p13, reg_8_1_p14, reg_8_1_p15, reg_8_1_p16, reg_8_1_p17, reg_8_1_p18, clk
  _2x157_Octal_Mux _2x157_octal_mux_2 (
    .B0(in_8), .A_nB(in_2), .A0(reg_8_1_p11), .B1(in_9), .A1(reg_8_1_p12), .B2(in_10), .A2(reg_8_1_p13),
    .B3(in_11), .A3(reg_8_1_p14), .B4(in_12), .A4(reg_8_1_p15), .B5(in_13), .A5(reg_8_1_p16), .B6(in_14),
    .A6(reg_8_1_p17), .B7(in_15), .A7(reg_8_1_p18), .D0(_2x157_octal_mux_2_d0), .D1(_2x157_octal_mux_2_d1),
    .D2(_2x157_octal_mux_2_d2), .D3(_2x157_octal_mux_2_d3), .D4(_2x157_octal_mux_2_d4),
    .D5(_2x157_octal_mux_2_d5), .D6(_2x157_octal_mux_2_d6), .D7(_2x157_octal_mux_2_d7), .VCC(1'b1),
    .GND(1'b0), .VSS(1'b0), .EN(1'b1));
  // ALU_8_W_Zero alu_8_w_zero_1: pin names not known; wires that end beside it: in_16, AR0, alu_8_w_zero_1_p3[0], alu_8_w_zero_1_p3[1], alu_8_w_zero_1_p3[2], alu_8_w_zero_1_p3[3], alu_8_w_zero_1_p10[0], alu_8_w_zero_1_p10[1], alu_8_w_zero_1_p10[2], alu_8_w_zero_1_p10[3], 1'b0, _2x157_octal_mux_2_d0, _2x157_octal_mux_2_d1, _2x157_octal_mux_2_d2, _2x157_octal_mux_2_d3, _2x157_octal_mux_2_d4, 1'b1, alu_8_w_zero_1_p18, in_17, AR3, AR2, AR1, AR0, AL
  LED led_1 (.in(alu_8_w_zero_1_p18));
  // Reg_8 reg_8_2: pin names not known; wires that end beside it: in_4, reg_8_2_p2, reg_8_2_p3, reg_8_2_p4, reg_8_2_p5, reg_8_2_p6, reg_8_2_p7, reg_8_2_p8, AC7, 1'b1, alu_8_w_zero_1_p3[0], alu_8_w_zero_1_p3[1], alu_8_w_zero_1_p3[2], alu_8_w_zero_1_p3[3], alu_8_w_zero_1_p10[0], alu_8_w_zero_1_p10[1], alu_8_w_zero_1_p10[2], alu_8_w_zero_1_p10[3], clk
  Delay #(.delayTime(2)) delay_1 (.in(clk), .out(CLK2));
  Seven_Seg_Hex seven_seg_hex_9 (.d(alu_8_w_zero_1_p10), .dp(1'b0));
  _7474 IC4 (
    .pin1(IC4_pin1), .pin2(IC4_pin2), .pin3(IC4_pin3), .pin4(1'b1), .pin5(IC14_pin14[3]), .pin6(IC4_pin2),
    .pin7(1'b0), .pin8(IC4_pin8), .pin9(IC14_pin14[2]), .pin10(1'b1), .pin11(IC4_pin11), .pin12(IC4_pin8),
    .pin13(IC4_pin1), .pin14(1'b1));
  Seven_Seg_Hex seven_seg_hex_10 (.d(alu_8_w_zero_1_p3), .dp(1'b0));
  Button #(.activeLow("true")) CLEAR (.out(IC4_pin1));
  _74173 IC14 (
    .pin1(nOE), .pin2(nOE), .pin3(IC14_pin6[0]), .pin4(IC14_pin6[1]), .pin5(IC14_pin6[2]),
    .pin6(IC14_pin6[3]), .pin7(DEP), .pin8(1'b0), .pin9(HOLD_LD), .pin10(HOLD_LD), .pin11(IC14_pin14[3]),
    .pin12(IC14_pin14[2]), .pin13(IC14_pin14[1]), .pin14(IC14_pin14[0]), .pin15(CLR), .pin16(1'b1));
  _74173 IC13 (
    .pin1(nOE), .pin2(nOE), .pin3(IC13_pin6[0]), .pin4(IC13_pin6[1]), .pin5(IC13_pin6[2]),
    .pin6(IC13_pin6[3]), .pin7(DEP), .pin8(1'b0), .pin9(HOLD_LD), .pin10(HOLD_LD), .pin11(IC13_pin12[3]),
    .pin12(IC13_pin12[2]), .pin13(IC13_pin12[1]), .pin14(IC13_pin12[0]), .pin15(CLR), .pin16(1'b1));
  _7474 IC3 (
    .pin1(IC4_pin1), .pin2(IC3_pin2), .pin3(IC3_pin3), .pin4(1'b1), .pin5(IC14_pin14[0]), .pin6(IC3_pin2),
    .pin7(1'b0), .pin8(IC3_pin8), .pin9(IC14_pin14[1]), .pin10(1'b1), .pin11(IC3_pin11), .pin12(IC3_pin8),
    .pin13(IC4_pin1), .pin14(1'b1));
  LED led_2 (.in(IC14_pin14[3]));
  Button button_1 (.out(IC4_pin3));
  LED led_3 (.in(IC14_pin14[2]));
  Button button_2 (.out(IC4_pin11));
  Seven_Seg_Hex seven_seg_hex_11 (.d(IC14_pin6), .dp(1'b0));
  Seven_Seg_Hex seven_seg_hex_12 (.d(IC13_pin6), .dp(1'b0));
  LED led_4 (.in(IC14_pin14[1]));
  Button button_3 (.out(IC3_pin11));
  LED led_5 (.in(IC14_pin14[0]));
  Button button_4 (.out(IC3_pin3));
  _74163 IC16 (
    .pin1(1'b1), .pin2(DEP), .pin3(IC14_pin6[0]), .pin4(IC14_pin6[1]), .pin5(IC14_pin6[2]),
    .pin6(IC14_pin6[3]), .pin7(1'b1), .pin8(1'b0), .pin9(LOAD), .pin10(IC16_pin10), .pin11(IC16_pin14[3]),
    .pin12(IC16_pin14[2]), .pin13(IC16_pin14[1]), .pin14(IC16_pin14[0]), .pin16(1'b1));  // open: pin15
  _7474 IC2 (
    .pin1(IC4_pin1), .pin2(IC2_pin2), .pin3(IC2_pin3), .pin4(1'b1), .pin5(IC13_pin12[3]), .pin6(IC2_pin2),
    .pin7(1'b0), .pin8(IC2_pin8), .pin9(IC13_pin12[2]), .pin10(1'b1), .pin11(IC2_pin11), .pin12(IC2_pin8),
    .pin13(IC4_pin1), .pin14(1'b1));
  LED led_6 (.in(IC13_pin12[3]));
  Button button_5 (.out(IC2_pin3));
  LED led_7 (.in(IC13_pin12[2]));
  Button button_6 (.out(IC2_pin11));
  Seven_Seg_Hex seven_seg_hex_13 (.d(IC16_pin14), .dp(1'b0));
  LED led_8 (.in(IC13_pin12[1]));
  _7474 IC1 (
    .pin1(IC4_pin1), .pin2(IC1_pin2), .pin3(IC1_pin3), .pin4(1'b1), .pin5(IC13_pin12[0]), .pin6(IC1_pin2),
    .pin7(1'b0), .pin8(IC1_pin8), .pin9(IC13_pin12[1]), .pin10(1'b1), .pin11(IC1_pin11), .pin12(IC1_pin8),
    .pin13(IC4_pin1), .pin14(1'b1));
  Button button_7 (.out(IC1_pin11));
  Seven_Seg_Hex seven_seg_hex_14 (.d(IC15_pin11), .dp(1'b0));
  Seven_Seg_Hex seven_seg_hex_15 (.d(IC14_pin14), .dp(1'b0));
  LED led_9 (.in(IC13_pin12[0]));
  Button button_8 (.out(IC1_pin3));
  _74163 IC15 (
    .pin1(1'b1), .pin2(DEP), .pin3(IC13_pin6[0]), .pin4(IC13_pin6[1]), .pin5(IC13_pin6[2]),
    .pin6(IC13_pin6[3]), .pin7(1'b1), .pin8(1'b0), .pin9(LOAD), .pin10(1'b1), .pin11(IC15_pin11[3]),
    .pin12(IC15_pin11[2]), .pin13(IC15_pin11[1]), .pin14(IC15_pin11[0]), .pin15(IC16_pin10), .pin16(1'b1));
  Seven_Seg_Hex seven_seg_hex_16 (.d(IC13_pin12), .dp(1'b0));
  // A623308A IC17: pin names not known; wires that end beside it: in_24, IC16_pin14[3], IC16_pin14[2], IC16_pin14[1], IC16_pin14[0], IC15_pin11[3], IC15_pin11[2], IC15_pin11[1], IC15_pin11[0], BUS0, BUS1, BUS2, 1'b0, 1'b1, nWE, in_25, in_26, in_27, nOE_t, in_28, 1'b0, BUS7
  _74173 IC6 (
    .pin1(nOE_2), .pin2(nOE_2), .pin3(BUS4), .pin4(BUS5), .pin5(BUS6), .pin6(BUS7), .pin7(CK), .pin8(1'b0),
    .pin9(HOLD_LD_2), .pin10(HOLD_LD_2), .pin11(IC14_pin14[3]), .pin12(IC14_pin14[2]), .pin13(IC14_pin14[1]),
    .pin14(IC14_pin14[0]), .pin15(CLR_2), .pin16(1'b1));
  _74173 IC5 (
    .pin1(nOE_2), .pin2(nOE_2), .pin3(BUS0), .pin4(BUS1), .pin5(BUS2), .pin6(BUS3), .pin7(CK), .pin8(1'b0),
    .pin9(HOLD_LD_2), .pin10(HOLD_LD_2), .pin11(IC13_pin12[3]), .pin12(IC13_pin12[2]), .pin13(IC13_pin12[1]),
    .pin14(IC13_pin12[0]), .pin15(CLR_2), .pin16(1'b1));
  Seven_Seg_Hex seven_seg_hex_17 (.d({BUS7, BUS6, BUS5, BUS4}), .dp(1'b0));
  Seven_Seg_Hex seven_seg_hex_18 (.d({BUS3, BUS2, BUS1, BUS0}), .dp(1'b0));

  // Other names for the same wires on the sheet: CLK1 = clk

  // Notes on the sheet:
  //   clk: Hz: 10
  //   CONTROL UNIT
  //   Data Source Selector
  //   PROGRAM COUNTER
  //   ROM ADDRESS
  //   16-bit Jump Detector
  //   LOAD
  //   AND
  //   XOR
  //   ADD
  //   SUB
  //   STORE
  //   JMP
  //   OR
  //   ~W
  //   ROM
  //   INST 8
  //   INST 9
  //   INST A
  //   INST B
  //   INST C
  //   INST D
  //   INST E
  //   INST F
  //   INSTRUCTION
  //   DATA
  //   ADDRESS REG
  //   ACCUMULATOR
  //   Opcode
  //   00    0
  //   01    1
  //   02
  //   03  ~B
  //   04
  //   05
  //   06    A ^ B
  //   07
  //   08    A | B
  //   09
  //   0A
  //   0B
  //   0C     ADD A+B +C
  //   0D
  //   0E
  //   0F
  //   AND
  //   OR                1000
  //   XOR              0110      
  //   ADD      AL   1100
  //   SUB
  //   INV
  //   ADDRESS
endmodule
