// Digital circuit Discrete_control_2.dig as structural Verilog
module Discrete_control_2 (
  input  D0,
  input  D1,
  input  D2,
  input  D3,
  input  D4,
  input  D5,
  input  D6,
  input  D7,
  input  C,
  input  S0,
  input  D,
  input  A,
  input  B,
  input  S1,
  input  EN,
  input  S0_2,
  input  S1_2,
  input  EN_2,
  input  clk,
  input  clk_2,
  output PHI0,
  output PHI1
);

  wire AL, AR0, AR1, AR2, AR3, diodebackward_5_out, EH, EL, IC20_pin7, IC20_pin9, IC20_pin12, IC20_pin13,
       IC20_pin14, IC20_pin15, IC22_pin7, IR0, IR1, IR2, IR3, IR4, IR5, IR6, IR7, IX, nAE, nand_1_out,
       nand_2_out, nand_3_out, nand_4_out, nand_5_out, nand_6_out, nand_7_out, nand_8_out, nand_9_out,
       nand_10_out, nand_11_out, nand_12_out, nand_13_out, nand_14_out, nand_15_out, nand_16_out,
       nand_17_out, nand_18_out, nand_19_out, nand_20_out, nand_21_out, nand_22_out, nand_23_out,
       nand_24_out, nand_25_out, nand_26_out, nand_27_out, nand_28_out, nand_29_out, nand_30_out,
       nand_31_out, nand_32_out, nand_33_out, nand_34_out, nand_35_out, nand_36_out, nand_37_out,
       nand_38_out, nand_39_out, nand_40_out, nand_41_out, nand_42_out, nand_43_out, nand_44_out,
       nand_45_out, nand_46_out, nand_47_out, nand_48_out, nand_49_out, nand_50_out, nand_51_out,
       nand_52_out, nand_53_out, nand_54_out, nand_55_out, nand_56_out, nand_57_out, nand_58_out,
       nand_59_out, nand_62_out, nand_63_out, nand_64_out, nand_65_out, nand_74_out, nand_75_out, nBF, nDE,
       nIE, nJMP, nLD, nOE, nOL, not_1_out, nPH, nPL, nW, nWE, nXL, nYL, pullup_1_out, pullup_6_out,
       pullup_7_out, pullup_8_out, pullup_9_out, pullup_10_out, W;

  nand nand_1 (nand_1_out, S0, S0);
  nand nand_2 (nand_2_out, S1, S1);
  nand nand_3 (nand_3_out, S0_2, S0_2);
  nand nand_4 (nand_4_out, S1_2, S1_2);
  nand nand_5 (nand_5_out, D, S0);
  nand nand_6 (nand_6_out, C, nand_1_out);
  nand nand_7 (nand_7_out, B, S0);
  nand nand_8 (nand_8_out, A, nand_1_out);
  nand nand_9 (nand_9_out, nand_3_out, nand_4_out);
  nand nand_10 (nand_10_out, S0_2, nand_4_out);
  nand nand_11 (nand_11_out, nand_3_out, S1_2);
  nand nand_12 (nand_12_out, S0_2, S1_2);
  nand nand_13 (nand_13_out, nand_5_out, nand_6_out);
  nand nand_14 (nand_14_out, nand_7_out, nand_8_out);
  nand nand_15 (nand_15_out, nand_9_out, nand_9_out);
  nand nand_16 (nand_16_out, nand_10_out, nand_10_out);
  nand nand_17 (nand_17_out, nand_11_out, nand_11_out);
  nand nand_18 (nand_18_out, nand_12_out, nand_12_out);
  nand nand_19 (nand_19_out, S1, nand_13_out);
  nand nand_20 (nand_20_out, nand_14_out, nand_2_out);
  nand nand_21 (nand_21_out, nand_15_out, EN_2);
  nand nand_22 (nand_22_out, nand_16_out, EN_2);
  nand nand_23 (nand_23_out, nand_17_out, EN_2);
  nand nand_24 (nand_24_out, nand_18_out, EN_2);
  nand nand_25 (nand_25_out, nand_19_out, nand_20_out);
  LED led_1 (.in(nand_21_out));
  LED led_2 (.in(nand_22_out));
  LED led_3 (.in(nand_23_out));
  LED led_4 (.in(nand_24_out));
  nand nand_26 (nand_26_out, nand_25_out, EN);
  nand nand_27 (nand_27_out, nand_26_out, nand_26_out);
  LED led_5 (.in(nand_27_out));
  _74153 IC22 (
    .pin1(nJMP), .pin2(1'b0), .pin3(1'b0), .pin4(IR4), .pin5(IR3), .pin6(IR2), .pin7(IC22_pin7), .pin8(1'b0),
    .pin10(1'b1), .pin11(1'b1), .pin12(1'b1), .pin13(1'b1), .pin14(1'b0), .pin15(1'b1), .pin16(1'b1));  // open: pin9
  _74139 IC21 (
    .pin1(1'b0), .pin2(IR0), .pin3(IR1), .pin4(nDE), .pin5(nOE), .pin6(nAE), .pin7(nIE), .pin8(1'b0),
    .pin12(nBF), .pin13(IR2), .pin14(IR3), .pin15(IR4), .pin16(1'b1));  // open: pin9, pin10, pin11
  _74138 IC20 (
    .pin1(IR2), .pin2(IR3), .pin3(IR4), .pin4(IR7), .pin5(1'b0), .pin6(1'b1), .pin7(IC20_pin7), .pin8(1'b0),
    .pin9(IC20_pin9), .pin10(nYL), .pin11(nXL), .pin12(IC20_pin12), .pin13(IC20_pin13), .pin14(IC20_pin14),
    .pin15(IC20_pin15), .pin16(1'b1));
  not not_1 (not_1_out, IC22_pin7);
  PullUp pullup_1 (.out(pullup_1_out));
  DiodeBackward diodebackward_1 (.in(IC20_pin15), .out(pullup_1_out));
  DiodeBackward diodebackward_2 (.in(IC20_pin14), .out(pullup_1_out));
  DiodeBackward diodebackward_3 (.in(IC20_pin13), .out(pullup_1_out));
  DiodeBackward diodebackward_4 (.in(IC20_pin12), .out(pullup_1_out));
  DiodeBackward diodebackward_5 (.in(IC20_pin9), .out(diodebackward_5_out));
  DiodeBackward diodebackward_6 (.in(IC20_pin7), .out(diodebackward_5_out));
  PullUp pullup_2 (.out(diodebackward_5_out));
  DiodeBackward diodebackward_7 (.in(IC20_pin14), .out(EL));
  DiodeBackward diodebackward_8 (.in(IC20_pin12), .out(EL));
  DiodeBackward diodebackward_9 (.in(IC20_pin7), .out(EL));
  or or_1 (nPH, nJMP, nBF);
  PullUp pullup_3 (.out(EL));
  PullUp pullup_4 (.out(EH));
  DiodeBackward diodebackward_10 (.in(IC20_pin13), .out(EH));
  DiodeBackward diodebackward_11 (.in(IC20_pin12), .out(EH));
  DiodeBackward diodebackward_12 (.in(IC20_pin7), .out(EH));
  DiodeBackward diodebackward_13 (.in(not_1_out), .out(nPL));
  DiodeBackward diodebackward_14 (.in(nPH), .out(nPL));
  PullUp pullup_5 (.out(nPL));
  not not_2 (IX, IC20_pin7);
  or or_2 (nOL, diodebackward_5_out, nW);
  or or_3 (nLD, pullup_1_out, nW);
  or or_4 (nWE, clk, W);
  _74573 _74573_1 (
    .pin1(1'b0), .pin2(D0), .pin3(D1), .pin4(D2), .pin5(D3), .pin6(D4), .pin7(D5), .pin8(D6), .pin9(D7),
    .pin10(1'b0), .pin11(clk), .pin12(IR7), .pin13(IR6), .pin14(IR5), .pin15(IR4), .pin16(IR3), .pin17(IR2),
    .pin18(IR1), .pin19(IR0), .pin20(1'b1));
  nand nand_28 (nand_28_out, IR4, IR4);
  nand nand_29 (nand_29_out, IR5, IR5);
  nand nand_30 (nand_30_out, IR6, IR6);
  nand nand_31 (nand_31_out, clk_2, clk_2);
  nand nand_32 (nand_32_out, nand_28_out, nand_29_out);
  nand nand_33 (nand_33_out, IR4, nand_29_out);
  nand nand_34 (nand_34_out, nand_28_out, IR5);
  nand nand_35 (nand_35_out, IR4, IR5);
  nand nand_36 (nand_36_out, nand_28_out, nand_29_out);
  nand nand_37 (nand_37_out, IR4, nand_29_out);
  nand nand_38 (nand_38_out, nand_28_out, IR5);
  nand nand_39 (nand_39_out, IR4, IR5);
  nand nand_40 (nand_40_out, nand_31_out, nand_31_out);
  nand nand_41 (nand_41_out, PHI1, PHI1);
  nand nand_42 (nand_42_out, PHI0, PHI0);
  nand nand_43 (nand_43_out, clk_2, clk_2);
  nand nand_44 (nand_44_out, nand_32_out, nand_32_out);
  nand nand_45 (nand_45_out, nand_33_out, nand_33_out);
  nand nand_46 (nand_46_out, nand_34_out, nand_34_out);
  nand nand_47 (nand_47_out, nand_35_out, nand_35_out);
  nand nand_48 (nand_48_out, nand_36_out, nand_36_out);
  nand nand_49 (nand_49_out, nand_37_out, nand_37_out);
  nand nand_50 (nand_50_out, nand_38_out, nand_38_out);
  nand nand_51 (nand_51_out, nand_39_out, nand_39_out);
  nand nand_52 (nand_52_out, nand_40_out, nand_41_out);
  nand nand_53 (nand_53_out, nand_42_out, nand_43_out);
  nand nand_54 (nand_54_out, nand_44_out, nand_30_out);
  nand nand_55 (nand_55_out, nand_45_out, nand_30_out);
  nand nand_56 (nand_56_out, nand_46_out, nand_30_out);
  nand nand_57 (nand_57_out, nand_47_out, nand_30_out);
  nand nand_58 (nand_58_out, nand_48_out, IR6);
  nand nand_59 (nand_59_out, nand_49_out, IR6);
  nand nand_60 (nW, nand_50_out, IR6);
  nand nand_61 (nJMP, nand_51_out, IR6);
  nand nand_62 (nand_62_out, nand_52_out, nand_52_out);
  nand nand_63 (nand_63_out, nand_53_out, nand_53_out);
  nand nand_64 (nand_64_out, nand_62_out, nand_62_out);
  nand nand_65 (nand_65_out, nand_63_out, nand_63_out);
  PullUp pullup_6 (.out(pullup_6_out));
  DiodeBackward diodebackward_15 (.in(nJMP), .out(pullup_6_out));
  DiodeBackward diodebackward_16 (.in(IR6), .out(pullup_6_out));
  nand nand_66 (AL, pullup_6_out, pullup_6_out);
  PullUp pullup_7 (.out(pullup_7_out));
  DiodeBackward diodebackward_17 (.in(nand_54_out), .out(pullup_7_out));
  DiodeBackward diodebackward_18 (.in(nand_55_out), .out(pullup_7_out));
  DiodeBackward diodebackward_19 (.in(nand_56_out), .out(pullup_7_out));
  DiodeBackward diodebackward_20 (.in(nand_58_out), .out(pullup_7_out));
  nand nand_67 (AR3, pullup_7_out, pullup_7_out);
  nand nand_68 (PHI0, nand_64_out, nand_64_out);
  nand nand_69 (PHI1, nand_65_out, nand_65_out);
  PullUp pullup_8 (.out(pullup_8_out));
  DiodeBackward diodebackward_21 (.in(nand_54_out), .out(pullup_8_out));
  DiodeBackward diodebackward_22 (.in(nand_56_out), .out(pullup_8_out));
  DiodeBackward diodebackward_23 (.in(nand_57_out), .out(pullup_8_out));
  DiodeBackward diodebackward_24 (.in(nand_58_out), .out(pullup_8_out));
  DiodeBackward diodebackward_25 (.in(nW), .out(pullup_8_out));
  nand nand_70 (AR2, pullup_8_out, pullup_8_out);
  PullUp pullup_9 (.out(pullup_9_out));
  DiodeBackward diodebackward_26 (.in(nand_56_out), .out(pullup_9_out));
  DiodeBackward diodebackward_27 (.in(nand_57_out), .out(pullup_9_out));
  DiodeBackward diodebackward_28 (.in(nand_59_out), .out(pullup_9_out));
  nand nand_71 (AR1, pullup_9_out, pullup_9_out);
  PullUp pullup_10 (.out(pullup_10_out));
  DiodeBackward diodebackward_29 (.in(nand_59_out), .out(pullup_10_out));
  DiodeBackward diodebackward_30 (.in(nW), .out(pullup_10_out));
  nand nand_72 (AR0, pullup_10_out, pullup_10_out);
  nand nand_73 (W, nW, nW);
  nand nand_74 (nand_74_out, 1'b0, 1'b0);
  LED led_6 (.in(nand_54_out));
  LED led_7 (.in(nand_55_out));
  LED led_8 (.in(nand_56_out));
  LED led_9 (.in(nand_57_out));
  LED led_10 (.in(nand_58_out));
  LED led_11 (.in(nand_59_out));
  LED led_12 (.in(nW));
  LED led_13 (.in(nJMP));
  nand nand_75 (nand_75_out, 1'b0, 1'b0);
  Seven_Seg_Hex seven_seg_hex_1 (.d({3'b000, AL}), .dp(1'b0));
  Seven_Seg_Hex seven_seg_hex_2 (.d({AR3, AR2, AR1, AR0}), .dp(1'b0));

  // Other names for the same wires on the sheet: B0 = D0; B1 = D1; B2 = D2; B3 = D3; B4 = D4; B5 = D5; B6 = D6;
  //   B7 = D7; CLK1 = clk

  // Notes on the sheet:
  //   clk: Hz: 2
  //   2 to 4 line decoder with enable ('139)
  //   4:1 Multiplexer with Enable
  //   16-bit Jump Detector
  //   CONTROL UNIT
  //   3 to 8 Instruction decoder - 27 Gates
  //   Octal Inverter/Driver
  //   LOAD
  //   AND
  //   OR
  //   XOR
  //   ADD
  //   SUB
  //   STORE
  //   JMP
  //   INSTRUCTION
endmodule
