// Digital circuit MS_flipflop.dig as structural Verilog
module MS_flipflop (
  input  Din
);

  wire nand_1_out, nand_2_out, nand_3_out, nand_4_out, nand_5_out, nand_6_out, nand_7_out, nand_8_out, PH0,
       PH1;

  nand nand_1 (nand_1_out, Din, PH1);
  nand nand_2 (nand_2_out, nand_1_out, PH1);
  nand nand_3 (nand_3_out, nand_1_out, nand_4_out);
  nand nand_4 (nand_4_out, nand_3_out, nand_2_out);
  nand nand_5 (nand_5_out, nand_3_out, PH0);
  nand nand_6 (nand_6_out, nand_5_out, PH0);
  nand nand_7 (nand_7_out, nand_5_out, nand_8_out);
  nand nand_8 (nand_8_out, nand_7_out, nand_6_out);

  // Notes on the sheet:
  //   Master
  //   Slave
endmodule
