// Digital circuit bit_serial_cpu_5.dig as structural Verilog
module bit_serial_cpu_5 (
  input  in_1,
  input  in_2,
  input  in_3,
  input  in_4,
  input  CLK,
  input  in_6,
  input  in_7,
  input  in_8,
  input  in_9,
  input  in_12,
  input  in_13,
  input  in_14,
  input  in_15,
  input  in_16,
  input  in_17,
  input  in_18,
  input  in_19,
  input  in_20,
  output SUM,
  output Cout
);

  wire _27c1024_1_p9, _27c1024_1_p10, _27c1024_1_p11, _27c1024_1_p12, _27c1024_1_p13, _27c1024_1_p15,
       _27c1024_1_p16, _27c1024_1_p17, _27c1024_1_p18, _27c1024_1_p19, _27c1024_1_p20, _27c1024_1_p21,
       _27c1024_1_p22, _74573_2_pin2, _74573_2_pin3, _74573_2_pin4, button_1_out, button_2_out, button_3_out,
       button_4_out, button_5_out, button_6_out, button_7_out, button_8_out, d_ff_1_nq, d_ff_2_nq, d_ff_3_nq,
       d_ff_4_nq, d_ff_5_nq, d_ff_6_nq, d_ff_7_nq, IC2_pin3, IC2_pin6, IC2_pin8, IC2_pin10, IC3_pin4,
       IC3_pin5, IC3_pin9, IC4_pin6, IC4_pin8, IC6_pin13, IC6_pin15, IC7_pin8, IC7_pin12, IC7_pin18,
       IC8_pin12, IC8_pin14, IC11_pin9, IC11_pin10, IC11_pin13, IC16_nq, IC22_pin10, IC23_pin10, INC_out,
       monoflop_1_q, nand_1_out, nand_3_out, nand_4_out, nand_5_out, nand_6_out, nand_7_out, nand_9_out,
       nand_10_out, TRIG_q, xor_2_out, xor_3_out;
  wire [3:0] _74573_1_pin15, _74573_1_pin19, _74573_2_pin15, _74573_2_pin19, IC4_pin5, IC4_pin13, IC6_pin10,
       IC7_pin7, IC7_pin16, IC16_q, IC22_pin14, IC23_pin14;

  _74161 IC23 (
    .pin1(1'b1), .pin2(CLK), .pin3(in_16), .pin4(in_17), .pin5(in_18), .pin6(in_19), .pin7(1'b1),
    .pin8(1'b0), .pin9(1'b1), .pin10(IC23_pin10), .pin11(IC23_pin14[3]), .pin12(IC23_pin14[2]),
    .pin13(IC23_pin14[1]), .pin14(IC23_pin14[0]), .pin16(1'b1));  // open: pin15
  _74299 IC7 (
    .pin1(in_9), .pin2(in_6), .pin3(in_7), .pin4(IC7_pin16[2]), .pin5(IC7_pin16[0]), .pin6(IC7_pin7[2]),
    .pin7(IC7_pin7[0]), .pin8(IC7_pin8), .pin9(1'b1), .pin10(1'b0), .pin11(in_8), .pin12(IC7_pin12),
    .pin13(IC7_pin7[1]), .pin14(IC7_pin7[3]), .pin15(IC7_pin16[1]), .pin16(IC7_pin16[3]), .pin18(IC7_pin18),
    .pin19(1'b1), .pin20(1'b1));  // open: pin17
  LED led_1 (.in(IC16_q[3]));
  D_FF IC16 (.D(IC16_nq), .C(button_1_out), .Q(IC16_q[3]), .nQ(IC16_nq));
  LED led_2 (.in(IC16_q[2]));
  D_FF d_ff_1 (.D(d_ff_1_nq), .C(button_2_out), .Q(IC16_q[2]), .nQ(d_ff_1_nq));
  Button button_1 (.out(button_1_out));
  LED led_3 (.in(IC16_q[1]));
  D_FF d_ff_2 (.D(d_ff_2_nq), .C(button_3_out), .Q(IC16_q[1]), .nQ(d_ff_2_nq));
  Button button_2 (.out(button_2_out));
  // Probe QA' on IC7_pin8
  LED led_4 (.in(IC16_q[0]));
  D_FF d_ff_3 (.D(d_ff_3_nq), .C(button_4_out), .Q(IC16_q[0]), .nQ(d_ff_3_nq));
  Button button_3 (.out(button_3_out));
  _74161 IC22 (
    .pin1(1'b1), .pin2(CLK), .pin3(in_12), .pin4(in_13), .pin5(in_14), .pin6(in_15), .pin7(1'b1),
    .pin8(1'b0), .pin9(1'b1), .pin10(IC22_pin10), .pin11(IC22_pin14[3]), .pin12(IC22_pin14[2]),
    .pin13(IC22_pin14[1]), .pin14(IC22_pin14[0]), .pin15(IC23_pin10), .pin16(1'b1));
  LED led_5 (.in(IC7_pin16[3]));
  LED led_6 (.in(IC7_pin16[2]));
  _74166 IC6 (
    .pin1(1'b0), .pin2(IC16_q[3]), .pin3(IC16_q[2]), .pin4(IC16_q[1]), .pin5(IC16_q[0]), .pin6(1'b0),
    .pin7(IC7_pin12), .pin8(1'b0), .pin9(1'b1), .pin10(IC6_pin10[3]), .pin11(IC6_pin10[2]),
    .pin12(IC6_pin10[1]), .pin13(IC6_pin13), .pin14(IC6_pin10[0]), .pin15(IC6_pin15), .pin16(1'b1));
  LED led_7 (.in(IC6_pin10[3]));
  D_FF d_ff_4 (.D(d_ff_4_nq), .C(button_5_out), .Q(IC6_pin10[3]), .nQ(d_ff_4_nq));
  Button button_4 (.out(button_4_out));
  Seven_Seg_Hex seven_seg_hex_1 (.d(IC23_pin14), .dp(1'b0));
  LED led_8 (.in(IC7_pin16[1]));
  LED led_9 (.in(IC7_pin16[0]));
  LED led_10 (.in(IC6_pin10[2]));
  D_FF d_ff_5 (.D(d_ff_5_nq), .C(button_6_out), .Q(IC6_pin10[2]), .nQ(d_ff_5_nq));
  Button button_5 (.out(button_5_out));
  Seven_Seg_Hex seven_seg_hex_2 (.d(IC22_pin14), .dp(1'b0));
  LED led_11 (.in(IC7_pin7[3]));
  LED led_12 (.in(IC7_pin7[2]));
  LED led_13 (.in(IC6_pin10[1]));
  D_FF d_ff_6 (.D(d_ff_6_nq), .C(button_7_out), .Q(IC6_pin10[1]), .nQ(d_ff_6_nq));
  Button button_6 (.out(button_6_out));
  LED led_14 (.in(IC7_pin7[1]));
  LED led_15 (.in(IC7_pin7[0]));
  LED led_16 (.in(IC6_pin10[0]));
  D_FF d_ff_7 (.D(d_ff_7_nq), .C(button_8_out), .Q(IC6_pin10[0]), .nQ(d_ff_7_nq));
  Button button_7 (.out(button_7_out));
  Seven_Seg_Hex seven_seg_hex_3 (.d(IC7_pin16), .dp(1'b0));
  Seven_Seg_Hex seven_seg_hex_4 (.d(IC16_q), .dp(1'b0));
  Button button_8 (.out(button_8_out));
  Seven_Seg_Hex seven_seg_hex_5 (.d(IC7_pin7), .dp(1'b0));
  // Probe Bin on IC6_pin13
  Button INC (.out(INC_out));
  // Probe Ain on IC8_pin14
  Seven_Seg_Hex seven_seg_hex_6 (.d(IC6_pin10), .dp(1'b0));
  // _27C1024 _27c1024_1: pin names not known; wires that end beside it: 1'b0, 1'b0, 1'b0, 1'b0, 1'b0, 1'b0, 1'b0, 1'b1, _27c1024_1_p9, _27c1024_1_p10, _27c1024_1_p11, _27c1024_1_p12, _27c1024_1_p13, 1'b0, _27c1024_1_p15, _27c1024_1_p16, _27c1024_1_p17, _27c1024_1_p18, _27c1024_1_p19, _27c1024_1_p20, _27c1024_1_p21, _27c1024_1_p22, 1'b0, 1'b1
  // Probe SCK on IC7_pin12
  Monoflop #(.timerDelay(2)) TRIG (.C(INC_out), .R(1'b0), .Q(TRIG_q));  // open: nQ
  // Probe LD on IC6_pin15
  _74573 _74573_1 (
    .pin1(1'b0), .pin2(_27c1024_1_p15), .pin3(_27c1024_1_p16), .pin4(_27c1024_1_p17), .pin5(_27c1024_1_p18),
    .pin6(_27c1024_1_p19), .pin7(_27c1024_1_p20), .pin8(_27c1024_1_p21), .pin9(_27c1024_1_p22), .pin10(1'b0),
    .pin11(in_20), .pin12(_74573_1_pin15[3]), .pin13(_74573_1_pin15[2]), .pin14(_74573_1_pin15[1]),
    .pin15(_74573_1_pin15[0]), .pin16(_74573_1_pin19[3]), .pin17(_74573_1_pin19[2]),
    .pin18(_74573_1_pin19[1]), .pin19(_74573_1_pin19[0]), .pin20(1'b1));
  Monoflop monoflop_1 (.C(IC2_pin8), .R(1'b0), .Q(monoflop_1_q), .nQ(IC6_pin15));
  _7474 IC11 (
    .pin1(1'b0), .pin2(1'b0), .pin3(1'b0), .pin4(1'b0), .pin7(1'b0), .pin9(IC11_pin9), .pin10(IC11_pin10),
    .pin11(IC7_pin12), .pin12(Cout), .pin13(IC11_pin13), .pin14(1'b1));  // open: pin5, pin6, pin8
  // Probe ENT on IC22_pin10
  _7474 IC2 (
    .pin1(1'b1), .pin2(TRIG_q), .pin3(IC2_pin3), .pin4(1'b1), .pin6(IC2_pin6), .pin7(1'b0), .pin8(IC2_pin8),
    .pin10(IC2_pin10), .pin11(1'b1), .pin12(IC2_pin8), .pin13(IC2_pin6), .pin14(1'b1));  // open: pin5, pin9
  xor xor_1 (IC11_pin10, nand_1_out, in_4);
  nand nand_1 (nand_1_out, in_4, IC6_pin15);
  _74573 _74573_2 (
    .pin1(1'b0), .pin2(_74573_2_pin2), .pin3(_74573_2_pin3), .pin4(_74573_2_pin4), .pin5(_27c1024_1_p9),
    .pin6(_27c1024_1_p10), .pin7(_27c1024_1_p11), .pin8(_27c1024_1_p12), .pin9(_27c1024_1_p13), .pin10(1'b0),
    .pin11(in_20), .pin12(_74573_2_pin15[3]), .pin13(_74573_2_pin15[2]), .pin14(_74573_2_pin15[1]),
    .pin15(_74573_2_pin15[0]), .pin16(_74573_2_pin19[3]), .pin17(_74573_2_pin19[2]),
    .pin18(_74573_2_pin19[1]), .pin19(_74573_2_pin19[0]), .pin20(1'b1));
  Reset reset_1 (.out(IC11_pin13));
  LED led_17 (.in(in_4));
  _7400 IC3 (
    .pin1(CLK), .pin2(CLK), .pin3(IC2_pin3), .pin4(IC3_pin4), .pin5(IC3_pin5), .pin6(IC2_pin10), .pin7(1'b0),
    .pin8(IC7_pin12), .pin9(IC3_pin9), .pin10(IC3_pin9), .pin11(IC3_pin9), .pin12(IC2_pin8), .pin13(CLK),
    .pin14(1'b1));
  // Probe SS on IC2_pin8
  LED led_18 (.in(IC11_pin9));
  Seven_Seg_Hex seven_seg_hex_7 (.d(_74573_1_pin15), .dp(1'b0));
  LED led_19 (.in(IC6_pin13));
  LED led_20 (.in(IC8_pin14));
  Seven_Seg_Hex seven_seg_hex_8 (.d(_74573_1_pin19), .dp(1'b0));
  _74163 IC1 (
    .pin1(IC2_pin8), .pin2(CLK), .pin3(1'b0), .pin4(1'b0), .pin5(1'b0), .pin6(1'b0), .pin7(IC2_pin8),
    .pin8(1'b0), .pin9(1'b1), .pin10(1'b1), .pin11(IC3_pin5), .pin14(IC3_pin4), .pin16(1'b1));  // open: pin12, pin13, pin15
  // Probe Cin on IC11_pin9
  // Probe Bin on IC6_pin13
  xor xor_2 (xor_2_out, IC6_pin13, in_4);
  Seven_Seg_Hex seven_seg_hex_9 (.d(_74573_2_pin15), .dp(1'b0));
  nand nand_2 (IC22_pin10, IC2_pin10, IC2_pin10);
  Seven_Seg_Hex seven_seg_hex_10 (.d(_74573_2_pin19), .dp(1'b0));
  xor xor_3 (xor_3_out, xor_2_out, IC8_pin14);
  nand nand_3 (nand_3_out, IC8_pin14, xor_2_out);
  nand nand_4 (nand_4_out, IC8_pin14, IC8_pin14);
  nand nand_5 (nand_5_out, IC6_pin13, IC6_pin13);
  _7425 IC4 (
    .pin1(IC4_pin5[0]), .pin2(IC4_pin5[1]), .pin4(IC4_pin5[2]), .pin5(IC4_pin5[3]), .pin6(IC4_pin6),
    .pin7(1'b0), .pin8(IC4_pin8), .pin9(IC4_pin13[0]), .pin10(IC4_pin13[1]), .pin12(IC4_pin13[2]),
    .pin13(IC4_pin13[3]), .pin14(1'b1));  // open: pin3, pin11
  _74595 IC8 (
    .pin1(IC4_pin5[2]), .pin2(IC4_pin5[1]), .pin3(IC4_pin5[0]), .pin4(IC4_pin13[3]), .pin5(IC4_pin13[2]),
    .pin6(IC4_pin13[1]), .pin7(IC4_pin13[0]), .pin8(1'b0), .pin9(IC7_pin18), .pin10(1'b1),
    .pin11(IC22_pin10), .pin12(IC8_pin12), .pin13(1'b0), .pin14(IC8_pin14), .pin15(IC4_pin5[3]), .pin16(1'b1));
  not not_1 (IC8_pin12, IC7_pin12);
  nand nand_6 (nand_6_out, IC4_pin8, IC4_pin6);
  xor xor_4 (SUM, xor_3_out, IC11_pin9);
  nand nand_7 (nand_7_out, xor_3_out, IC11_pin9);
  nand nand_8 (Cout, nand_7_out, nand_3_out);
  nand nand_9 (nand_9_out, nand_4_out, nand_5_out);
  nand nand_10 (nand_10_out, nand_3_out, nand_3_out);
  LED led_21 (.in(nand_6_out));
  // Probe Zero on nand_6_out
  // Probe LATCH on IC22_pin10
  Seven_Seg_Hex seven_seg_hex_11 (.d(IC4_pin5), .dp(1'b0));
  _74151 IC13 (
    .pin1(nand_4_out), .pin2(xor_3_out), .pin3(nand_9_out), .pin4(nand_10_out), .pin5(IC7_pin18),
    .pin7(in_1), .pin8(1'b0), .pin9(in_2), .pin10(in_3), .pin11(in_4), .pin12(SUM), .pin13(SUM), .pin14(SUM),
    .pin15(SUM), .pin16(1'b1));  // open: pin6
  Seven_Seg_Hex seven_seg_hex_12 (.d(IC4_pin13), .dp(1'b0));
  LED led_22 (.in(Cout));
  LED led_23 (.in(SUM));
  // Probe Dout on IC7_pin18

  // Notes on the sheet:
  //   8-bit Serial ALU
  //   RAM Sub-system
  //   S1     S0       MODE
  //   0          0       HOLD
  //   0          1       RIGHT
  //   1          0       LEFT
  //   1          1       LOAD
  //   ALU Result Register
  //   B Register
  //   LOAD
  //   INSTRUCTION
  //   SPI Sequencer
  //   Carry FF
  //   SET CARRY LOGIC
  //   /+_-
  //   Full Adder using XOR and NAND gates
  //   Cin
  //   Ain
  //   Bin
  //   A
  //   B
  //   NotB
  //   IC15B
  //   IC10 (XOR)
  //   IC11,12 (NAND)
  //   IC12
  //   AxorB
  //   SCK
  //   Zero Detect
  //   IC15A
  //   Slave Register
  //   NOT
  //   XOR
  //   OR
  //   AND
  //   Dout
  //   Cout
  //   SUM
  //   contents of ROM1 (hex, n*v repeats v):
  //   c001,c001,c001,c001,c001
endmodule
