// Digital circuit multifunction_gate_1.dig as structural Verilog
module multifunction_gate_1 (
  input  B,
  input  I1,
  input  I0,
  input  A,
  output Q
);

  wire nand_1_out, nand_2_out, nand_3_out, nand_4_out, nand_5_out, nand_6_out, nand_7_out;

  nand nand_1 (nand_1_out, A, B);
  nand nand_2 (nand_2_out, A, nand_1_out);
  nand nand_3 (nand_3_out, nand_1_out, nand_1_out);
  nand nand_4 (nand_4_out, nand_1_out, B);
  nand nand_5 (nand_5_out, nand_2_out, nand_4_out);
  nand nand_6 (nand_6_out, I1, nand_5_out);
  nand nand_7 (nand_7_out, nand_3_out, I0);
  nand nand_8 (Q, nand_6_out, nand_7_out);

  // Notes on the sheet:
  //   Multifunction Gate #1 - Zero, AND, XOR, OR
endmodule
