// Digital circuit terminal_1.dig as structural Verilog
module terminal_1 (
);

  wire CLK1, keyboard_1_d;

  Keyboard keyboard_1 (.C(CLK1), .en(1'b1), .D(keyboard_1_d));  // open: av
  Terminal terminal_1 (.D(keyboard_1_d), .C(CLK1), .en(1'b1));
endmodule
